// Logisim project da2_task1.circ as structural Verilog: 3 circuits, main circuit DUT
module DUT (
  input  DIN,
  input  CLK,
  input  RST,
  output DOUT
);

  wire and_1_out, and_2_out, and_3_out, d_ff_1_q, d_ff_1_qn, d_ff_2_qn, or_1_out;

  and and_1 (and_1_out, DOUT, DIN);
  and and_2 (and_2_out, DIN, d_ff_1_q);
  or or_1 (or_1_out, and_1_out, and_2_out);
  and and_3 (and_3_out, DIN, d_ff_2_qn, d_ff_1_qn);
  D_Flip_Flop d_ff_1 (.D(or_1_out), .clk(CLK), .Q(d_ff_1_q), .Qn(d_ff_1_qn), .reset(RST));  // open: preset
  D_Flip_Flop d_ff_2 (.D(and_3_out), .clk(CLK), .Q(DOUT), .Qn(d_ff_2_qn), .reset(RST));  // open: preset

  // Notes on the sheet:
  //   Please put your deisgn below. You may also use subcircuits.
  //   However, do not move, rename, add, or delete any pins.
  //   Put your design below and wire it up to the pins.
  //   Feel free to remove this text.
endmodule

module TB (
);

  wire BUTTON_1_out, clk_out, dut_1_dout, pwr_on_reset_1_rst, t_ff_1_q;

  Clock sysclk ();  // open: out
  Button BUTTON_1 (.out(BUTTON_1_out));
  Clock #(.highDuration(2), .lowDuration(2)) clk (.out(clk_out));
  pwr_on_reset pwr_on_reset_1 (.CLK(clk_out), .RST(pwr_on_reset_1_rst));
  T_Flip_Flop t_ff_1 (.T(dut_1_dout), .clk(clk_out), .Q(t_ff_1_q));  // open: Qn, reset, preset
  DUT dut_1 (.DIN(BUTTON_1_out), .CLK(clk_out), .RST(pwr_on_reset_1_rst), .DOUT(dut_1_dout));
  LED LED1 (.in(t_ff_1_q));

  // Notes on the sheet:
  //   DO NOT MODIFY THIS
  //   YOU MAY TEST YOUR CIRCUITS USING THIS TO MAKE SURE YOU HAVE NOT ALTERED PIN OUT
  //   LED1 will toggle every clock tick that output of test circuit is high.
endmodule

module pwr_on_reset (
  input  CLK,
  output RST
);

  wire d_ff_1_q, nor_1_out, not_1_out;

  not not_1 (not_1_out, nor_1_out);
  D_Flip_Flop d_ff_1 (.D(not_1_out), .clk(CLK), .Q(d_ff_1_q));  // open: Qn, preset, reset
  D_Flip_Flop d_ff_2 (.D(nor_1_out), .clk(CLK), .Q(RST));  // open: Qn, preset, reset
  nor nor_1 (nor_1_out, d_ff_1_q, RST);

  // Notes on the sheet:
  //   DO NOT MODIFY THIS
endmodule
