// Logisim project da2_task3.circ as structural Verilog: 3 circuits, main circuit DUT
module DUT (
  input  DIN,
  input  CLK,
  input  RST,
  output DOUT
);

  wire and_1_out, and_2_out, and_3_out, and_4_out, and_5_out, and_6_out, and_7_out, and_8_out, and_9_out,
       and_10_out, and_11_out, or_1_out, or_2_out, or_3_out, or_4_out, R1_4, R2_5, R3;

  and and_1 (and_1_out, DIN, DOUT);
  and and_2 (and_2_out, ~DIN, R2_5);  // AND_Gate
  and and_3 (and_3_out, DIN, R3);
  and and_4 (and_4_out, R1_4, DIN);
  or or_1 (or_1_out, and_1_out, and_2_out, and_3_out);
  D_Flip_Flop Remainder3 (.D(or_2_out), .clk(CLK), .Q(R3));  // open: Qn, preset, reset
  or or_2 (or_2_out, RST, and_4_out);
  D_Flip_Flop Remainder1or4 (.D(and_5_out), .clk(CLK), .Q(R1_4));  // open: Qn, preset, reset
  and and_5 (and_5_out, ~RST, or_1_out);  // AND_Gate
  and and_6 (and_6_out, DIN, R2_5);
  and and_7 (and_7_out, ~DIN, R1_4);  // AND_Gate
  and and_8 (and_8_out, ~DIN, DOUT);  // AND_Gate
  or or_3 (or_3_out, and_8_out, and_9_out);
  and and_9 (and_9_out, ~DIN, R3);  // AND_Gate
  or or_4 (or_4_out, and_6_out, and_7_out);
  and and_10 (and_10_out, ~RST, or_3_out);  // AND_Gate
  D_Flip_Flop Remainder0 (.D(and_10_out), .clk(CLK), .Q(DOUT));  // open: Qn, preset, reset
  D_Flip_Flop Remainder2or5 (.D(and_11_out), .clk(CLK), .Q(R2_5));  // open: Qn, preset, reset
  and and_11 (and_11_out, ~RST, or_4_out);  // AND_Gate

  // Other names for the same wires on the sheet: R0 = DOUT

  // Notes on the sheet:
  //   Please put your deisgn below. You may also use subcircuits.
  //   However, do not move, rename, add, or delete any pins.
  //   Put your design below and wire it up to the pins.
  //   Feel free to remove this text.
endmodule

module TB (
);

  wire clk_out, pwr_on_reset_1_rst;
  wire [0:0] dut_1_dout, random_1_out;

  Clock sysclk ();  // open: out
  Random #(.width(1)) random_1 (.clk(clk_out), .out(random_1_out[0]));  // open: clr, next
  Clock #(.highDuration(2), .lowDuration(2)) clk (.out(clk_out));
  pwr_on_reset pwr_on_reset_1 (.CLK(clk_out), .RST(pwr_on_reset_1_rst));
  LED led_1 (.in(random_1_out[0]));
  DUT dut_1 (.DIN(random_1_out[0]), .CLK(clk_out), .RST(pwr_on_reset_1_rst), .DOUT(dut_1_dout[0]));
  TTY #(.rows(4)) tty_1 (.data({6'b011000, dut_1_dout[0]}), .clk(clk_out));  // open: we, clr
  TTY #(.rows(4)) tty_2 (.data({6'b011000, random_1_out[0]}), .clk(clk_out));  // open: we, clr

  // Notes on the sheet:
  //   DO NOT MODIFY THIS
  //   YOU MAY TEST YOUR CIRCUITS USING THIS TO MAKE SURE YOU HAVE NOT ALTERED PIN OUT
  //   Top screen shows output, bottom screen shows the random input.
endmodule

module pwr_on_reset (
  input  CLK,
  output RST
);

  wire d_ff_1_q, nor_1_out, not_1_out;

  not not_1 (not_1_out, nor_1_out);
  D_Flip_Flop d_ff_1 (.D(not_1_out), .clk(CLK), .Q(d_ff_1_q));  // open: Qn, preset, reset
  D_Flip_Flop d_ff_2 (.D(nor_1_out), .clk(CLK), .Q(RST));  // open: Qn, preset, reset
  nor nor_1 (nor_1_out, d_ff_1_q, RST);

  // Notes on the sheet:
  //   DO NOT MODIFY THIS
endmodule
