// Logisim project da2_task4_tb.circ as structural Verilog: 2 circuits, main circuit main
module main (
  output halt,
  output [11:0] CYCLE,
  output RST,
  output RDY,
  output [6:0] DIN,
  output F
);

  wire CLK_out, d_ff_1_q;
  wire [8:0] counter_2_q;

  Clock sysclk ();  // open: out
  Clock CLK (.out(CLK_out));
  Counter #(.width(12), .max('hfff)) counter_1 (.clk(CLK_out), .Q(CYCLE));  // open: clr, load, up, count, D, carry
  Counter #(.width(9), .max('h1ff)) counter_2 (
    .count(RDY), .clk(CLK_out), .carry(halt), .Q(counter_2_q));  // open: clr, load, up, D
  Random #(.width(1), .seed(10)) RNGRDY (.clk(CLK_out), .out(RDY));  // open: clr, next
  poweron_reset_random poweron_reset_random_1 (.CLK(CLK_out), .RST(RST));
  ROM #(.addrWidth(9), .dataWidth(7)) TEXTROM (.addr(counter_2_q), .data(DIN));
  DUT dut_1 (.DIN(DIN), .RDY(RDY), .CLK(CLK_out), .RST(RST), .F(F));
  D_Flip_Flop d_ff_1 (.D(RDY), .clk(CLK_out), .Q(d_ff_1_q));  // open: Qn, preset, reset
  TTY #(.rows(4)) tty_1 (.data({6'b011000, F}), .clk(CLK_out), .we(d_ff_1_q));  // open: clr
  TTY tty_2 (.data(DIN), .clk(CLK_out), .we(RDY));  // open: clr

  // Notes on the sheet:
  //   contents of TEXTROM (hex, n*v repeats v):
  //   46 5c 58 56 69 72 75 73 27 31 2e 26 45 56 69 72 75 73 76 4c 43 4f 52 4f 4e 41 6a 34 30 43 4f 56 49
  //   52 55 53 9 25 7d 31 76 57 61 63 6f 76 69 72 75 73 9 76 69 72 75 73 28 7c 6c 70 62 9 71 28 3e 3b 5e
  //   7e b 49 35 4b 2d 56 69 72 75 73 37 7a 65 3c 38 74 5f 55 27 43 6f 63 6f 72 6f 6e 61 30 62 63 6f 72 6f
  //   6e 61 2c 4e 69 68 37 6a 43 4f 56 49 44 47 30 72 c 62 3c 73 2a 43 4f 56 49 52 55 53 78 78 4a 55 43 6f
  //   72 6f 6e 61 77 45 4a 6d 52 3e 7c 78 37 43 3d 43 6f 63 6f 72 6f 6e 61 26 6e 33 2a 6f 53 42 25 62 7a
  //   6b 43 6f 63 6f 72 6f 6e 61 74 76 69 72 75 73 2f 43 6f 72 6f 6e 61 56 69 72 75 73 7b 22 26 23 a 69 64
  //   64 34 4b 3e 6c 6c 25 d 3b 36 6d 38 79 43 6f 76 69 64 69 35 51 66 41 56 69 72 75 73 63 6f 76 69 64 d
  //   73 56 69 72 75 73 62 43 4f 56 49 44 36 4d 31 78 56 69 72 75 73 4f 63 6f 72 6f 6e 61 44 69 76 69 72
  //   75 73 63 6f 76 69 72 75 73 a 77 76 69 72 75 73 39 71 63 6f 63 6f 72 6f 6e 61 45 5d 43 63 6f 63 6f 72
  //   6f 6e 61 d 3a 2a 76 69 72 75 73 6f 31 5a 51 40 4c 56 54 3e 5f 7b 3b 5d 63 6f 76 69 64 63 5a 5b 2e 63
  //   6f 76 69 72 75 73 7b 4e 43 60 6c 2b 4f b 6c 5f 43 6f 63 6f 72 6f 6e 61 43 4f 56 49 44 43 6f 76 69 64
  //   58 3a 5f 56 48 35 31 60 63 6f 76 69 64 43 6f 63 6f 72 6f 6e 61 3b 43 4f 52 4f 4e 41 2c 55 32 43 6f
  //   63 6f 72 6f 6e 61 61 53 43 6f 72 6f 6e 61 4f 56 69 72 75 73 50 38 28 43 6f 72 6f 6e 61 36 5a 47 3b
  //   4a 2c 4d c 28 7a 63 6f 63 6f 72 6f 6e 61 45 67 63 6f 63 6f 72 6f 6e 61 71 a c 61 43 6f 72 6f 6e 61
  //   31 34 2c 3d 69 76 69 72 75 73 a 40 56 49 52 55 53 63 6f 76 69 72 75 73 43 4f 52 4f 4e 41 74 70 64 75
  //   65 63 6f 63 6f 72 6f
endmodule

module poweron_reset_random (
  input  CLK,
  output RST
);

  wire and_1_out, clock_1_out, d_ff_1_q, not_1_out, RNGRST_out, t_ff_1_qn;

  Clock clock_1 (.out(clock_1_out));
  Random #(.width(1), .seed(20)) RNGRST (.next(t_ff_1_qn), .clk(clock_1_out), .out(RNGRST_out));  // open: clr
  T_Flip_Flop t_ff_1 (.T(and_1_out), .clk(clock_1_out), .Qn(t_ff_1_qn));  // open: Q, reset, preset
  and and_1 (and_1_out, t_ff_1_qn, not_1_out, d_ff_1_q);
  not not_1 (not_1_out, RNGRST_out);
  D_Flip_Flop d_ff_1 (.D(RNGRST_out), .clk(clock_1_out), .Q(d_ff_1_q));  // open: Qn, preset, reset
  and and_2 (RST, t_ff_1_qn, d_ff_1_q);
  TTY #(.rows(4), .cols(16)) tty_1 (.data({6'b011000, RST}), .clk(clock_1_out));  // open: we, clr
endmodule
