// Logisim project da3.circ as structural Verilog: 3 circuits, main circuit DUT
module DUT (
  input  CLK,
  input  RST,
  input  REQ,
  input  [15:0] A,
  input  [15:0] D,
  output ACK,
  output FDBZ,
  output [15:0] Q,
  output [15:0] R
);

  wire and_1_out, and_2_out, bitselector_1_out, bitselector_2_out, bitselector_3_out, bitselector_4_out,
       bitselector_5_out, bitselector_6_out, bitselector_7_out, bitselector_8_out, bitselector_9_out,
       bitselector_10_out, bitselector_11_out, bitselector_12_out, bitselector_13_out, bitselector_14_out,
       bitselector_15_out, bitselector_16_out, bitselector_17_out, bitselector_18_out, bitselector_19_out,
       bitselector_20_out, bitselector_21_out, bitselector_22_out, bitselector_23_out, bitselector_24_out,
       bitselector_25_out, bitselector_26_out, bitselector_27_out, bitselector_28_out, bitselector_29_out,
       bitselector_30_out, bitselector_31_out, comparator_1_eq, comparator_2_lt, comparator_3_lt,
       comparator_4_eq, comparator_4_gt, comparator_5_eq, comparator_5_gt, comparator_6_eq, comparator_6_gt,
       comparator_7_eq, comparator_7_gt, comparator_8_eq, comparator_8_gt, comparator_9_eq, comparator_9_gt,
       comparator_10_eq, comparator_10_gt, comparator_11_eq, comparator_11_gt, comparator_12_eq,
       comparator_12_gt, comparator_13_eq, comparator_13_gt, comparator_14_eq, comparator_14_gt,
       comparator_15_eq, comparator_15_gt, comparator_16_eq, comparator_16_gt, comparator_17_eq,
       comparator_17_gt, comparator_18_eq, comparator_18_gt, comparator_19_eq, comparator_19_gt,
       comparator_20_lt, comparator_21_gt, comparator_21_lt, comparator_22_eq, d_ff_2_q, d_ff_3_q,
       multiplexer_108_out, not_2_out, or_2_out, or_3_out, or_4_out, or_5_out, or_6_out, or_7_out, or_8_out,
       or_9_out, or_10_out, or_11_out, or_12_out, or_13_out, or_14_out, or_15_out, or_16_out, or_17_out,
       or_18_out, Reset_q, xor_1_out;
  wire [3:0] multiplexer_91_out, multiplexer_93_out, multiplexer_94_out, multiplexer_95_out,
       multiplexer_96_out, multiplexer_97_out, multiplexer_98_out, multiplexer_99_out, multiplexer_100_out,
       multiplexer_101_out, multiplexer_102_out, multiplexer_103_out, multiplexer_104_out,
       multiplexer_105_out;
  wire [4:0] bit_extender_1_out, multiplexer_92_out, multiplexer_106_out, multiplexer_107_out, register_33_q,
       subtractor_18_out;
  wire [15:0] adder_1_out, adder_2_out, adder_3_out, adder_4_out, adder_5_out, adder_6_out, adder_7_out,
       adder_8_out, adder_9_out, adder_10_out, adder_11_out, adder_12_out, adder_13_out, adder_14_out,
       adder_15_out, adder_16_out, adder_17_out, adder_18_out, adder_19_out, adder_20_out, adder_21_out,
       adder_22_out, adder_23_out, adder_24_out, adder_25_out, adder_26_out, adder_27_out, adder_28_out,
       adder_29_out, adder_30_out, adder_31_out, adder_32_out, adder_33_out, adder_34_out, adder_35_out,
       adder_36_out, adder_37_out, multiplexer_1_out, multiplexer_3_out, multiplexer_4_out,
       multiplexer_5_out, multiplexer_6_out, multiplexer_7_out, multiplexer_8_out, multiplexer_9_out,
       multiplexer_10_out, multiplexer_11_out, multiplexer_12_out, multiplexer_13_out, multiplexer_14_out,
       multiplexer_15_out, multiplexer_16_out, multiplexer_17_out, multiplexer_18_out, multiplexer_19_out,
       multiplexer_21_out, multiplexer_22_out, multiplexer_23_out, multiplexer_24_out, multiplexer_25_out,
       multiplexer_26_out, multiplexer_27_out, multiplexer_28_out, multiplexer_29_out, multiplexer_30_out,
       multiplexer_31_out, multiplexer_32_out, multiplexer_33_out, multiplexer_34_out, multiplexer_35_out,
       multiplexer_36_out, multiplexer_37_out, multiplexer_38_out, multiplexer_39_out, multiplexer_40_out,
       multiplexer_41_out, multiplexer_42_out, multiplexer_43_out, multiplexer_44_out, multiplexer_45_out,
       multiplexer_46_out, multiplexer_47_out, multiplexer_48_out, multiplexer_49_out, multiplexer_50_out,
       multiplexer_51_out, multiplexer_52_out, multiplexer_53_out, multiplexer_54_out, multiplexer_55_out,
       multiplexer_56_out, multiplexer_57_out, multiplexer_58_out, multiplexer_59_out, multiplexer_60_out,
       multiplexer_61_out, multiplexer_62_out, multiplexer_63_out, multiplexer_64_out, multiplexer_65_out,
       multiplexer_66_out, multiplexer_67_out, multiplexer_68_out, multiplexer_69_out, multiplexer_70_out,
       multiplexer_71_out, multiplexer_72_out, multiplexer_73_out, multiplexer_74_out, multiplexer_75_out,
       multiplexer_76_out, multiplexer_77_out, multiplexer_78_out, multiplexer_79_out, multiplexer_80_out,
       multiplexer_81_out, multiplexer_82_out, multiplexer_83_out, multiplexer_84_out, multiplexer_85_out,
       multiplexer_86_out, multiplexer_87_out, multiplexer_88_out, multiplexer_89_out, multiplexer_90_out,
       not_1_out, not_3_out, not_4_out, not_5_out, register_1_q, register_2_q, register_3_q, register_4_q,
       register_5_q, register_6_q, register_7_q, register_8_q, register_9_q, register_10_q, register_11_q,
       register_12_q, register_13_q, register_14_q, register_15_q, register_16_q, register_17_q,
       register_18_q, register_19_q, register_20_q, register_21_q, register_22_q, register_23_q,
       register_24_q, register_25_q, register_26_q, register_27_q, register_28_q, register_29_q,
       register_30_q, register_31_q, register_32_q, shifter_1_out, shifter_2_out, shifter_3_out,
       shifter_4_out, shifter_5_out, shifter_6_out, shifter_7_out, shifter_8_out, shifter_9_out,
       shifter_10_out, shifter_11_out, shifter_12_out, shifter_13_out, shifter_14_out, shifter_15_out,
       subtractor_1_out, subtractor_2_out, subtractor_3_out, subtractor_4_out, subtractor_5_out,
       subtractor_6_out, subtractor_7_out, subtractor_8_out, subtractor_9_out, subtractor_10_out,
       subtractor_11_out, subtractor_12_out, subtractor_13_out, subtractor_14_out, subtractor_15_out,
       subtractor_16_out, subtractor_17_out;

  assign not_1_out = ~D;  // NOT_Gate not_1, 16 bits wide
  Comparator #(.width(16)) comparator_1 (.a(D), .b({16{1'b0}}), .eq(comparator_1_eq));  // open: gt, lt
  Comparator #(.width(16)) comparator_2 (.a(D), .b({16{1'b0}}), .lt(comparator_2_lt));  // open: gt, eq
  Adder #(.width(16)) adder_1 (.a(not_1_out), .b(16'h1), .out(adder_1_out));  // open: cin, cout
  not not_2 (not_2_out, RST);
  Shifter #(.width(16)) shifter_1 (.in(register_1_q), .\dist (4'b0001), .out(shifter_1_out));
  Shifter #(.width(16)) shifter_2 (.in(register_2_q), .\dist (4'b0001), .out(shifter_2_out));
  Shifter #(.width(16)) shifter_3 (.in(register_3_q), .\dist (4'b0001), .out(shifter_3_out));
  Shifter #(.width(16)) shifter_4 (.in(register_4_q), .\dist (4'b0001), .out(shifter_4_out));
  Shifter #(.width(16)) shifter_5 (.in(register_5_q), .\dist (4'b0001), .out(shifter_5_out));
  Shifter #(.width(16)) shifter_6 (.in(register_7_q), .\dist (4'b0001), .out(shifter_6_out));
  Shifter #(.width(16)) shifter_7 (.in(register_8_q), .\dist (4'b0001), .out(shifter_7_out));
  Shifter #(.width(16)) shifter_8 (.in(register_9_q), .\dist (4'b0001), .out(shifter_8_out));
  Shifter #(.width(16)) shifter_9 (.in(register_10_q), .\dist (4'b0001), .out(shifter_9_out));
  Shifter #(.width(16)) shifter_10 (.in(register_11_q), .\dist (4'b0001), .out(shifter_10_out));
  Shifter #(.width(16)) shifter_11 (.in(register_12_q), .\dist (4'b0001), .out(shifter_11_out));
  Shifter #(.width(16)) shifter_12 (.in(register_13_q), .\dist (4'b0001), .out(shifter_12_out));
  Shifter #(.width(16)) shifter_13 (.in(register_14_q), .\dist (4'b0001), .out(shifter_13_out));
  Shifter #(.width(16)) shifter_14 (.in(register_15_q), .\dist (4'b0001), .out(shifter_14_out));
  Shifter #(.width(16)) shifter_15 (.in(register_16_q), .\dist (4'b0001), .out(shifter_15_out));
  and and_1 (and_1_out, REQ, not_2_out, comparator_1_eq);
  Comparator #(.width(16)) comparator_3 (.a(A), .b({16{1'b0}}), .lt(comparator_3_lt));  // open: gt, eq
  Multiplexer #(.width(16), .enable("false")) multiplexer_1 (
    .in0(D), .in1(adder_1_out), .out(multiplexer_1_out), .sel(comparator_2_lt));
  BitSelector #(.width(16)) bitselector_1 (.in(multiplexer_3_out), .out(bitselector_1_out), .sel(4'b1111));
  BitSelector #(.width(16)) bitselector_2 (.in(multiplexer_3_out), .out(bitselector_2_out), .sel(4'b1110));
  BitSelector #(.width(16)) bitselector_3 (.in(multiplexer_3_out), .out(bitselector_3_out), .sel(4'b1101));
  BitSelector #(.width(16)) bitselector_4 (.in(multiplexer_3_out), .out(bitselector_4_out), .sel(4'b1100));
  BitSelector #(.width(16)) bitselector_5 (.in(multiplexer_3_out), .out(bitselector_5_out), .sel(4'b1011));
  BitSelector #(.width(16)) bitselector_6 (.in(multiplexer_3_out), .out(bitselector_6_out), .sel(4'b1010));
  BitSelector #(.width(16)) bitselector_7 (.in(multiplexer_3_out), .out(bitselector_7_out), .sel(4'b1001));
  BitSelector #(.width(16)) bitselector_8 (.in(multiplexer_3_out), .out(bitselector_8_out), .sel(4'b1000));
  BitSelector #(.width(16)) bitselector_9 (.in(multiplexer_3_out), .out(bitselector_9_out), .sel(4'b0111));
  BitSelector #(.width(16)) bitselector_10 (.in(multiplexer_3_out), .out(bitselector_10_out), .sel(4'b0110));
  BitSelector #(.width(16)) bitselector_11 (.in(multiplexer_3_out), .out(bitselector_11_out), .sel(4'b0101));
  BitSelector #(.width(16)) bitselector_12 (.in(multiplexer_3_out), .out(bitselector_12_out), .sel(4'b0100));
  BitSelector #(.width(16)) bitselector_13 (.in(multiplexer_3_out), .out(bitselector_13_out), .sel(4'b0011));
  BitSelector #(.width(16)) bitselector_14 (.in(multiplexer_3_out), .out(bitselector_14_out), .sel(4'b0010));
  BitSelector #(.width(16)) bitselector_15 (.in(multiplexer_3_out), .out(bitselector_15_out), .sel(4'b0001));
  BitSelector #(.width(16)) bitselector_16 (.in(multiplexer_3_out), .out(bitselector_16_out), .sel(4'b0000));
  D_Flip_Flop d_ff_1 (.D(and_1_out), .clk(CLK), .Q(FDBZ));  // open: Qn, preset, reset
  D_Flip_Flop Reset (.D(RST), .clk(CLK), .Q(Reset_q));  // open: Qn, preset, reset
  Adder #(.width(16)) adder_2 (.a({16{1'b0}}), .b(16'h1), .out(adder_2_out));  // open: cin, cout
  Adder #(.width(16)) adder_3 (.a(shifter_1_out), .b(16'h1), .out(adder_3_out));  // open: cin, cout
  Adder #(.width(16)) adder_4 (.a(shifter_2_out), .b(16'h1), .out(adder_4_out));  // open: cin, cout
  Adder #(.width(16)) adder_5 (.a(shifter_3_out), .b(16'h1), .out(adder_5_out));  // open: cin, cout
  Adder #(.width(16)) adder_6 (.a(shifter_4_out), .b(16'h1), .out(adder_6_out));  // open: cin, cout
  Adder #(.width(16)) adder_7 (.a(shifter_5_out), .b(16'h1), .out(adder_7_out));  // open: cin, cout
  Adder #(.width(16)) adder_8 (.a(shifter_6_out), .b(16'h1), .out(adder_8_out));  // open: cin, cout
  Adder #(.width(16)) adder_9 (.a(shifter_7_out), .b(16'h1), .out(adder_9_out));  // open: cin, cout
  Adder #(.width(16)) adder_10 (.a(shifter_8_out), .b(16'h1), .out(adder_10_out));  // open: cin, cout
  Adder #(.width(16)) adder_11 (.a(shifter_9_out), .b(16'h1), .out(adder_11_out));  // open: cin, cout
  Adder #(.width(16)) adder_12 (.a(shifter_10_out), .b(16'h1), .out(adder_12_out));  // open: cin, cout
  Adder #(.width(16)) adder_13 (.a(shifter_11_out), .b(16'h1), .out(adder_13_out));  // open: cin, cout
  Adder #(.width(16)) adder_14 (.a(shifter_12_out), .b(16'h1), .out(adder_14_out));  // open: cin, cout
  Adder #(.width(16)) adder_15 (.a(shifter_13_out), .b(16'h1), .out(adder_15_out));  // open: cin, cout
  Adder #(.width(16)) adder_16 (.a(shifter_14_out), .b(16'h1), .out(adder_16_out));  // open: cin, cout
  Adder #(.width(16)) adder_17 (.a(shifter_15_out), .b(16'h1), .out(adder_17_out));  // open: cin, cout
  assign not_3_out = ~A;  // NOT_Gate not_3, 16 bits wide
  Adder #(.width(16)) adder_18 (.a(not_3_out), .b(16'h1), .out(adder_18_out));  // open: cin, cout
  or or_1 (ACK, or_18_out, FDBZ);
  Multiplexer #(.width(16), .enable("false")) multiplexer_2 (
    .in0(multiplexer_25_out), .in1({16{1'b0}}), .out(R), .sel(FDBZ));
  Multiplexer #(.width(16), .enable("false")) multiplexer_3 (
    .in0(A), .in1(adder_18_out), .out(multiplexer_3_out), .sel(comparator_3_lt));
  Multiplexer #(.width(16), .enable("false")) multiplexer_4 (
    .in0({16{1'b0}}), .in1(adder_2_out), .out(multiplexer_4_out), .sel(bitselector_1_out));
  Multiplexer #(.width(16), .enable("false")) multiplexer_5 (
    .in0(shifter_1_out), .in1(adder_3_out), .out(multiplexer_5_out), .sel(bitselector_2_out));
  Multiplexer #(.width(16), .enable("false")) multiplexer_6 (
    .in0(shifter_2_out), .in1(adder_4_out), .out(multiplexer_6_out), .sel(bitselector_3_out));
  Multiplexer #(.width(16), .enable("false")) multiplexer_7 (
    .in0(shifter_3_out), .in1(adder_5_out), .out(multiplexer_7_out), .sel(bitselector_4_out));
  Multiplexer #(.width(16), .enable("false")) multiplexer_8 (
    .in0(shifter_4_out), .in1(adder_6_out), .out(multiplexer_8_out), .sel(bitselector_5_out));
  Multiplexer #(.width(16), .enable("false")) multiplexer_9 (
    .in0(shifter_5_out), .in1(adder_7_out), .out(multiplexer_9_out), .sel(bitselector_6_out));
  Multiplexer #(.width(16), .enable("false")) multiplexer_10 (
    .in0(shifter_8_out), .in1(adder_10_out), .out(multiplexer_10_out), .sel(bitselector_9_out));
  Multiplexer #(.width(16), .enable("false")) multiplexer_11 (
    .in0(shifter_9_out), .in1(adder_11_out), .out(multiplexer_11_out), .sel(bitselector_10_out));
  Multiplexer #(.width(16), .enable("false")) multiplexer_12 (
    .in0(shifter_10_out), .in1(adder_12_out), .out(multiplexer_12_out), .sel(bitselector_11_out));
  Multiplexer #(.width(16), .enable("false")) multiplexer_13 (
    .in0(shifter_11_out), .in1(adder_13_out), .out(multiplexer_13_out), .sel(bitselector_12_out));
  Multiplexer #(.width(16), .enable("false")) multiplexer_14 (
    .in0(shifter_12_out), .in1(adder_14_out), .out(multiplexer_14_out), .sel(bitselector_13_out));
  Multiplexer #(.width(16), .enable("false")) multiplexer_15 (
    .in0(shifter_13_out), .in1(adder_15_out), .out(multiplexer_15_out), .sel(bitselector_14_out));
  Multiplexer #(.width(16), .enable("false")) multiplexer_16 (
    .in0(shifter_14_out), .in1(adder_16_out), .out(multiplexer_16_out), .sel(bitselector_15_out));
  Multiplexer #(.width(16), .enable("false")) multiplexer_17 (
    .in0(shifter_15_out), .in1(adder_17_out), .out(multiplexer_17_out), .sel(bitselector_16_out));
  Multiplexer #(.width(16), .enable("false")) multiplexer_18 (
    .in0(shifter_6_out), .in1(adder_8_out), .out(multiplexer_18_out), .sel(bitselector_7_out));
  Multiplexer #(.width(16), .enable("false")) multiplexer_19 (
    .in0(shifter_7_out), .in1(adder_9_out), .out(multiplexer_19_out), .sel(bitselector_8_out));
  Multiplexer #(.width(16), .enable("false")) multiplexer_20 (
    .in0(multiplexer_24_out), .in1(multiplexer_74_out), .out(Q), .sel(FDBZ));
  assign not_4_out = ~register_6_q;  // NOT_Gate not_4, 16 bits wide
  Adder #(.width(16)) adder_19 (.a(not_4_out), .b(16'h1), .out(adder_19_out));  // open: cin, cout
  Comparator #(.width(16), .mode("unsigned")) comparator_4 (
    .a(multiplexer_4_out), .b(multiplexer_1_out), .gt(comparator_4_gt), .eq(comparator_4_eq));  // open: lt
  Comparator #(.width(16), .mode("unsigned")) comparator_5 (
    .a(multiplexer_5_out), .b(multiplexer_1_out), .gt(comparator_5_gt), .eq(comparator_5_eq));  // open: lt
  Comparator #(.width(16), .mode("unsigned")) comparator_6 (
    .a(multiplexer_6_out), .b(multiplexer_1_out), .gt(comparator_6_gt), .eq(comparator_6_eq));  // open: lt
  Comparator #(.width(16), .mode("unsigned")) comparator_7 (
    .a(multiplexer_7_out), .b(multiplexer_1_out), .gt(comparator_7_gt), .eq(comparator_7_eq));  // open: lt
  Comparator #(.width(16), .mode("unsigned")) comparator_8 (
    .a(multiplexer_8_out), .b(multiplexer_1_out), .gt(comparator_8_gt), .eq(comparator_8_eq));  // open: lt
  Comparator #(.width(16), .mode("unsigned")) comparator_9 (
    .a(multiplexer_9_out), .b(multiplexer_1_out), .gt(comparator_9_gt), .eq(comparator_9_eq));  // open: lt
  Comparator #(.width(16), .mode("unsigned")) comparator_10 (
    .a(multiplexer_10_out), .b(multiplexer_1_out), .gt(comparator_10_gt), .eq(comparator_10_eq));  // open: lt
  Comparator #(.width(16), .mode("unsigned")) comparator_11 (
    .a(multiplexer_11_out), .b(multiplexer_1_out), .gt(comparator_11_gt), .eq(comparator_11_eq));  // open: lt
  Comparator #(.width(16), .mode("unsigned")) comparator_12 (
    .a(multiplexer_12_out), .b(multiplexer_1_out), .gt(comparator_12_gt), .eq(comparator_12_eq));  // open: lt
  Comparator #(.width(16), .mode("unsigned")) comparator_13 (
    .a(multiplexer_13_out), .b(multiplexer_1_out), .gt(comparator_13_gt), .eq(comparator_13_eq));  // open: lt
  Comparator #(.width(16), .mode("unsigned")) comparator_14 (
    .a(multiplexer_14_out), .b(multiplexer_1_out), .gt(comparator_14_gt), .eq(comparator_14_eq));  // open: lt
  Comparator #(.width(16), .mode("unsigned")) comparator_15 (
    .a(multiplexer_17_out), .b(multiplexer_1_out), .gt(comparator_15_gt), .eq(comparator_15_eq));  // open: lt
  xor xor_1 (xor_1_out, comparator_3_lt, comparator_2_lt);
  or or_2 (or_2_out, comparator_4_gt, comparator_4_eq);
  or or_3 (or_3_out, comparator_5_gt, comparator_5_eq);
  or or_4 (or_4_out, comparator_6_gt, comparator_6_eq);
  or or_5 (or_5_out, comparator_7_gt, comparator_7_eq);
  or or_6 (or_6_out, comparator_8_gt, comparator_8_eq);
  or or_7 (or_7_out, comparator_9_gt, comparator_9_eq);
  Comparator #(.width(16), .mode("unsigned")) comparator_16 (
    .a(multiplexer_18_out), .b(multiplexer_1_out), .gt(comparator_16_gt), .eq(comparator_16_eq));  // open: lt
  or or_8 (or_8_out, comparator_16_gt, comparator_16_eq);
  Comparator #(.width(16), .mode("unsigned")) comparator_17 (
    .a(multiplexer_19_out), .b(multiplexer_1_out), .gt(comparator_17_gt), .eq(comparator_17_eq));  // open: lt
  or or_9 (or_9_out, comparator_10_gt, comparator_10_eq);
  or or_10 (or_10_out, comparator_11_gt, comparator_11_eq);
  or or_11 (or_11_out, comparator_12_gt, comparator_12_eq);
  or or_12 (or_12_out, comparator_13_gt, comparator_13_eq);
  or or_13 (or_13_out, comparator_14_gt, comparator_14_eq);
  Comparator #(.width(16), .mode("unsigned")) comparator_18 (
    .a(multiplexer_15_out), .b(multiplexer_1_out), .gt(comparator_18_gt), .eq(comparator_18_eq));  // open: lt
  or or_14 (or_14_out, comparator_18_gt, comparator_18_eq);
  Comparator #(.width(16), .mode("unsigned")) comparator_19 (
    .a(multiplexer_16_out), .b(multiplexer_1_out), .gt(comparator_19_gt), .eq(comparator_19_eq));  // open: lt
  or or_15 (or_15_out, comparator_19_gt, comparator_19_eq);
  or or_16 (or_16_out, comparator_15_gt, comparator_15_eq);
  Multiplexer #(.width(16), .enable("false")) multiplexer_21 (
    .in0(register_6_q), .in1(adder_19_out), .out(multiplexer_21_out), .sel(xor_1_out));
  Subtractor #(.width(16)) subtractor_1 (
    .a(multiplexer_4_out), .b(multiplexer_1_out), .out(subtractor_1_out));  // open: bin, bout
  or or_17 (or_17_out, comparator_17_gt, comparator_17_eq);
  assign not_5_out = ~register_31_q;  // NOT_Gate not_5, 16 bits wide
  Adder #(.width(16)) adder_20 (.a(not_5_out), .b(16'h1), .out(adder_20_out));  // open: cin, cout
  Comparator #(.width(16)) comparator_20 (
    .a(multiplexer_21_out), .b({16{1'b0}}), .lt(comparator_20_lt));  // open: gt, eq
  Subtractor #(.width(16)) subtractor_2 (
    .a(multiplexer_5_out), .b(multiplexer_1_out), .out(subtractor_2_out));  // open: bin, bout
  Subtractor #(.width(16)) subtractor_3 (
    .a(multiplexer_6_out), .b(multiplexer_1_out), .out(subtractor_3_out));  // open: bin, bout
  Subtractor #(.width(16)) subtractor_4 (
    .a(multiplexer_8_out), .b(multiplexer_1_out), .out(subtractor_4_out));  // open: bin, bout
  Subtractor #(.width(16)) subtractor_5 (
    .a(multiplexer_9_out), .b(multiplexer_1_out), .out(subtractor_5_out));  // open: bin, bout
  Subtractor #(.width(16)) subtractor_6 (
    .a(multiplexer_19_out), .b(multiplexer_1_out), .out(subtractor_6_out));  // open: bin, bout
  Subtractor #(.width(16)) subtractor_7 (
    .a(multiplexer_10_out), .b(multiplexer_1_out), .out(subtractor_7_out));  // open: bin, bout
  Subtractor #(.width(16)) subtractor_8 (
    .a(multiplexer_12_out), .b(multiplexer_1_out), .out(subtractor_8_out));  // open: bin, bout
  Subtractor #(.width(16)) subtractor_9 (
    .a(multiplexer_15_out), .b(multiplexer_1_out), .out(subtractor_9_out));  // open: bin, bout
  Subtractor #(.width(16)) subtractor_10 (
    .a(multiplexer_16_out), .b(multiplexer_1_out), .out(subtractor_10_out));  // open: bin, bout
  Subtractor #(.width(16)) subtractor_11 (
    .a(multiplexer_17_out), .b(multiplexer_1_out), .out(subtractor_11_out));  // open: bin, bout
  Multiplexer #(.width(16), .enable("false")) multiplexer_22 (
    .in0(register_31_q), .in1(adder_20_out), .out(multiplexer_22_out), .sel(xor_1_out));
  Adder #(.width(16)) adder_21 (.a(multiplexer_1_out), .b(multiplexer_21_out), .out(adder_21_out));  // open: cin, cout
  Multiplexer #(.width(16), .enable("false")) multiplexer_23 (
    .in0(multiplexer_4_out), .in1(subtractor_1_out), .out(multiplexer_23_out), .sel(or_2_out));
  Subtractor #(.width(16)) subtractor_12 (
    .a(subtractor_4_out), .b(multiplexer_1_out), .out(subtractor_12_out));  // open: bin, bout
  Subtractor #(.width(16)) subtractor_13 (
    .a(multiplexer_18_out), .b(multiplexer_1_out), .out(subtractor_13_out));  // open: bin, bout
  Subtractor #(.width(16)) subtractor_14 (
    .a(multiplexer_11_out), .b(multiplexer_1_out), .out(subtractor_14_out));  // open: bin, bout
  Subtractor #(.width(16)) subtractor_15 (
    .a(multiplexer_13_out), .b(multiplexer_1_out), .out(subtractor_15_out));  // open: bin, bout
  Subtractor #(.width(16)) subtractor_16 (
    .a(multiplexer_14_out), .b(multiplexer_1_out), .out(subtractor_16_out));  // open: bin, bout
  Multiplexer #(.width(16), .enable("false")) multiplexer_24 (
    .in0(multiplexer_22_out), .in1(subtractor_17_out), .out(multiplexer_24_out), .sel(comparator_20_lt));
  Subtractor #(.width(16)) subtractor_17 (
    .a(multiplexer_22_out), .b(16'h1), .out(subtractor_17_out));  // open: bin, bout
  Multiplexer #(.width(16), .enable("false")) multiplexer_25 (
    .in0(multiplexer_21_out), .in1(adder_21_out), .out(multiplexer_25_out), .sel(comparator_20_lt));
  Multiplexer #(.width(16), .enable("false")) multiplexer_26 (
    .in0(multiplexer_5_out), .in1(subtractor_2_out), .out(multiplexer_26_out), .sel(or_3_out));
  Multiplexer #(.width(16), .enable("false")) multiplexer_27 (
    .in0(multiplexer_6_out), .in1(subtractor_3_out), .out(multiplexer_27_out), .sel(or_4_out));
  Multiplexer #(.width(16), .enable("false")) multiplexer_28 (
    .in0(multiplexer_7_out), .in1(subtractor_12_out), .out(multiplexer_28_out), .sel(or_5_out));
  Multiplexer #(.width(16), .enable("false")) multiplexer_29 (
    .in0(multiplexer_8_out), .in1(subtractor_4_out), .out(multiplexer_29_out), .sel(or_6_out));
  Multiplexer #(.width(16), .enable("false")) multiplexer_30 (
    .in0(multiplexer_9_out), .in1(subtractor_5_out), .out(multiplexer_30_out), .sel(or_7_out));
  Multiplexer #(.width(16), .enable("false")) multiplexer_31 (
    .in0(multiplexer_18_out), .in1(subtractor_13_out), .out(multiplexer_31_out), .sel(or_8_out));
  Multiplexer #(.width(16), .enable("false")) multiplexer_32 (
    .in0(multiplexer_19_out), .in1(subtractor_6_out), .out(multiplexer_32_out), .sel(or_17_out));
  Multiplexer #(.width(16), .enable("false")) multiplexer_33 (
    .in0(multiplexer_10_out), .in1(subtractor_7_out), .out(multiplexer_33_out), .sel(or_9_out));
  Multiplexer #(.width(16), .enable("false")) multiplexer_34 (
    .in0(multiplexer_11_out), .in1(subtractor_14_out), .out(multiplexer_34_out), .sel(or_10_out));
  Multiplexer #(.width(16), .enable("false")) multiplexer_35 (
    .in0(multiplexer_12_out), .in1(subtractor_8_out), .out(multiplexer_35_out), .sel(or_11_out));
  Multiplexer #(.width(16), .enable("false")) multiplexer_36 (
    .in0(multiplexer_13_out), .in1(subtractor_15_out), .out(multiplexer_36_out), .sel(or_12_out));
  Multiplexer #(.width(16), .enable("false")) multiplexer_37 (
    .in0(multiplexer_14_out), .in1(subtractor_16_out), .out(multiplexer_37_out), .sel(or_13_out));
  Multiplexer #(.width(16), .enable("false")) multiplexer_38 (
    .in0(multiplexer_15_out), .in1(subtractor_9_out), .out(multiplexer_38_out), .sel(or_14_out));
  Multiplexer #(.width(16), .enable("false")) multiplexer_39 (
    .in0(multiplexer_16_out), .in1(subtractor_10_out), .out(multiplexer_39_out), .sel(or_15_out));
  Multiplexer #(.width(16), .enable("false")) multiplexer_40 (
    .in0(multiplexer_17_out), .in1(subtractor_11_out), .out(multiplexer_40_out), .sel(or_16_out));
  Multiplexer #(.width(16), .enable("false")) multiplexer_41 (
    .in0({16{1'b0}}), .in1(multiplexer_23_out), .out(multiplexer_41_out), .sel(REQ));
  Multiplexer #(.width(16), .enable("false")) multiplexer_42 (
    .in0({16{1'b0}}), .in1(multiplexer_26_out), .out(multiplexer_42_out), .sel(REQ));
  Multiplexer #(.width(16), .enable("false")) multiplexer_43 (
    .in0({16{1'b0}}), .in1(multiplexer_27_out), .out(multiplexer_43_out), .sel(REQ));
  Multiplexer #(.width(16), .enable("false")) multiplexer_44 (
    .in0({16{1'b0}}), .in1(multiplexer_28_out), .out(multiplexer_44_out), .sel(REQ));
  Multiplexer #(.width(16), .enable("false")) multiplexer_45 (
    .in0({16{1'b0}}), .in1(multiplexer_29_out), .out(multiplexer_45_out), .sel(REQ));
  Multiplexer #(.width(16), .enable("false")) multiplexer_46 (
    .in0({16{1'b0}}), .in1(multiplexer_30_out), .out(multiplexer_46_out), .sel(REQ));
  Multiplexer #(.width(16), .enable("false")) multiplexer_47 (
    .in0({16{1'b0}}), .in1(multiplexer_31_out), .out(multiplexer_47_out), .sel(REQ));
  Multiplexer #(.width(16), .enable("false")) multiplexer_48 (
    .in0({16{1'b0}}), .in1(multiplexer_32_out), .out(multiplexer_48_out), .sel(REQ));
  Multiplexer #(.width(16), .enable("false")) multiplexer_49 (
    .in0({16{1'b0}}), .in1(multiplexer_33_out), .out(multiplexer_49_out), .sel(REQ));
  Multiplexer #(.width(16), .enable("false")) multiplexer_50 (
    .in0({16{1'b0}}), .in1(multiplexer_34_out), .out(multiplexer_50_out), .sel(REQ));
  Multiplexer #(.width(16), .enable("false")) multiplexer_51 (
    .in0({16{1'b0}}), .in1(multiplexer_35_out), .out(multiplexer_51_out), .sel(REQ));
  Multiplexer #(.width(16), .enable("false")) multiplexer_52 (
    .in0({16{1'b0}}), .in1(multiplexer_36_out), .out(multiplexer_52_out), .sel(REQ));
  Multiplexer #(.width(16), .enable("false")) multiplexer_53 (
    .in0({16{1'b0}}), .in1(multiplexer_37_out), .out(multiplexer_53_out), .sel(REQ));
  Multiplexer #(.width(16), .enable("false")) multiplexer_54 (
    .in0({16{1'b0}}), .in1(multiplexer_38_out), .out(multiplexer_54_out), .sel(REQ));
  Multiplexer #(.width(16), .enable("false")) multiplexer_55 (
    .in0({16{1'b0}}), .in1(multiplexer_39_out), .out(multiplexer_55_out), .sel(REQ));
  Multiplexer #(.width(16), .enable("false")) multiplexer_56 (
    .in0({16{1'b0}}), .in1(multiplexer_40_out), .out(multiplexer_56_out), .sel(REQ));
  Register #(.width(16)) register_1 (.D(multiplexer_41_out), .clk(CLK), .Q(register_1_q), .clr(Reset_q));  // open: en
  Register #(.width(16)) register_2 (.D(multiplexer_42_out), .clk(CLK), .Q(register_2_q), .clr(Reset_q));  // open: en
  Register #(.width(16)) register_3 (.D(multiplexer_43_out), .clk(CLK), .Q(register_3_q), .clr(Reset_q));  // open: en
  Register #(.width(16)) register_4 (.D(multiplexer_44_out), .clk(CLK), .Q(register_4_q), .clr(Reset_q));  // open: en
  Register #(.width(16)) register_5 (.D(multiplexer_45_out), .clk(CLK), .Q(register_5_q), .clr(Reset_q));  // open: en
  Register #(.width(16)) register_6 (.D(multiplexer_56_out), .clk(CLK), .Q(register_6_q), .clr(Reset_q));  // open: en
  Comparator #(.width(16)) comparator_21 (
    .a(A), .b({16{1'b0}}), .gt(comparator_21_gt), .lt(comparator_21_lt));  // open: eq
  Register #(.width(16)) register_7 (.D(multiplexer_46_out), .clk(CLK), .Q(register_7_q), .clr(Reset_q));  // open: en
  Register #(.width(16)) register_8 (.D(multiplexer_47_out), .clk(CLK), .Q(register_8_q), .clr(Reset_q));  // open: en
  Register #(.width(16)) register_9 (.D(multiplexer_48_out), .clk(CLK), .Q(register_9_q), .clr(Reset_q));  // open: en
  Register #(.width(16)) register_10 (.D(multiplexer_49_out), .clk(CLK), .Q(register_10_q), .clr(Reset_q));  // open: en
  Register #(.width(16)) register_11 (.D(multiplexer_50_out), .clk(CLK), .Q(register_11_q), .clr(Reset_q));  // open: en
  Register #(.width(16)) register_12 (.D(multiplexer_51_out), .clk(CLK), .Q(register_12_q), .clr(Reset_q));  // open: en
  Register #(.width(16)) register_13 (.D(multiplexer_52_out), .clk(CLK), .Q(register_13_q), .clr(Reset_q));  // open: en
  Register #(.width(16)) register_14 (.D(multiplexer_53_out), .clk(CLK), .Q(register_14_q), .clr(Reset_q));  // open: en
  Register #(.width(16)) register_15 (.D(multiplexer_54_out), .clk(CLK), .Q(register_15_q), .clr(Reset_q));  // open: en
  Register #(.width(16)) register_16 (.D(multiplexer_55_out), .clk(CLK), .Q(register_16_q), .clr(Reset_q));  // open: en
  Multiplexer #(.width(16), .enable("false")) multiplexer_57 (
    .in0({16{1'b0}}), .in1(16'h7fff), .out(multiplexer_57_out), .sel(comparator_21_gt));
  Adder #(.width(16)) adder_22 (.a({16{1'b0}}), .b(16'h8000), .out(adder_22_out));  // open: cin, cout
  Adder #(.width(16)) adder_23 (.a(register_17_q), .b(16'h4000), .out(adder_23_out));  // open: cin, cout
  Adder #(.width(16)) adder_24 (.a(register_19_q), .b(16'h2000), .out(adder_24_out));  // open: cin, cout
  Adder #(.width(16)) adder_25 (.a(register_20_q), .b(16'h1000), .out(adder_25_out));  // open: cin, cout
  Adder #(.width(16)) adder_26 (.a(register_21_q), .b(16'h800), .out(adder_26_out));  // open: cin, cout
  Adder #(.width(16)) adder_27 (.a(register_22_q), .b(16'h400), .out(adder_27_out));  // open: cin, cout
  Adder #(.width(16)) adder_28 (.a(register_23_q), .b(16'h200), .out(adder_28_out));  // open: cin, cout
  Adder #(.width(16)) adder_29 (.a(register_25_q), .b(16'h80), .out(adder_29_out));  // open: cin, cout
  Adder #(.width(16)) adder_30 (.a(register_26_q), .b(16'h40), .out(adder_30_out));  // open: cin, cout
  Multiplexer #(.width(16), .enable("false")) multiplexer_58 (
    .in0({16{1'b0}}), .in1(adder_22_out), .out(multiplexer_58_out), .sel(or_2_out));
  Multiplexer #(.width(16), .enable("false")) multiplexer_59 (
    .in0(register_17_q), .in1(adder_23_out), .out(multiplexer_59_out), .sel(or_3_out));
  Multiplexer #(.width(16), .enable("false")) multiplexer_60 (
    .in0(register_19_q), .in1(adder_24_out), .out(multiplexer_60_out), .sel(or_4_out));
  Multiplexer #(.width(16), .enable("false")) multiplexer_61 (
    .in0(register_20_q), .in1(adder_25_out), .out(multiplexer_61_out), .sel(or_5_out));
  Multiplexer #(.width(16), .enable("false")) multiplexer_62 (
    .in0(register_21_q), .in1(adder_26_out), .out(multiplexer_62_out), .sel(or_6_out));
  Multiplexer #(.width(16), .enable("false")) multiplexer_63 (
    .in0(register_22_q), .in1(adder_27_out), .out(multiplexer_63_out), .sel(or_7_out));
  Multiplexer #(.width(16), .enable("false")) multiplexer_64 (
    .in0(register_23_q), .in1(adder_28_out), .out(multiplexer_64_out), .sel(or_8_out));
  Multiplexer #(.width(16), .enable("false")) multiplexer_65 (
    .in0(register_24_q), .in1(adder_31_out), .out(multiplexer_65_out), .sel(or_17_out));
  Adder #(.width(16)) adder_31 (.a(register_24_q), .b(16'h100), .out(adder_31_out));  // open: cin, cout
  Multiplexer #(.width(16), .enable("false")) multiplexer_66 (
    .in0(register_25_q), .in1(adder_29_out), .out(multiplexer_66_out), .sel(or_9_out));
  Multiplexer #(.width(16), .enable("false")) multiplexer_67 (
    .in0(register_26_q), .in1(adder_30_out), .out(multiplexer_67_out), .sel(or_10_out));
  Adder #(.width(16)) adder_32 (.a(register_27_q), .b(16'h20), .out(adder_32_out));  // open: cin, cout
  Multiplexer #(.width(16), .enable("false")) multiplexer_68 (
    .in0(register_27_q), .in1(adder_32_out), .out(multiplexer_68_out), .sel(or_11_out));
  Multiplexer #(.width(16), .enable("false")) multiplexer_69 (
    .in0(register_28_q), .in1(adder_33_out), .out(multiplexer_69_out), .sel(or_12_out));
  Adder #(.width(16)) adder_33 (.a(register_28_q), .b(16'h10), .out(adder_33_out));  // open: cin, cout
  Multiplexer #(.width(16), .enable("false")) multiplexer_70 (
    .in0(register_29_q), .in1(adder_34_out), .out(multiplexer_70_out), .sel(or_13_out));
  Adder #(.width(16)) adder_34 (.a(register_29_q), .b(16'h8), .out(adder_34_out));  // open: cin, cout
  Multiplexer #(.width(16), .enable("false")) multiplexer_71 (
    .in0(register_18_q), .in1(adder_35_out), .out(multiplexer_71_out), .sel(or_14_out));
  Adder #(.width(16)) adder_35 (.a(register_18_q), .b(16'h4), .out(adder_35_out));  // open: cin, cout
  Adder #(.width(16)) adder_36 (.a(register_30_q), .b(16'h2), .out(adder_36_out));  // open: cin, cout
  Multiplexer #(.width(16), .enable("false")) multiplexer_72 (
    .in0(register_30_q), .in1(adder_36_out), .out(multiplexer_72_out), .sel(or_15_out));
  Multiplexer #(.width(16), .enable("false")) multiplexer_73 (
    .in0(register_32_q), .in1(adder_37_out), .out(multiplexer_73_out), .sel(or_16_out));
  Adder #(.width(16)) adder_37 (.a(register_32_q), .b(16'h1), .out(adder_37_out));  // open: cin, cout
  Register #(.width(16)) register_17 (.D(multiplexer_75_out), .clk(CLK), .Q(register_17_q), .clr(Reset_q));  // open: en
  Multiplexer #(.width(16), .enable("false")) multiplexer_74 (
    .in0(multiplexer_57_out), .in1(16'h8000), .out(multiplexer_74_out), .sel(comparator_21_lt));
  Multiplexer #(.width(16), .enable("false")) multiplexer_75 (
    .in0({16{1'b0}}), .in1(multiplexer_58_out), .out(multiplexer_75_out), .sel(REQ));
  Multiplexer #(.width(16), .enable("false")) multiplexer_76 (
    .in0({16{1'b0}}), .in1(multiplexer_59_out), .out(multiplexer_76_out), .sel(REQ));
  Multiplexer #(.width(16), .enable("false")) multiplexer_77 (
    .in0({16{1'b0}}), .in1(multiplexer_60_out), .out(multiplexer_77_out), .sel(REQ));
  Multiplexer #(.width(16), .enable("false")) multiplexer_78 (
    .in0({16{1'b0}}), .in1(multiplexer_61_out), .out(multiplexer_78_out), .sel(REQ));
  Multiplexer #(.width(16), .enable("false")) multiplexer_79 (
    .in0({16{1'b0}}), .in1(multiplexer_62_out), .out(multiplexer_79_out), .sel(REQ));
  Multiplexer #(.width(16), .enable("false")) multiplexer_80 (
    .in0({16{1'b0}}), .in1(multiplexer_63_out), .out(multiplexer_80_out), .sel(REQ));
  Multiplexer #(.width(16), .enable("false")) multiplexer_81 (
    .in0({16{1'b0}}), .in1(multiplexer_64_out), .out(multiplexer_81_out), .sel(REQ));
  Multiplexer #(.width(16), .enable("false")) multiplexer_82 (
    .in0({16{1'b0}}), .in1(multiplexer_65_out), .out(multiplexer_82_out), .sel(REQ));
  Multiplexer #(.width(16), .enable("false")) multiplexer_83 (
    .in0({16{1'b0}}), .in1(multiplexer_66_out), .out(multiplexer_83_out), .sel(REQ));
  Multiplexer #(.width(16), .enable("false")) multiplexer_84 (
    .in0({16{1'b0}}), .in1(multiplexer_67_out), .out(multiplexer_84_out), .sel(REQ));
  Multiplexer #(.width(16), .enable("false")) multiplexer_85 (
    .in0({16{1'b0}}), .in1(multiplexer_68_out), .out(multiplexer_85_out), .sel(REQ));
  Multiplexer #(.width(16), .enable("false")) multiplexer_86 (
    .in0({16{1'b0}}), .in1(multiplexer_69_out), .out(multiplexer_86_out), .sel(REQ));
  Multiplexer #(.width(16), .enable("false")) multiplexer_87 (
    .in0({16{1'b0}}), .in1(multiplexer_70_out), .out(multiplexer_87_out), .sel(REQ));
  Multiplexer #(.width(16), .enable("false")) multiplexer_88 (
    .in0({16{1'b0}}), .in1(multiplexer_71_out), .out(multiplexer_88_out), .sel(REQ));
  Multiplexer #(.width(16), .enable("false")) multiplexer_89 (
    .in0({16{1'b0}}), .in1(multiplexer_72_out), .out(multiplexer_89_out), .sel(REQ));
  Multiplexer #(.width(16), .enable("false")) multiplexer_90 (
    .in0({16{1'b0}}), .in1(multiplexer_73_out), .out(multiplexer_90_out), .sel(REQ));
  Register #(.width(16)) register_18 (.D(multiplexer_87_out), .clk(CLK), .Q(register_18_q), .clr(Reset_q));  // open: en
  Register #(.width(16)) register_19 (.D(multiplexer_76_out), .clk(CLK), .Q(register_19_q), .clr(Reset_q));  // open: en
  Register #(.width(16)) register_20 (.D(multiplexer_77_out), .clk(CLK), .Q(register_20_q), .clr(Reset_q));  // open: en
  Register #(.width(16)) register_21 (.D(multiplexer_78_out), .clk(CLK), .Q(register_21_q), .clr(Reset_q));  // open: en
  Register #(.width(16)) register_22 (.D(multiplexer_79_out), .clk(CLK), .Q(register_22_q), .clr(Reset_q));  // open: en
  Register #(.width(16)) register_23 (.D(multiplexer_80_out), .clk(CLK), .Q(register_23_q), .clr(Reset_q));  // open: en
  Register #(.width(16)) register_24 (.D(multiplexer_81_out), .clk(CLK), .Q(register_24_q), .clr(Reset_q));  // open: en
  Register #(.width(16)) register_25 (.D(multiplexer_82_out), .clk(CLK), .Q(register_25_q), .clr(Reset_q));  // open: en
  Register #(.width(16)) register_26 (.D(multiplexer_83_out), .clk(CLK), .Q(register_26_q), .clr(Reset_q));  // open: en
  Register #(.width(16)) register_27 (.D(multiplexer_84_out), .clk(CLK), .Q(register_27_q), .clr(Reset_q));  // open: en
  Register #(.width(16)) register_28 (.D(multiplexer_85_out), .clk(CLK), .Q(register_28_q), .clr(Reset_q));  // open: en
  Register #(.width(16)) register_29 (.D(multiplexer_86_out), .clk(CLK), .Q(register_29_q), .clr(Reset_q));  // open: en
  Register #(.width(16)) register_30 (.D(multiplexer_88_out), .clk(CLK), .Q(register_30_q), .clr(Reset_q));  // open: en
  Register #(.width(16)) register_31 (.D(multiplexer_90_out), .clk(CLK), .Q(register_31_q), .clr(Reset_q));  // open: en
  Register #(.width(16)) register_32 (.D(multiplexer_89_out), .clk(CLK), .Q(register_32_q), .clr(Reset_q));  // open: en
  BitSelector #(.width(16)) bitselector_17 (.in(multiplexer_3_out), .out(bitselector_17_out), .sel(4'b1111));
  BitSelector #(.width(16)) bitselector_18 (.in(multiplexer_3_out), .out(bitselector_18_out), .sel(4'b1110));
  BitSelector #(.width(16)) bitselector_19 (.in(multiplexer_3_out), .out(bitselector_19_out), .sel(4'b1101));
  BitSelector #(.width(16)) bitselector_20 (.in(multiplexer_3_out), .out(bitselector_20_out), .sel(4'b1100));
  BitSelector #(.width(16)) bitselector_21 (.in(multiplexer_3_out), .out(bitselector_21_out), .sel(4'b1011));
  BitSelector #(.width(16)) bitselector_22 (.in(multiplexer_3_out), .out(bitselector_22_out), .sel(4'b1010));
  BitSelector #(.width(16)) bitselector_23 (.in(multiplexer_3_out), .out(bitselector_23_out), .sel(4'b1001));
  BitSelector #(.width(16)) bitselector_24 (.in(multiplexer_3_out), .out(bitselector_24_out), .sel(4'b1000));
  BitSelector #(.width(16)) bitselector_25 (.in(multiplexer_3_out), .out(bitselector_25_out), .sel(4'b0111));
  BitSelector #(.width(16)) bitselector_26 (.in(multiplexer_3_out), .out(bitselector_26_out), .sel(4'b0110));
  BitSelector #(.width(16)) bitselector_27 (.in(multiplexer_3_out), .out(bitselector_27_out), .sel(4'b0101));
  BitSelector #(.width(16)) bitselector_28 (.in(multiplexer_3_out), .out(bitselector_28_out), .sel(4'b0100));
  BitSelector #(.width(16)) bitselector_29 (.in(multiplexer_3_out), .out(bitselector_29_out), .sel(4'b0011));
  BitSelector #(.width(16)) bitselector_30 (.in(multiplexer_3_out), .out(bitselector_30_out), .sel(4'b0010));
  BitSelector #(.width(16)) bitselector_31 (.in(multiplexer_3_out), .out(bitselector_31_out), .sel(4'b0001));
  assign bit_extender_1_out = {{1{1'b0}}, multiplexer_93_out};  // Bit_Extender bit_extender_1
  Multiplexer #(.width(4), .enable("false")) multiplexer_91 (
    .in0(multiplexer_98_out), .in1(4'b1010), .out(multiplexer_91_out), .sel(bitselector_23_out));
  Multiplexer #(.width(5), .enable("false")) multiplexer_92 (
    .in0(bit_extender_1_out), .in1(5'b10000), .out(multiplexer_92_out), .sel(bitselector_17_out));
  Multiplexer #(.width(4), .enable("false")) multiplexer_93 (
    .in0(multiplexer_94_out), .in1(4'b1111), .out(multiplexer_93_out), .sel(bitselector_18_out));
  Multiplexer #(.width(4), .enable("false")) multiplexer_94 (
    .in0(multiplexer_95_out), .in1(4'b1110), .out(multiplexer_94_out), .sel(bitselector_19_out));
  Multiplexer #(.width(4), .enable("false")) multiplexer_95 (
    .in0(multiplexer_96_out), .in1(4'b1101), .out(multiplexer_95_out), .sel(bitselector_20_out));
  Multiplexer #(.width(4), .enable("false")) multiplexer_96 (
    .in0(multiplexer_97_out), .in1(4'b1100), .out(multiplexer_96_out), .sel(bitselector_21_out));
  Multiplexer #(.width(4), .enable("false")) multiplexer_97 (
    .in0(multiplexer_91_out), .in1(4'b1011), .out(multiplexer_97_out), .sel(bitselector_22_out));
  Multiplexer #(.width(4), .enable("false")) multiplexer_98 (
    .in0(multiplexer_99_out), .in1(4'b1001), .out(multiplexer_98_out), .sel(bitselector_24_out));
  Multiplexer #(.width(4), .enable("false")) multiplexer_99 (
    .in0(multiplexer_100_out), .in1(4'b1000), .out(multiplexer_99_out), .sel(bitselector_25_out));
  Multiplexer #(.width(4), .enable("false")) multiplexer_100 (
    .in0(multiplexer_101_out), .in1(4'b0111), .out(multiplexer_100_out), .sel(bitselector_26_out));
  Multiplexer #(.width(4), .enable("false")) multiplexer_101 (
    .in0(multiplexer_103_out), .in1(4'b0110), .out(multiplexer_101_out), .sel(bitselector_27_out));
  Multiplexer #(.width(4), .enable("false")) multiplexer_102 (
    .in0(4'b0001), .in1(4'b0010), .out(multiplexer_102_out), .sel(bitselector_31_out));
  Multiplexer #(.width(4), .enable("false")) multiplexer_103 (
    .in0(multiplexer_104_out), .in1(4'b0101), .out(multiplexer_103_out), .sel(bitselector_28_out));
  Multiplexer #(.width(4), .enable("false")) multiplexer_104 (
    .in0(multiplexer_105_out), .in1(4'b0100), .out(multiplexer_104_out), .sel(bitselector_29_out));
  Multiplexer #(.width(4), .enable("false")) multiplexer_105 (
    .in0(multiplexer_102_out), .in1(4'b0011), .out(multiplexer_105_out), .sel(bitselector_30_out));
  D_Flip_Flop d_ff_2 (.D(REQ), .clk(CLK), .Q(d_ff_2_q));  // open: Qn, preset, reset
  Subtractor #(.width(5)) subtractor_18 (.a(register_33_q), .b(5'b00001), .out(subtractor_18_out));  // open: bin, bout
  Multiplexer #(.width(5), .enable("false")) multiplexer_106 (
    .in0(multiplexer_92_out), .in1(subtractor_18_out), .out(multiplexer_106_out), .sel(d_ff_2_q));
  Register #(.width(5)) register_33 (.D(multiplexer_107_out), .clk(CLK), .Q(register_33_q), .clr(Reset_q));  // open: en
  Comparator #(.width(5), .mode("unsigned")) comparator_22 (
    .a(subtractor_18_out), .b({5{1'b0}}), .eq(comparator_22_eq));  // open: gt, lt
  Multiplexer #(.width(5), .enable("false")) multiplexer_107 (
    .in0({5{1'b0}}), .in1(multiplexer_106_out), .out(multiplexer_107_out), .sel(REQ));
  or or_18 (or_18_out, d_ff_3_q, comparator_22_eq);
  D_Flip_Flop d_ff_3 (.D(and_2_out), .clk(CLK), .Q(d_ff_3_q), .reset(Reset_q));  // open: Qn, preset
  Multiplexer #(.enable("false")) multiplexer_108 (
    .in0(comparator_22_eq), .in1(d_ff_3_q), .out(multiplexer_108_out), .sel(d_ff_3_q));
  and and_2 (and_2_out, multiplexer_108_out, REQ);

  // Notes on the sheet:
  //   Please put your deisgn below. You may also use subcircuits.
  //   However, do not move, rename, add, or delete any pins.
  //   Note that A, D, Q, and R in Hex
endmodule

module TB (
  input  [15:0] Dividend,
  input  [15:0] Divisor,
  input  REQ,
  output [15:0] Quotient,
  output [15:0] Remainder
);

  wire clock_1_out, Divider16bitSigned_ack, Divider16bitSigned_fdbz, pwr_on_reset_1_rst;

  Clock clock_1 (.out(clock_1_out));
  Clock sysclk ();  // open: out
  pwr_on_reset pwr_on_reset_1 (.CLK(clock_1_out), .RST(pwr_on_reset_1_rst));
  DUT Divider16bitSigned (
    .CLK(clock_1_out), .RST(pwr_on_reset_1_rst), .REQ(REQ), .A(Dividend), .D(Divisor),
    .ACK(Divider16bitSigned_ack), .FDBZ(Divider16bitSigned_fdbz), .Q(Quotient), .R(Remainder));
  LED ACK (.in(Divider16bitSigned_ack));
  LED DivideByZero (.in(Divider16bitSigned_fdbz));

  // Notes on the sheet:
  //   DO NOT MODIFY THIS
  //   YOU MAY TEST YOUR CIRCUITS USING THIS TO MAKE SURE YOU HAVE NOT ALTERED PIN OUT
  //   The multibit values are in Hexadeximal
endmodule

module pwr_on_reset (
  input  CLK,
  output RST
);

  wire d_ff_1_q, nor_1_out, not_1_out;

  not not_1 (not_1_out, nor_1_out);
  D_Flip_Flop d_ff_1 (.D(not_1_out), .clk(CLK), .Q(d_ff_1_q));  // open: Qn, preset, reset
  D_Flip_Flop d_ff_2 (.D(nor_1_out), .clk(CLK), .Q(RST));  // open: Qn, preset, reset
  nor nor_1 (nor_1_out, d_ff_1_q, RST);

  // Notes on the sheet:
  //   DO NOT MODIFY THIS
endmodule
