// Logisim project da3_tb.circ as structural Verilog: 3 circuits, main circuit main
module main (
  output halt,
  output [15:0] CYCLE,
  output RST,
  output REQ,
  output [15:0] A,
  output [15:0] D,
  output [15:0] Q,
  output [15:0] R,
  output FDBZ,
  output ACK,
  output [7:0] REQNUM,
  output LDCTR,
  output [3:0] CTRVALIN,
  output CTRDONE,
  output [3:0] CTRVALOUT
);

  wire and_1_out, CLK_out, counter_1_carry, counter_2_carry, d_ff_1_q, decoder_1_out0, decoder_1_out2,
       decoder_1_out4, decoder_1_out5, decoder_1_out9, decoder_1_out11, decoder_1_out12, decoder_1_out13,
       multiplexer_1_out, not_1_out, or_1_out, xor_1_out;
  wire [2:2] S0_q;

  Decoder #(.select(4)) decoder_1 (
    .out0(decoder_1_out0), .out2(decoder_1_out2), .out4(decoder_1_out4), .out5(decoder_1_out5),
    .out9(decoder_1_out9), .out11(decoder_1_out11), .out12(decoder_1_out12), .out13(decoder_1_out13),
    .sel({REQ, S0_q[2], CTRDONE, ACK}));  // open: out1, out3, out6, out7, out8, out10, out14, out15, en
  Clock sysclk ();  // open: out
  Clock CLK (.out(CLK_out));
  Counter #(.width(16), .max('hffff)) counter_1 (
    .clk(CLK_out), .carry(counter_1_carry), .Q(CYCLE));  // open: clr, load, up, count, D
  Random #(.width(4), .seed(10)) RNGRDY (.clk(CLK_out), .out(CTRVALIN));  // open: clr, next
  or or_1 (or_1_out, decoder_1_out0, decoder_1_out2, decoder_1_out4, decoder_1_out5, decoder_1_out9, decoder_1_out11, decoder_1_out12, decoder_1_out13);
  D_Flip_Flop S0 (.D(or_1_out), .clk(CLK_out), .Q(S0_q[2]), .Qn(LDCTR), .reset(RST));  // open: preset
  poweron_reset_random poweron_reset_random_1 (.CLK(CLK_out), .RST(RST));
  LED CounterIsLoading (.in(LDCTR));
  Counter #(.ongoal("stay")) counter_2 (
    .count(and_1_out), .clk(CLK_out), .carry(counter_2_carry), .Q(REQNUM));  // open: clr, load, up, D
  Counter #(.width(4), .max('hf), .ongoal("stay")) counter_3 (
    .load(LDCTR), .up(1'b1), .clk(CLK_out), .D(CTRVALIN), .carry(CTRDONE), .Q(CTRVALOUT));  // open: clr, count
  xor xor_1 (xor_1_out, REQ, S0_q[2]);
  Multiplexer #(.enable("false")) multiplexer_1 (.in0(REQ), .in1(xor_1_out), .out(multiplexer_1_out), .sel(CTRDONE));
  DUT dut_1 (.CLK(CLK_out), .RST(RST), .REQ(REQ), .A(A), .D(D), .ACK(ACK), .FDBZ(FDBZ), .Q(Q), .R(R));
  operands operands_1 (.i(REQNUM), .A(A), .D(D));
  D_Flip_Flop S1 (.D(multiplexer_1_out), .clk(CLK_out), .Q(REQ), .reset(RST));  // open: Qn, preset
  not not_1 (not_1_out, REQ);
  D_Flip_Flop d_ff_1 (.D(REQ), .clk(CLK_out), .Q(d_ff_1_q));  // open: Qn, preset, reset
  LED PowerReset (.in(RST));
  LED Request (.in(REQ));
  LED Acknowledge (.in(ACK));
  or or_2 (halt, counter_1_carry, counter_2_carry);
  and and_1 (and_1_out, not_1_out, d_ff_1_q);
endmodule

module poweron_reset_random (
  input  CLK,
  output RST
);

  wire and_1_out, clock_1_out, d_ff_1_q, not_1_out, RNGRST_out, t_ff_1_qn;

  Clock clock_1 (.out(clock_1_out));
  Random #(.width(1), .seed(20)) RNGRST (.next(t_ff_1_qn), .clk(clock_1_out), .out(RNGRST_out));  // open: clr
  T_Flip_Flop t_ff_1 (.T(and_1_out), .clk(clock_1_out), .Qn(t_ff_1_qn));  // open: Q, reset, preset
  and and_1 (and_1_out, t_ff_1_qn, not_1_out, d_ff_1_q);
  not not_1 (not_1_out, RNGRST_out);
  D_Flip_Flop d_ff_1 (.D(RNGRST_out), .clk(clock_1_out), .Q(d_ff_1_q));  // open: Qn, preset, reset
  and and_2 (RST, t_ff_1_qn, d_ff_1_q);
  TTY #(.rows(4), .cols(16)) tty_1 (.data({6'b011000, RST}), .clk(clock_1_out));  // open: we, clr
endmodule

module operands (
  input  [7:0] i,
  output [15:0] A,
  output [15:0] D
);

  ROM #(.dataWidth(16)) Dividends (.addr(i), .data(A));
  ROM #(.dataWidth(16)) Divisors (.addr(i), .data(D));

  // Notes on the sheet:
  //   contents of Dividends (hex, n*v repeats v):
  //   16*8000 16*ffff 16*0 16*1 16*7fff 16*2 16*3 16*4 16*9 16*64 16*fffe 16*fffd 16*fffc 16*fff7 16*ff9c
  //   16*f0ff
  //   contents of Divisors (hex, n*v repeats v):
  //   8000 ffff 0 1 7fff 2 3 4 9 64 fffe fffd fffc fff7 ff9c f0ff 8000 ffff 0 1 7fff 2 3 4 9 64 fffe fffd
  //   fffc fff7 ff9c f0ff 8000 ffff 0 1 7fff 2 3 4 9 64 fffe fffd fffc fff7 ff9c f0ff 8000 ffff 0 1 7fff 2
  //   3 4 9 64 fffe fffd fffc fff7 ff9c f0ff 8000 ffff 0 1 7fff 2 3 4 9 64 fffe fffd fffc fff7 ff9c f0ff
  //   8000 ffff 0 1 7fff 2 3 4 9 64 fffe fffd fffc fff7 ff9c f0ff 8000 ffff 0 1 7fff 2 3 4 9 64 fffe fffd
  //   fffc fff7 ff9c f0ff 8000 ffff 0 1 7fff 2 3 4 9 64 fffe fffd fffc fff7 ff9c f0ff 8000 ffff 0 1 7fff 2
  //   3 4 9 64 fffe fffd fffc fff7 ff9c f0ff 8000 ffff 0 1 7fff 2 3 4 9 64 fffe fffd fffc fff7 ff9c f0ff
  //   8000 ffff 0 1 7fff 2 3 4 9 64 fffe fffd fffc fff7 ff9c f0ff 8000 ffff 0 1 7fff 2 3 4 9 64 fffe fffd
  //   fffc fff7 ff9c f0ff 8000 ffff 0 1 7fff 2 3 4 9 64 fffe fffd fffc fff7 ff9c f0ff 8000 ffff 0 1 7fff 2
  //   3 4 9 64 fffe fffd fffc fff7 ff9c f0ff 8000 ffff 0 1 7fff 2 3 4 9 64 fffe fffd fffc fff7 ff9c f0ff
  //   8000 ffff 0 1 7fff 2 3 4 9 64 fffe fffd fffc fff7 ff9c f0ff
endmodule
