// Logisim project final_part2_tb.circ as structural Verilog: 1 circuit, main circuit TB
module TB (
  output halt,
  output [15:0] CYCLE,
  output RST,
  output REQ,
  output [15:0] DIN,
  output ACK,
  output [7:0] DOUT,
  output [6:0] CNTREQ,
  output [6:0] CNTACK,
  output ASSERTIONS
);

  wire and_1_out, CLK_out, clock_1_out, comparator_1_lt, counter_1_carry, counter_3_carry,
       genpulseatnegedge_1_pulse, genpulseatnegedge_2_pulse, genpulseatnegedge_3_pulse,
       genpulseatnegedge_4_pulse, not_1_out, not_2_out, or_1_out, or_2_out, sysclk_out;
  wire [6:0] subtractor_1_out;
  wire [15:0] random_1_out, register_1_q;

  Clock sysclk (.out(sysclk_out));
  Clock CLK (.out(CLK_out));
  Counter #(.width(16), .max('hffff)) counter_1 (
    .clk(CLK_out), .carry(counter_1_carry), .Q(CYCLE));  // open: clr, load, up, count, D
  not not_1 (not_1_out, REQ);
  // poweron_reset_random poweron_reset_random_1: pin names not known; wires that end beside it: sysclk_out, CLK_out, RST
  not not_2 (not_2_out, ACK);
  GenPulseAtNegEdge genpulseatnegedge_1 (.CLK(CLK_out), .X(REQ), .PULSE(genpulseatnegedge_1_pulse));
  GenPulseAtNegEdge genpulseatnegedge_2 (.CLK(CLK_out), .X(not_1_out), .PULSE(genpulseatnegedge_2_pulse));
  Counter #(.width(7), .max('h7f)) counter_2 (
    .clr(RST), .count(or_1_out), .clk(CLK_out), .Q(CNTREQ));  // open: load, up, D, carry
  or or_1 (or_1_out, genpulseatnegedge_1_pulse, genpulseatnegedge_2_pulse);
  GenPulseAtNegEdge genpulseatnegedge_3 (.CLK(CLK_out), .X(ACK), .PULSE(genpulseatnegedge_3_pulse));
  GenPulseAtNegEdge genpulseatnegedge_4 (.CLK(CLK_out), .X(not_2_out), .PULSE(genpulseatnegedge_4_pulse));
  MAIN main_1 (.CLK(CLK_out), .RST(RST), .REQ(REQ), .DIN(DIN), .ACK(ACK), .DOUT(DOUT));
  or or_2 (or_2_out, genpulseatnegedge_3_pulse, genpulseatnegedge_4_pulse);
  D_Flip_Flop d_ff_1 (.D(REQ), .clk(clock_1_out));  // open: Q, Qn, preset, reset
  Clock #(.highDuration(4), .lowDuration(4)) clock_1 (.out(clock_1_out));
  RndDlyHSClient rnddlyhsclient_1 (.CLK(CLK_out), .RST(RST), .ACK(ACK), .REQ(REQ));
  Random #(.width(16), .seed(10)) random_1 (.next(or_2_out), .clk(CLK_out), .out(random_1_out));  // open: clr
  LED led_1 (.in(RST));
  LED led_2 (.in(REQ));
  LED led_3 (.in(ACK));
  Multiplexer #(.width(16), .enable("false")) multiplexer_1 (
    .in0(register_1_q), .in1(16'hfa00), .out(DIN), .sel(and_1_out));
  Register #(.width(16)) register_1 (.D(random_1_out), .en(or_2_out), .clk(CLK_out), .Q(register_1_q));  // open: clr
  Counter #(.width(7), .max('h7f)) counter_3 (
    .clr(RST), .count(or_2_out), .clk(CLK_out), .carry(counter_3_carry), .Q(CNTACK));  // open: load, up, D
  and and_1 (and_1_out, 1'b0, comparator_1_lt);
  Comparator #(.width(16), .mode("unsigned")) comparator_1 (
    .a(16'hfa00), .b(register_1_q), .lt(comparator_1_lt));  // open: gt, eq
  or or_3 (halt, counter_1_carry, counter_3_carry);
  Subtractor #(.width(7)) subtractor_1 (.a(CNTREQ), .b(CNTACK), .out(subtractor_1_out));  // open: bin, bout
  Comparator #(.width(7)) comparator_2 (.a(subtractor_1_out), .b(7'b0000010), .lt(ASSERTIONS));  // open: gt, eq

  // Notes on the sheet:
  //   Edge@REQ
  //   Edge@ACK
  //   Change to 1 to saturate DIN
endmodule
