// Logisim project final_MAIN.circ as structural Verilog: 8 circuits, main circuit MAIN
module FSM_2PHS (
  input  CLK,
  input  RST,
  input  REQ,
  input  DONE,
  output ACK,
  output GO
);

  wire and_1_out, and_2_out, and_3_out, and_4_out, and_5_out, and_6_out, and_7_out, and_8_out, and_9_out,
       and_10_out, and_11_out, and_12_out, or_1_out, or_2_out, or_3_out, or_4_out, or_5_out, or_6_out, Q1,
       Q2, Q3, Q4, Q5, Q6;

  and and_1 (and_1_out, REQ, Q1);
  and and_2 (and_2_out, ~DONE, Q2);  // AND_Gate
  and and_3 (and_3_out, ~DONE, Q3);  // AND_Gate
  and and_4 (and_4_out, ~REQ, Q4);  // AND_Gate
  and and_5 (and_5_out, ~DONE, Q5);  // AND_Gate
  and and_6 (and_6_out, ~DONE, Q6);  // AND_Gate
  and and_7 (and_7_out, ~REQ, Q1);  // AND_Gate
  and and_8 (and_8_out, DONE, Q6);
  or or_1 (or_1_out, and_1_out, and_9_out);
  and and_9 (and_9_out, DONE, Q2);
  or or_2 (or_2_out, and_2_out, and_3_out);
  and and_10 (and_10_out, DONE, Q3);
  and and_11 (and_11_out, REQ, Q4);
  or or_3 (or_3_out, and_4_out, and_12_out);
  and and_12 (and_12_out, DONE, Q5);
  or or_4 (or_4_out, and_5_out, and_6_out);
  D_Flip_Flop D1 (.D(or_5_out), .clk(CLK), .Q(Q1), .preset(RST));  // open: Qn, reset
  or or_5 (or_5_out, and_7_out, and_8_out);
  D_Flip_Flop D2 (.D(or_1_out), .clk(CLK), .Q(Q2), .reset(RST));  // open: Qn, preset
  D_Flip_Flop D3 (.D(or_2_out), .clk(CLK), .Q(Q3), .reset(RST));  // open: Qn, preset
  D_Flip_Flop D4 (.D(or_6_out), .clk(CLK), .Q(Q4), .reset(RST));  // open: Qn, preset
  or or_6 (or_6_out, and_10_out, and_11_out);
  D_Flip_Flop D5 (.D(or_3_out), .clk(CLK), .Q(Q5), .reset(RST));  // open: Qn, preset
  D_Flip_Flop D6 (.D(or_4_out), .clk(CLK), .Q(Q6), .reset(RST));  // open: Qn, preset
  or or_7 (ACK, Q4, Q5, Q6);
  or or_8 (GO, Q1, Q3, Q6, Q4);

  // Notes on the sheet:
  //   You Need to Edit This
  //   Two Phase Handshake FSM from Part 1
  //   Do not move/delete/add/rename pins
  //   States are represented with one-hot representation.
  //   The state assignment is detailed in my state table in my final.pdf
  //   Therefore, D1 corresponds with the 1st state,D2 corresponds with the 2nd state, etc.
endmodule

module TB_FSM_2PHS (
  input  REQ,
  input  [31:0] X,
  output [31:0] out_3,
  output [31:0] X_SQUARE
);

  wire CLK_out, DUT_ack, DUT_go, poweron_reset_random_1_p2, rnddlymul_1_p5, sysclk_out;

  Clock sysclk (.out(sysclk_out));
  Clock CLK (.out(CLK_out));
  // poweron_reset_random poweron_reset_random_1: pin names not known; wires that end beside it: sysclk_out, poweron_reset_random_1_p2
  LED REQis1 (.in(REQ));
  LED ACKis1 (.in(DUT_ack));
  FSM_2PHS DUT (
    .CLK(CLK_out), .RST(poweron_reset_random_1_p2), .REQ(REQ), .DONE(rnddlymul_1_p5), .ACK(DUT_ack),
    .GO(DUT_go));
  // RndDlyMul rnddlymul_1: pin names not known; wires that end beside it: CLK_out, DUT_go, X, X, rnddlymul_1_p5, X_SQUARE, out_3

  // Notes on the sheet:
  //   Simple testbench for manual testing of FSM_2PHS
  //   Feel free to edit it for your needs.
endmodule

module FSM_SQROOT (
  input  CLK,
  input  RST,
  input  GO,
  input  STATUS,
  output DONE,
  output COMMAND
);


  assign COMMAND = GO;
  assign DONE = STATUS;

  // Notes on the sheet:
  //   You Need to Edit This
  //   Controller for Part 2
  //   Modify Status and Command signals for Datapath
  //   If you don't need controller, just feed GO to COMMAND, and STATUS to DONE
endmodule

module DP_SQROOT (
  input  CLK,
  input  RST,
  input  COMMAND,
  input  [15:0] DIN,
  output STATUS,
  output [7:0] DOUT
);

  wire ABSCOND, and_1_out, and_2_out, and_3_out, and_4_out, and_5_out, and_6_out, comparator_1_eq,
       comparator_1_gt, comparator_1_lt, comparator_2_eq, comparator_2_gt, COND, d_ff_1_q, EQUALS, GO1CLK,
       GO_q, LESSTHAN, multiplexer_4_out, multiplexer_12_out, not_1_out, not_2_out, not_3_out, not_4_out,
       not_5_out, not_6_out, or_2_out, or_4_out, or_5_out, or_6_out, or_7_out;
  wire [7:0] adder_2_out, bit_extender_1_out, multiplexer_1_out, multiplexer_5_out, multiplexer_8_out,
       multiplexer_11_out, SQRT;
  wire [15:0] adder_1_out, FLOOR, MID, multiplexer_2_out, multiplexer_3_out, multiplexer_6_out,
       multiplexer_7_out, multiplexer_9_out, multiplexer_10_out, ROOF, subtractor_1_out;

  Comparator #(.width(16), .mode("unsigned")) comparator_1 (
    .a(FLOOR), .b(ROOF), .gt(comparator_1_gt), .eq(comparator_1_eq), .lt(comparator_1_lt));
  or or_1 (COND, comparator_1_eq, comparator_1_lt);
  if1 if1_1 (.FLOOR(FLOOR), .ROOF(ROOF), .DIN(DIN), .MID(MID), .EQUALS(EQUALS), .LESSTHAN(LESSTHAN));
  Bit_Extender #(.in_width(16), .out_width(8), .\type ("zero")) bit_extender_1 (.in(MID), .out(bit_extender_1_out));
  and and_1 (and_1_out, ~EQUALS, LESSTHAN);  // AND_Gate
  or or_2 (or_2_out, and_1_out, and_2_out);
  and and_2 (and_2_out, ~LESSTHAN, EQUALS);  // AND_Gate
  Adder #(.width(16)) adder_1 (.a(MID), .b(16'h1), .out(adder_1_out));  // open: cin, cout
  and and_3 (and_3_out, ~EQUALS, LESSTHAN);  // AND_Gate
  Subtractor #(.width(16)) subtractor_1 (.a(MID), .b(16'h1), .out(subtractor_1_out));  // open: bin, bout
  and and_4 (and_4_out, ~EQUALS, ~LESSTHAN);  // AND_Gate
  Multiplexer #(.width(8), .enable("false")) multiplexer_1 (
    .in0(SQRT), .in1(bit_extender_1_out), .out(multiplexer_1_out), .sel(or_2_out));
  Multiplexer #(.width(16), .enable("false")) multiplexer_2 (
    .in0(FLOOR), .in1(adder_1_out), .out(multiplexer_2_out), .sel(and_3_out));
  Multiplexer #(.width(16), .enable("false")) multiplexer_3 (
    .in0(ROOF), .in1(subtractor_1_out), .out(multiplexer_3_out), .sel(and_4_out));
  abscond abscond_1 (.SQRT(SQRT), .DIN(DIN), .ABSCOND(ABSCOND));
  Multiplexer #(.enable("false")) multiplexer_4 (
    .in0(1'b0), .in1(comparator_1_gt), .out(multiplexer_4_out), .sel(GO1CLK));
  Multiplexer #(.width(8), .enable("false")) multiplexer_5 (
    .in0(multiplexer_1_out), .in1(SQRT), .out(multiplexer_5_out), .sel(STATUS));
  or or_3 (STATUS, multiplexer_4_out, d_ff_1_q);
  Multiplexer #(.width(16), .enable("false")) multiplexer_6 (
    .in0(multiplexer_2_out), .in1(FLOOR), .out(multiplexer_6_out), .sel(STATUS));
  Multiplexer #(.width(16), .enable("false")) multiplexer_7 (
    .in0(multiplexer_3_out), .in1(ROOF), .out(multiplexer_7_out), .sel(STATUS));
  Multiplexer #(.width(8), .enable("false")) multiplexer_8 (
    .in0(multiplexer_5_out), .in1({8{1'b0}}), .out(multiplexer_8_out), .sel(not_1_out));
  not not_1 (not_1_out, GO1CLK);
  Multiplexer #(.width(16), .enable("false")) multiplexer_9 (
    .in0(multiplexer_6_out), .in1({16{1'b0}}), .out(multiplexer_9_out), .sel(not_2_out));
  not not_2 (not_2_out, GO1CLK);
  Multiplexer #(.width(16), .enable("false")) multiplexer_10 (
    .in0(multiplexer_7_out), .in1(DIN), .out(multiplexer_10_out), .sel(not_3_out));
  not not_3 (not_3_out, GO1CLK);
  D_Flip_Flop d_ff_1 (.D(EQUALS), .clk(CLK), .Q(d_ff_1_q), .reset(RST));  // open: Qn, preset
  Register u_SQRT (.D(multiplexer_8_out), .clk(CLK), .Q(SQRT), .clr(or_4_out));  // open: en
  or or_4 (or_4_out, RST, not_4_out);
  Register #(.width(16)) u_FLOOR (.D(multiplexer_9_out), .clk(CLK), .Q(FLOOR), .clr(or_6_out));  // open: en
  Register #(.width(16)) u_ROOF (.D(multiplexer_10_out), .clk(CLK), .Q(ROOF), .clr(or_5_out));  // open: en
  or or_5 (or_5_out, RST, not_5_out);
  Adder adder_2 (.a(SQRT), .b(8'h1), .out(adder_2_out));  // open: cin, cout
  not not_4 (not_4_out, COMMAND);
  not not_5 (not_5_out, COMMAND);
  Multiplexer #(.width(8), .enable("false")) multiplexer_11 (
    .in0(SQRT), .in1(adder_2_out), .out(multiplexer_11_out), .sel(and_5_out));
  and and_5 (and_5_out, ABSCOND, STATUS);
  or or_6 (or_6_out, RST, not_6_out);
  not not_6 (not_6_out, COMMAND);
  Comparator #(.mode("unsigned")) comparator_2 (
    .a(SQRT), .b({8{1'b1}}), .gt(comparator_2_gt), .eq(comparator_2_eq));  // open: lt
  Register #(.width(1)) GO (.D(multiplexer_12_out), .clk(CLK), .Q(GO_q), .clr(RST));  // open: en
  Multiplexer #(.enable("false")) multiplexer_12 (.in0(1'b0), .in1(1'b1), .out(multiplexer_12_out), .sel(COMMAND));
  or or_7 (or_7_out, comparator_2_gt, comparator_2_eq);
  Multiplexer #(.width(8), .enable("false")) multiplexer_13 (
    .in0(multiplexer_11_out), .in1({8{1'b1}}), .out(DOUT), .sel(and_6_out));
  and and_6 (and_6_out, or_7_out, STATUS);
  Comparator #(.width(1), .mode("unsigned")) comparator_3 (.a(GO_q), .b(1'b1), .eq(GO1CLK));  // open: gt, lt

  // Other names for the same wires on the sheet: DONE = STATUS; FINALSQRT[7:0] = DOUT; GO = COMMAND

  // Notes on the sheet:
  //   if condition:
  //   Implementing Binary Search:
  //   while condition:
  //   You Need to Edit This
  //   Datapath for Part 2
  //   Modify Status and Command signals for Controller
  //   If you don't have a controller then COMMAND is GO, and STATUS is DONE
  //   accounting for rounding and absolute value:
  //   keeps track of GO's prev and current state:
endmodule

module MAIN (
  input  CLK,
  input  RST,
  input  REQ,
  input  [15:0] DIN,
  output ACK,
  output [7:0] DOUT
);

  wire dp_sqroot_1_status, fsm_2phs_1_go, fsm_sqroot_1_command, fsm_sqroot_1_done;

  FSM_2PHS fsm_2phs_1 (.CLK(CLK), .RST(RST), .REQ(REQ), .DONE(fsm_sqroot_1_done), .ACK(ACK), .GO(fsm_2phs_1_go));
  FSM_SQROOT fsm_sqroot_1 (
    .CLK(CLK), .RST(RST), .GO(fsm_2phs_1_go), .STATUS(dp_sqroot_1_status), .DONE(fsm_sqroot_1_done),
    .COMMAND(fsm_sqroot_1_command));
  DP_SQROOT dp_sqroot_1 (
    .CLK(CLK), .RST(RST), .COMMAND(fsm_sqroot_1_command), .DIN(DIN), .STATUS(dp_sqroot_1_status), .DOUT(DOUT));

  // Notes on the sheet:
  //   No Need to Edit This
endmodule

module TB_MAIN (
  input  REQ,
  input  [15:0] DIN,
  output [7:0] DOUT
);

  wire CLK_out, DUT_ack, poweron_reset_random_1_p2;

  Clock sysclk ();  // open: out
  Clock CLK (.out(CLK_out));
  // poweron_reset_random poweron_reset_random_1: pin names not known; wires that end beside it: CLK_out, poweron_reset_random_1_p2
  LED REQis1 (.in(REQ));
  LED ACKis1 (.in(DUT_ack));
  MAIN DUT (.CLK(CLK_out), .RST(poweron_reset_random_1_p2), .REQ(REQ), .DIN(DIN), .ACK(DUT_ack), .DOUT(DOUT));

  // Notes on the sheet:
  //   X
  //   Testbench for manual testing of MAIN system
  //   Feel free to edit it for your needs.
  //   sqrt(X)
endmodule

module if1 (
  input  [15:0] FLOOR,
  input  [15:0] ROOF,
  input  [15:0] DIN,
  output [15:0] MID,
  output EQUALS,
  output LESSTHAN
);

  wire [15:0] adder_1_out;
  wire [29:0] bit_extender_1_out, bit_extender_2_out, MIDSQUARED;

  Adder #(.width(16)) adder_1 (.a(FLOOR), .b(ROOF), .out(adder_1_out));  // open: cin, cout
  Divider #(.width(16)) divider_1 (.a(adder_1_out), .b(16'h2), .out(MID));  // open: upper, rem
  assign bit_extender_1_out = {{14{DIN[15]}}, DIN};  // Bit_Extender bit_extender_1
  assign bit_extender_2_out = {{14{1'b0}}, MID};  // Bit_Extender bit_extender_2
  Comparator #(.width(30)) comparator_1 (
    .a(MIDSQUARED), .b(bit_extender_1_out), .eq(EQUALS), .lt(LESSTHAN));  // open: gt
  Multiplier #(.width(30)) multiplier_1 (
    .a(bit_extender_2_out), .b(bit_extender_2_out), .out(MIDSQUARED));  // open: cin, cout

  // Notes on the sheet:
  //   mid = (floor + roof)/2
  //   to create 2-bit condition for if statement mux:
  //   (mid * mid)
endmodule

module abscond (
  input  [7:0] SQRT,
  input  [15:0] DIN,
  output ABSCOND
);

  wire [7:0] adder_1_out, multiplier_1_out;
  wire [15:0] bit_extender_1_out, bit_extender_2_out, multiplier_2_out, subtractor_1_out, subtractor_2_out;

  Adder adder_1 (.a(SQRT), .b(8'h1), .out(adder_1_out));  // open: cin, cout
  Multiplier multiplier_1 (.a(SQRT), .b(SQRT), .out(multiplier_1_out));  // open: cin, cout
  assign bit_extender_1_out = {{8{1'b0}}, adder_1_out};  // Bit_Extender bit_extender_1
  assign bit_extender_2_out = {{8{1'b0}}, multiplier_1_out};  // Bit_Extender bit_extender_2
  Multiplier #(.width(16)) multiplier_2 (
    .a(bit_extender_1_out), .b(bit_extender_1_out), .out(multiplier_2_out));  // open: cin, cout
  Subtractor #(.width(16)) subtractor_1 (.a(multiplier_2_out), .b(DIN), .out(subtractor_1_out));  // open: bin, bout
  Subtractor #(.width(16)) subtractor_2 (.a(DIN), .b(bit_extender_2_out), .out(subtractor_2_out));  // open: bin, bout
  Comparator #(.width(16), .mode("unsigned")) comparator_1 (
    .a(subtractor_1_out), .b(subtractor_2_out), .lt(ABSCOND));  // open: gt, eq

  // Notes on the sheet:
  //   upper = sqrt+1
endmodule
