// Logisim project final_part1_tb.circ as structural Verilog: 1 circuit, main circuit TB
module TB (
  output halt,
  output [15:0] CYCLE,
  output RST,
  output REQ,
  output ACK,
  output GO,
  output DONE,
  output [4:0] CNTREQ,
  output [4:0] CNTACK,
  output ASSERTIONS
);

  wire CLK_out, counter_1_carry, counter_3_carry, genpulseatnegedge_1_pulse, genpulseatnegedge_2_pulse,
       genpulseatnegedge_3_pulse, genpulseatnegedge_4_pulse, not_1_out, not_2_out, or_1_out, or_2_out,
       sysclk_out;
  wire [4:0] subtractor_1_out;

  Clock sysclk (.out(sysclk_out));
  Clock CLK (.out(CLK_out));
  Counter #(.width(16), .max('hffff)) counter_1 (
    .clk(CLK_out), .carry(counter_1_carry), .Q(CYCLE));  // open: clr, load, up, count, D
  not not_1 (not_1_out, ACK);
  // poweron_reset_random poweron_reset_random_1: pin names not known; wires that end beside it: sysclk_out, CLK_out, RST
  GenPulseAtNegEdge genpulseatnegedge_1 (.CLK(CLK_out), .X(ACK), .PULSE(genpulseatnegedge_1_pulse));
  GenPulseAtNegEdge genpulseatnegedge_2 (.CLK(CLK_out), .X(not_1_out), .PULSE(genpulseatnegedge_2_pulse));
  or or_1 (or_1_out, genpulseatnegedge_1_pulse, genpulseatnegedge_2_pulse);
  not not_2 (not_2_out, REQ);
  FSM_2PHS DUT (.CLK(CLK_out), .RST(RST), .REQ(REQ), .DONE(DONE), .ACK(ACK), .GO(GO));
  // RandomTimer randomtimer_1: pin names not known; wires that end beside it: CLK_out, GO, DONE
  Counter #(.width(5), .max('h1f)) counter_2 (
    .clr(RST), .count(or_2_out), .clk(CLK_out), .Q(CNTREQ));  // open: load, up, D, carry
  RndDlyHSClient rnddlyhsclient_1 (.CLK(CLK_out), .RST(RST), .ACK(ACK), .REQ(REQ));
  GenPulseAtNegEdge genpulseatnegedge_3 (.CLK(CLK_out), .X(REQ), .PULSE(genpulseatnegedge_3_pulse));
  GenPulseAtNegEdge genpulseatnegedge_4 (.CLK(CLK_out), .X(not_2_out), .PULSE(genpulseatnegedge_4_pulse));
  Counter #(.width(5), .max('h1f)) counter_3 (
    .clr(RST), .count(or_1_out), .clk(CLK_out), .carry(counter_3_carry), .Q(CNTACK));  // open: load, up, D
  LED led_1 (.in(RST));
  LED led_2 (.in(REQ));
  LED led_3 (.in(ACK));
  LED led_4 (.in(GO));
  LED led_5 (.in(DONE));
  or or_2 (or_2_out, genpulseatnegedge_3_pulse, genpulseatnegedge_4_pulse);
  or or_3 (halt, counter_1_carry, counter_3_carry);
  Subtractor #(.width(5)) subtractor_1 (.a(CNTREQ), .b(CNTACK), .out(subtractor_1_out));  // open: bin, bout
  Comparator #(.width(5)) comparator_1 (.a(subtractor_1_out), .b(5'b00010), .lt(ASSERTIONS));  // open: gt, eq

  // Notes on the sheet:
  //   Edge@Ack
  //   Edge@Req
endmodule
