// Logisim project final_task1_tester.circ as structural Verilog: 3 circuits, main circuit Tester
module Tester (
  output halt,
  output [15:0] CYCLE,
  output RST,
  output GO1,
  output GO2,
  output GO3,
  output DONE,
  output [15:0] DIN1,
  output [15:0] DIN2,
  output [15:0] DIN3,
  output [15:0] DOUT,
  output [15:0] CNTRST,
  output [15:0] CNTGO1,
  output [15:0] CNTGO2,
  output [15:0] CNTGO3,
  output [15:0] CNTDONE
);

  wire CLK_out, comparator_1_eq, comparator_2_eq, comparator_3_eq, counter_2_carry, counter_3_carry,
       counter_4_carry, genpulseatnegedge_1_pulse, not_1_out, not_2_out, not_3_out, not_4_out, not_5_out,
       not_6_out, not_7_out, not_8_out, not_9_out, or_1_out;
  wire [3:0] multiplexer_1_out, multiplexer_2_out, multiplexer_3_out, random_1_out, random_2_out,
       random_3_out;
  wire [15:0] random_4_out, random_5_out, random_6_out;

  Clock sysclk ();  // open: out
  Clock CLK (.out(CLK_out));
  Counter #(.max('hffff), .width(16)) counter_1 (
    .clk(CLK_out), .carry(halt), .Q(CYCLE));  // open: clr, load, up, count, D
  Random #(.seed(10), .width(4)) random_1 (.next(not_1_out), .clk(CLK_out), .out(random_1_out));  // open: clr
  Random #(.seed(100), .width(4)) random_2 (.next(not_1_out), .clk(CLK_out), .out(random_2_out));  // open: clr
  Random #(.seed(1000), .width(4)) random_3 (.next(not_1_out), .clk(CLK_out), .out(random_3_out));  // open: clr
  not not_1 (not_1_out, RST);
  SysRunner sysrunner_1 (.CLK(CLK_out), .RUNMIN(13'h40), .RUNMAX(13'h100), .RSTMIN(13'h1), .RSTMAX(13'h8), .RST(RST));
  Multiplexer #(.width(4)) multiplexer_1 (
    .in0(random_1_out), .in1(4'b1110), .out(multiplexer_1_out), .sel(comparator_1_eq));
  Comparator #(.width(4)) comparator_1 (.a(random_1_out), .b(4'b1111), .eq(comparator_1_eq));  // open: gt, lt
  Multiplexer #(.width(4)) multiplexer_2 (
    .in0(random_2_out), .in1(4'b1110), .out(multiplexer_2_out), .sel(comparator_2_eq));
  Comparator #(.width(4)) comparator_2 (.a(random_2_out), .b(4'b1111), .eq(comparator_2_eq));  // open: gt, lt
  Multiplexer #(.width(4)) multiplexer_3 (
    .in0(random_3_out), .in1(4'b1110), .out(multiplexer_3_out), .sel(comparator_3_eq));
  Comparator #(.width(4)) comparator_3 (.a(random_3_out), .b(4'b1111), .eq(comparator_3_eq));  // open: gt, lt
  LED led_1 (.in(RST));
  Counter #(.max('hf), .ongoal("stay"), .width(4)) counter_2 (
    .load(or_1_out), .clk(CLK_out), .D(multiplexer_1_out), .carry(counter_2_carry));  // open: clr, up, count, Q
  Counter #(.max('hf), .ongoal("stay"), .width(4)) counter_3 (
    .load(or_1_out), .clk(CLK_out), .D(multiplexer_2_out), .carry(counter_3_carry));  // open: clr, up, count, Q
  Counter #(.max('hf), .ongoal("stay"), .width(4)) counter_4 (
    .load(or_1_out), .clk(CLK_out), .D(multiplexer_3_out), .carry(counter_4_carry));  // open: clr, up, count, Q
  not not_2 (not_2_out, DONE);
  not not_3 (not_3_out, counter_2_carry);
  not not_4 (not_4_out, counter_3_carry);
  not not_5 (not_5_out, counter_4_carry);
  Random #(.seed(4242), .width(16)) random_4 (
    .next(genpulseatnegedge_1_pulse), .clk(CLK_out), .out(random_4_out));  // open: clr
  GenPulseAtNegEdge genpulseatnegedge_1 (.CLK(CLK_out), .X(not_2_out), .PULSE(genpulseatnegedge_1_pulse));
  Random #(.seed(5151), .width(16)) random_5 (
    .next(genpulseatnegedge_1_pulse), .clk(CLK_out), .out(random_5_out));  // open: clr
  Random #(.seed(6363), .width(16)) random_6 (
    .next(genpulseatnegedge_1_pulse), .clk(CLK_out), .out(random_6_out));  // open: clr
  or or_1 (or_1_out, RST, genpulseatnegedge_1_pulse);
  LED led_2 (.in(RST));
  // DUT dut_1: pin names not known; wires that end beside it: DOUT, DONE
  GenPulseAtNegEdge genpulseatnegedge_2 (.CLK(CLK_out), .X(not_3_out), .PULSE(GO1));
  GenPulseAtNegEdge genpulseatnegedge_3 (.CLK(CLK_out), .X(not_4_out), .PULSE(GO2));
  GenPulseAtNegEdge genpulseatnegedge_4 (.CLK(CLK_out), .X(not_5_out), .PULSE(GO3));
  LED led_3 (.in(GO1));
  LED led_4 (.in(GO2));
  LED led_5 (.in(GO3));
  LED led_6 (.in(DONE));
  Multiplexer #(.width(16)) multiplexer_4 (.in0(16'haaaa), .in1(random_4_out), .out(DIN1), .sel(GO1));
  Multiplexer #(.width(16)) multiplexer_5 (.in0(16'h5555), .in1(random_5_out), .out(DIN2), .sel(GO2));
  Multiplexer #(.width(16)) multiplexer_6 (.in0(16'h2431), .in1(random_6_out), .out(DIN3), .sel(GO3));
  not not_6 (not_6_out, GO1);
  not not_7 (not_7_out, GO2);
  not not_8 (not_8_out, GO3);
  not not_9 (not_9_out, DONE);
  CountNegEdges16b countnegedges16b_1 (.CLK(CLK_out), .X(RST), .COUNT(CNTRST));
  CountNegEdges16b countnegedges16b_2 (.CLK(CLK_out), .X(not_6_out), .COUNT(CNTGO1));
  CountNegEdges16b countnegedges16b_3 (.CLK(CLK_out), .X(not_7_out), .COUNT(CNTGO2));
  CountNegEdges16b countnegedges16b_4 (.CLK(CLK_out), .X(not_8_out), .COUNT(CNTGO3));
  CountNegEdges16b countnegedges16b_5 (.CLK(CLK_out), .X(not_9_out), .COUNT(CNTDONE));
endmodule

module Median (
  input  [15:0] A,
  input  [15:0] B,
  input  [15:0] C,
  output [15:0] X
);

  wire and_1_out, and_2_out, and_3_out, and_4_out, comparator_1_gt, comparator_1_lt, comparator_2_gt,
       comparator_2_lt, comparator_3_gt, comparator_3_lt, or_1_out, or_2_out;
  wire [1:0] priority_encoder_1_out;

  Comparator #(.width(16)) comparator_1 (.a(A), .b(B), .gt(comparator_1_gt), .lt(comparator_1_lt));  // open: eq
  Comparator #(.width(16)) comparator_2 (.a(B), .b(C), .gt(comparator_2_gt), .lt(comparator_2_lt));  // open: eq
  Comparator #(.width(16)) comparator_3 (.a(A), .b(C), .gt(comparator_3_gt), .lt(comparator_3_lt));  // open: eq
  and and_1 (and_1_out, ~comparator_1_gt, ~comparator_2_gt);  // AND_Gate
  and and_2 (and_2_out, ~comparator_2_lt, ~comparator_1_lt);  // AND_Gate
  and and_3 (and_3_out, ~comparator_1_lt, ~comparator_3_gt);  // AND_Gate
  and and_4 (and_4_out, ~comparator_3_lt, ~comparator_1_gt);  // AND_Gate
  or or_1 (or_1_out, and_1_out, and_2_out);
  or or_2 (or_2_out, and_3_out, and_4_out);
  Priority_Encoder #(.select(2)) priority_encoder_1 (
    .in0(1'b1), .in1(1'b1), .in2(or_2_out), .in3(or_1_out), .out(priority_encoder_1_out));  // open: gs, en_out, en_in
  Multiplexer #(.select(2), .width(16)) multiplexer_1 (
    .in0(C), .in1(C), .in2(A), .in3(B), .out(X), .sel(priority_encoder_1_out));
endmodule

module CountNegEdges16b (
  input  CLK,
  input  X,
  output [15:0] COUNT
);

  wire genpulseatnegedge_1_pulse;

  GenPulseAtNegEdge genpulseatnegedge_1 (.CLK(CLK), .X(X), .PULSE(genpulseatnegedge_1_pulse));
  Counter #(.max('hffff), .width(16)) counter_1 (
    .count(genpulseatnegedge_1_pulse), .clk(CLK), .Q(COUNT));  // open: clr, load, up, D, carry
endmodule
