// Logisim project M16 Components.circ as structural Verilog: 16 circuits, main circuit SysRunner
module SysRunner (
  input  CLK,
  input  [12:0] RUNMIN,
  input  [12:0] RUNMAX,
  input  [12:0] RSTMIN,
  input  [12:0] RSTMAX,
  output RST
);

  wire and_1_out, and_2_out, and_3_out, and_4_out, and_5_out, d_ff_1_q, d_ff_2_q, d_ff_3_q, not_1_out,
       not_2_out, not_3_out, or_1_out, or_2_out, or_4_out, rndpor_1_rst, rndtimer13b_1_done,
       rndtimer13b_2_done;

  not not_1 (not_1_out, rndtimer13b_1_done);
  D_Flip_Flop d_ff_1 (.D(rndpor_1_rst), .clk(CLK), .Q(d_ff_1_q));  // open: Qn, preset, reset
  and and_1 (and_1_out, d_ff_3_q, rndtimer13b_2_done);
  or or_1 (or_1_out, and_1_out, and_2_out);
  and and_2 (and_2_out, d_ff_2_q, not_1_out);
  RndPOR rndpor_1 (.CLK(CLK), .RST(rndpor_1_rst));
  D_Flip_Flop d_ff_2 (.D(or_2_out), .clk(CLK), .Q(d_ff_2_q));  // open: Qn, preset, reset
  or or_2 (or_2_out, or_1_out, and_3_out);
  or or_3 (RST, rndpor_1_rst, d_ff_3_q);
  not not_2 (not_2_out, rndpor_1_rst);
  and and_3 (and_3_out, not_2_out, d_ff_1_q);
  // Probe on d_ff_2_q
  RndTimer13b rndtimer13b_1 (
    .CLK(CLK), .GO(d_ff_2_q), .MIN(RUNMIN), .MAX(RUNMAX), .DONE(rndtimer13b_1_done));  // open: RST
  // Probe on and_3_out
  not not_3 (not_3_out, rndtimer13b_2_done);
  and and_4 (and_4_out, d_ff_3_q, not_3_out);
  D_Flip_Flop d_ff_3 (.D(or_4_out), .clk(CLK), .Q(d_ff_3_q));  // open: Qn, preset, reset
  or or_4 (or_4_out, and_4_out, and_5_out);
  and and_5 (and_5_out, d_ff_2_q, rndtimer13b_1_done);
  RndTimer13b rndtimer13b_2 (
    .CLK(CLK), .GO(d_ff_3_q), .MIN(RSTMIN), .MAX(RSTMAX), .DONE(rndtimer13b_2_done));  // open: RST
  // Probe on d_ff_3_q
endmodule

module SysRunnerL (
  input  CLK,
  input  [15:0] RUNMIN,
  input  [15:0] RUNMAX,
  input  [12:0] RSTMIN,
  input  [12:0] RSTMAX,
  output RST
);

  wire and_1_out, and_2_out, and_3_out, and_4_out, and_5_out, d_ff_1_q, d_ff_2_q, d_ff_3_q, not_1_out,
       not_2_out, not_3_out, or_1_out, or_2_out, or_4_out, rndpor_1_rst, rndtimer13b_1_done,
       rndtimer16b_1_done;

  not not_1 (not_1_out, rndtimer16b_1_done);
  D_Flip_Flop d_ff_1 (.D(rndpor_1_rst), .clk(CLK), .Q(d_ff_1_q));  // open: Qn, preset, reset
  and and_1 (and_1_out, d_ff_3_q, rndtimer13b_1_done);
  or or_1 (or_1_out, and_1_out, and_2_out);
  and and_2 (and_2_out, d_ff_2_q, not_1_out);
  RndPOR rndpor_1 (.CLK(CLK), .RST(rndpor_1_rst));
  D_Flip_Flop d_ff_2 (.D(or_2_out), .clk(CLK), .Q(d_ff_2_q));  // open: Qn, preset, reset
  or or_2 (or_2_out, or_1_out, and_3_out);
  or or_3 (RST, rndpor_1_rst, d_ff_3_q);
  not not_2 (not_2_out, rndpor_1_rst);
  and and_3 (and_3_out, not_2_out, d_ff_1_q);
  // Probe on d_ff_2_q
  RndTimer16b rndtimer16b_1 (
    .CLK(CLK), .GO(d_ff_2_q), .MIN(RUNMIN), .MAX(RUNMAX), .DONE(rndtimer16b_1_done));  // open: RST
  // Probe on and_3_out
  not not_3 (not_3_out, rndtimer13b_1_done);
  and and_4 (and_4_out, d_ff_3_q, not_3_out);
  D_Flip_Flop d_ff_3 (.D(or_4_out), .clk(CLK), .Q(d_ff_3_q));  // open: Qn, preset, reset
  or or_4 (or_4_out, and_4_out, and_5_out);
  and and_5 (and_5_out, d_ff_2_q, rndtimer16b_1_done);
  RndTimer13b rndtimer13b_1 (
    .CLK(CLK), .GO(d_ff_3_q), .MIN(RSTMIN), .MAX(RSTMAX), .DONE(rndtimer13b_1_done));  // open: RST
  // Probe on d_ff_3_q
endmodule

module MyPOR (
  input  CLK,
  output RST
);

  wire d_ff_1_q, nor_1_out, not_1_out;

  not not_1 (not_1_out, nor_1_out);
  D_Flip_Flop d_ff_1 (.D(not_1_out), .clk(CLK), .Q(d_ff_1_q));  // open: Qn, preset, reset
  D_Flip_Flop d_ff_2 (.D(nor_1_out), .clk(CLK), .Q(RST));  // open: Qn, preset, reset
  nor nor_1 (nor_1_out, d_ff_1_q, RST);
  LED led_1 (.in(RST));

  // Notes on the sheet:
  //   Generates a 1 clock period long RST=1 at power up
endmodule

module RndPOR (
  input  CLK,
  output RST
);

  wire and_1_out, d_ff_1_q, not_1_out, RNGRST_out, t_ff_1_qn;

  Random #(.seed(1), .width(1)) RNGRST (.next(t_ff_1_qn), .clk(CLK), .out(RNGRST_out));  // open: clr
  T_Flip_Flop t_ff_1 (.T(and_1_out), .clk(CLK), .Qn(t_ff_1_qn));  // open: Q, reset, preset
  not not_1 (not_1_out, RNGRST_out);
  and and_1 (and_1_out, t_ff_1_qn, not_1_out, d_ff_1_q);
  D_Flip_Flop d_ff_1 (.D(RNGRST_out), .clk(CLK), .Q(d_ff_1_q));  // open: Qn, preset, reset
  and and_2 (RST, t_ff_1_qn, d_ff_1_q);
  TTY #(.cols(16), .rows(4)) tty_1 (.data({6'b011000, RST}), .clk(CLK));  // open: we, clr

  // Notes on the sheet:
  //   Generates a RST pulse of random length after a random wait upon power up
endmodule

module GenPulseAtNegEdge (
  input  CLK,
  input  X,
  output PULSE
);

  wire d_ff_1_q, not_1_out;

  not not_1 (not_1_out, X);
  D_Flip_Flop d_ff_1 (.D(X), .clk(CLK), .Q(d_ff_1_q));  // open: Qn, preset, reset
  and and_1 (PULSE, not_1_out, d_ff_1_q);
endmodule

module RndDlyHSClient (
  input  CLK,
  input  RST,
  input  ACK,
  output REQ
);

  wire d_ff_1_qn, decoder_1_out0, decoder_1_out2, decoder_1_out4, decoder_1_out5, decoder_1_out9,
       decoder_1_out11, decoder_1_out12, decoder_1_out13, multiplexer_1_out, or_1_out, xor_1_out;
  wire [2:1] counter_1_carry;
  wire [3:0] random_1_out;

  Clock sysclk ();  // open: out
  Decoder #(.select(4)) decoder_1 (
    .out0(decoder_1_out0), .out2(decoder_1_out2), .out4(decoder_1_out4), .out5(decoder_1_out5),
    .out9(decoder_1_out9), .out11(decoder_1_out11), .out12(decoder_1_out12), .out13(decoder_1_out13),
    .sel({REQ, counter_1_carry, ACK}));  // open: out1, out3, out6, out7, out8, out10, out14, out15, en
  Random #(.seed(10), .width(4)) random_1 (.clk(CLK), .out(random_1_out));  // open: clr, next
  D_Flip_Flop d_ff_1 (.D(or_1_out), .clk(CLK), .Q(counter_1_carry[2]), .Qn(d_ff_1_qn), .reset(RST));  // open: preset
  or or_1 (or_1_out, decoder_1_out0, decoder_1_out2, decoder_1_out4, decoder_1_out5, decoder_1_out9, decoder_1_out11, decoder_1_out12, decoder_1_out13);
  Counter #(.max('hf), .ongoal("stay"), .width(4)) counter_1 (
    .load(d_ff_1_qn), .up(1'b1), .clk(CLK), .D(random_1_out), .carry(counter_1_carry[1]));  // open: clr, count, Q
  Multiplexer multiplexer_1 (.in0(REQ), .in1(xor_1_out), .out(multiplexer_1_out), .sel(counter_1_carry[1]));
  xor xor_1 (xor_1_out, REQ, counter_1_carry[2]);
  D_Flip_Flop d_ff_2 (.D(multiplexer_1_out), .clk(CLK), .Q(REQ), .reset(RST));  // open: Qn, preset

  // Notes on the sheet:
  //   Initial: REQ=0, ACK=0
  //   1. Wait for random time
  //   2. Set REQ=1
  //   3. Wait for ACK==1
  //   4. Wait for random time
  //   5. Set REQ = 0
  //   6. Wait for ACK==0
  //   7. Go to Step 1
  //   This module implements the client side of the REQ-ACK Handshake.
endmodule

module RndDlyHSServer (
  input  CLK,
  input  RST,
  input  REQ,
  output ACK
);

  wire not_1_out;

  not not_1 (not_1_out, REQ);
  RndDlyHSClient rnddlyhsclient_1 (.CLK(CLK), .RST(RST), .ACK(not_1_out), .REQ(ACK));
endmodule

module OperandSequencer256x16 (
  input  CLK,
  input  RST,
  input  NXT,
  output DONE,
  output [7:0] i,
  output [15:0] D
);

  Counter #(.ongoal("stay")) counter_1 (
    .load(RST), .count(NXT), .clk(CLK), .D({8{1'b0}}), .carry(DONE), .Q(i));  // open: clr, up
  ROM #(.dataWidth(16)) rom_1 (.addr(i), .data(D));

  // Notes on the sheet:
  //   i = iteration number; D = i-th operand in ROM; DONE indicated end
  //   contents of rom_1 (hex, n*v repeats v):
  //   16*8000 16*ffff 16*0 16*1 16*7fff 16*2 16*3 16*4 16*9 16*64 16*fffe 16*fffd 16*fffc 16*fff7 16*ff9c
  //   16*f0ff
  //   Iterates through data in the ROM, moving to new value on every clock tick that NXT=1
endmodule

module MulOrDivU16b (
  input  SelDiv,
  input  [15:0] A,
  input  [15:0] B,
  output [15:0] X,
  output [15:0] Y
);

  wire [15:0] divider_1_out, divider_1_rem, multiplier_1_cout, multiplier_1_out;

  Multiplier #(.width(16)) multiplier_1 (.a(A), .b(B), .out(multiplier_1_out), .cout(multiplier_1_cout));  // open: cin
  Divider #(.width(16)) divider_1 (.a(A), .b(B), .out(divider_1_out), .rem(divider_1_rem));  // open: upper
  Multiplexer #(.width(16)) multiplexer_1 (.in0(multiplier_1_out), .in1(divider_1_out), .out(X), .sel(SelDiv));
  Multiplexer #(.width(16)) multiplexer_2 (.in0(multiplier_1_cout), .in1(divider_1_rem), .out(Y), .sel(SelDiv));

  // Notes on the sheet:
  //   If SelDiv==0, performs unsigned multiplication with Y[15:0] & X[15:0] being upper & lower bits of A[15:0]*B[15:0]
  //   If SelDiv==1, performs unsigned division with X[15:0]=A[15:0]/B[15:0] and Y[15:0]=A[15:0]%Y[15:0]
  //   If SelDiv==1 and B[15:0] then no division is performed, i.e. divisor is assumed to be 1
endmodule

module RndTimer5b (
  input  CLK,
  input  GO,
  input  RST,
  input  [4:0] MIN,
  input  [4:0] MAX,
  output DONE
);

  wire and_1_out, comparator_1_lt, comparator_2_gt, d_ff_1_qn, not_1_out;
  wire [4:0] multiplexer_1_out, multiplexer_2_out, random_1_out, subtractor_1_out;

  Random #(.seed(10), .width(5)) random_1 (.next(and_1_out), .clk(CLK), .out(random_1_out));  // open: clr
  D_Flip_Flop d_ff_1 (.D(GO), .clk(CLK), .Qn(d_ff_1_qn), .reset(RST));  // open: Q, preset
  not not_1 (not_1_out, GO);
  and and_1 (and_1_out, d_ff_1_qn, GO);
  Multiplexer #(.width(5)) multiplexer_1 (
    .in0(random_1_out), .in1(MIN), .out(multiplexer_1_out), .sel(comparator_1_lt));
  Comparator #(.mode("unsigned"), .width(5)) comparator_1 (
    .a(random_1_out), .b(MIN), .lt(comparator_1_lt));  // open: gt, eq
  Multiplexer #(.width(5)) multiplexer_2 (
    .in0(multiplexer_1_out), .in1(MAX), .out(multiplexer_2_out), .sel(comparator_2_gt));
  Comparator #(.mode("unsigned"), .width(5)) comparator_2 (
    .a(multiplexer_1_out), .b(MAX), .gt(comparator_2_gt));  // open: eq, lt
  Counter #(.max('h1f), .ongoal("stay"), .width(5)) counter_1 (
    .clr(RST), .load(not_1_out), .clk(CLK), .D(subtractor_1_out), .carry(DONE));  // open: up, count, Q
  Subtractor #(.width(5)) subtractor_1 (
    .a({5{1'b1}}), .b(multiplexer_2_out), .out(subtractor_1_out));  // open: bin, bout
  LED led_1 (.in(DONE));

  // Notes on the sheet:
  //   Makes DONE=1 a random # of clock ticks (>MIN, <MAX, MIN<=MAX, MIN>=1, MAX<=31) after GO==1; DONE=0 as soon as GO=1
endmodule

module RndTimer13b (
  input  CLK,
  input  GO,
  input  RST,
  input  [12:0] MIN,
  input  [12:0] MAX,
  output DONE
);

  wire and_1_out, comparator_1_lt, comparator_2_gt, d_ff_1_qn, not_1_out;
  wire [12:0] multiplexer_1_out, multiplexer_2_out, random_1_out, subtractor_1_out;

  Random #(.seed(1000), .width(13)) random_1 (.next(and_1_out), .clk(CLK), .out(random_1_out));  // open: clr
  D_Flip_Flop d_ff_1 (.D(GO), .clk(CLK), .Qn(d_ff_1_qn), .reset(RST));  // open: Q, preset
  not not_1 (not_1_out, GO);
  and and_1 (and_1_out, d_ff_1_qn, GO);
  Multiplexer #(.width(13)) multiplexer_1 (
    .in0(random_1_out), .in1(MIN), .out(multiplexer_1_out), .sel(comparator_1_lt));
  Comparator #(.mode("unsigned"), .width(13)) comparator_1 (
    .a(random_1_out), .b(MIN), .lt(comparator_1_lt));  // open: gt, eq
  Multiplexer #(.width(13)) multiplexer_2 (
    .in0(multiplexer_1_out), .in1(MAX), .out(multiplexer_2_out), .sel(comparator_2_gt));
  Comparator #(.mode("unsigned"), .width(13)) comparator_2 (
    .a(multiplexer_1_out), .b(MAX), .gt(comparator_2_gt));  // open: eq, lt
  Subtractor #(.width(13)) subtractor_1 (
    .a({13{1'b1}}), .b(multiplexer_2_out), .out(subtractor_1_out));  // open: bin, bout
  Counter #(.max('h1fff), .ongoal("stay"), .width(13)) counter_1 (
    .clr(RST), .load(not_1_out), .clk(CLK), .D(subtractor_1_out), .carry(DONE));  // open: up, count, Q
  LED led_1 (.in(DONE));

  // Notes on the sheet:
  //   Makes DONE=1 a random # of clock ticks (>MIN, <MAX, MIN<=MAX, MIN>=1, MAX<=8191) after GO==1; DONE=0 as soon as GO=1
endmodule

module RndTimer16b (
  input  CLK,
  input  GO,
  input  RST,
  input  [15:0] MIN,
  input  [15:0] MAX,
  output DONE
);

  wire and_1_out, comparator_1_lt, comparator_2_gt, d_ff_1_qn, not_1_out;
  wire [15:0] multiplexer_1_out, multiplexer_2_out, random_1_out, subtractor_1_out;

  Random #(.seed(1000), .width(16)) random_1 (.next(and_1_out), .clk(CLK), .out(random_1_out));  // open: clr
  D_Flip_Flop d_ff_1 (.D(GO), .clk(CLK), .Qn(d_ff_1_qn), .reset(RST));  // open: Q, preset
  not not_1 (not_1_out, GO);
  and and_1 (and_1_out, d_ff_1_qn, GO);
  Multiplexer #(.width(16)) multiplexer_1 (
    .in0(random_1_out), .in1(MIN), .out(multiplexer_1_out), .sel(comparator_1_lt));
  Comparator #(.mode("unsigned"), .width(16)) comparator_1 (
    .a(random_1_out), .b(MIN), .lt(comparator_1_lt));  // open: gt, eq
  Multiplexer #(.width(16)) multiplexer_2 (
    .in0(multiplexer_1_out), .in1(MAX), .out(multiplexer_2_out), .sel(comparator_2_gt));
  Comparator #(.mode("unsigned"), .width(16)) comparator_2 (
    .a(multiplexer_1_out), .b(MAX), .gt(comparator_2_gt));  // open: eq, lt
  Subtractor #(.width(16)) subtractor_1 (
    .a({16{1'b1}}), .b(multiplexer_2_out), .out(subtractor_1_out));  // open: bin, bout
  Counter #(.max('hffff), .ongoal("stay"), .width(16)) counter_1 (
    .clr(RST), .load(not_1_out), .clk(CLK), .D(subtractor_1_out), .carry(DONE));  // open: up, count, Q
  LED led_1 (.in(DONE));

  // Notes on the sheet:
  //   Makes DONE=1 a random # of clock ticks (>MIN, <MAX, MIN<=MAX, MIN>=1, MAX<=65535) after GO==1; DONE=0 as soon as GO=1
endmodule

module RndDlyAdd32b (
  input  CLK,
  input  GO,
  input  RST,
  input  [31:0] A,
  input  [31:0] B,
  output DONE,
  output [31:0] DOUT
);

  wire [31:0] adder_1_out, multiplexer_1_out, multiplexer_2_out, register_1_q;

  Multiplexer #(.width(32)) multiplexer_1 (.in0({32{1'b0}}), .in1(A), .out(multiplexer_1_out), .sel(GO));
  Multiplexer #(.width(32)) multiplexer_2 (.in0({32{1'b0}}), .in1(B), .out(multiplexer_2_out), .sel(GO));
  Adder #(.width(32)) adder_1 (.a(multiplexer_1_out), .b(multiplexer_2_out), .out(adder_1_out));  // open: cin, cout
  Register #(.width(32)) register_1 (.D(adder_1_out), .en(1'b1), .clk(CLK), .Q(register_1_q), .clr(RST));
  RndTimer5b rndtimer5b_1 (.CLK(CLK), .GO(GO), .RST(RST), .MIN(5'b00001), .MAX(5'b11110), .DONE(DONE));
  Multiplexer #(.width(32)) multiplexer_3 (.in0({32{1'b0}}), .in1(register_1_q), .out(DOUT), .sel(DONE));

  // Notes on the sheet:
  //   Adder that take random # of clock cycles to compute
endmodule

module RndDlyMul32b (
  input  CLK,
  input  GO,
  input  RST,
  input  [31:0] A,
  input  [31:0] B,
  output DONE,
  output [31:0] AxBLo,
  output [31:0] AxBHi
);

  wire [31:0] multiplexer_1_out, multiplexer_2_out, multiplier_1_cout, multiplier_1_out, register_1_q;

  Multiplexer #(.width(32)) multiplexer_1 (.in0({32{1'b0}}), .in1(A), .out(multiplexer_1_out), .sel(RST));
  Multiplexer #(.width(32)) multiplexer_2 (.in0({32{1'b0}}), .in1(B), .out(multiplexer_2_out), .sel(RST));
  Multiplier #(.width(32)) multiplier_1 (
    .a(multiplexer_1_out), .b(multiplexer_2_out), .out(multiplier_1_out), .cout(multiplier_1_cout));  // open: cin
  Register #(.width(32)) register_1 (.D(multiplier_1_out), .en(1'b1), .clk(CLK), .Q(register_1_q), .clr(RST));
  RndTimer5b rndtimer5b_1 (.CLK(CLK), .GO(GO), .RST(RST), .MIN(5'b00001), .MAX(5'b11110), .DONE(DONE));
  Multiplexer #(.width(32)) multiplexer_3 (.in0({32{1'b0}}), .in1(register_1_q), .out(AxBLo), .sel(DONE));
  Multiplexer #(.width(32)) multiplexer_4 (.in0({32{1'b0}}), .in1(multiplier_1_cout), .out(AxBHi), .sel(DONE));

  // Notes on the sheet:
  //   Multiplier that take random # of clock cycles to compute
endmodule

module RndDlyNot8 (
  input  CLK,
  input  GO,
  input  RST,
  input  [7:0] X,
  output DONE,
  output [7:0] F
);

  wire and_1_out, d_ff_1_qn;
  wire [7:0] not_1_out, register_1_q;

  D_Flip_Flop d_ff_1 (.D(GO), .clk(CLK), .Qn(d_ff_1_qn), .reset(RST));  // open: Q, preset
  Register register_1 (.D(X), .en(and_1_out), .clk(CLK), .Q(register_1_q), .clr(RST));
  and and_1 (and_1_out, GO, d_ff_1_qn);
  RndTimer5b rndtimer5b_1 (.CLK(CLK), .GO(GO), .RST(RST), .MIN(5'b00001), .MAX(5'b11110), .DONE(DONE));
  Multiplexer #(.width(8)) multiplexer_1 (.in0({8{1'b0}}), .in1(not_1_out), .out(F), .sel(DONE));
  assign not_1_out = ~register_1_q;  // NOT_Gate not_1, 8 bits wide

  // Notes on the sheet:
  //   1's Complement that take random # of clock cycles to compute
endmodule

module PulseCounter16b (
  input  CLK,
  input  RST,
  input  PULSE,
  output REACHEDMAX,
  output [15:0] COUNT
);

  Counter #(.max('hffff), .width(16)) counter_1 (
    .clr(RST), .count(PULSE), .clk(CLK), .carry(REACHEDMAX), .Q(COUNT));  // open: load, up, D
endmodule
