// Logisim project final_alt_task1_tester.circ as structural Verilog: 3 circuits, main circuit Tester
module Tester (
  output halt,
  output [17:0] CYCLE,
  output RST,
  output REQ,
  output ACK,
  output [7:0] X1,
  output [7:0] Y1,
  output [7:0] X2,
  output [7:0] Y2,
  output [11:0] DIST,
  output [15:0] CNTRST,
  output [15:0] CNTREQ,
  output [15:0] CNTACK,
  output ASSERTIONS
);

  wire and_1_out, and_2_out, CLK_out, counter_1_carry, counter_2_carry, countnegedges16b_1_reachedmax,
       EdgeACK, FEdgeACK, FEdgeREQ, GT2RST, not_1_out, not_2_out, not_3_out, NXTOP, OLDNXTOP, or_4_out,
       pulsecounter16b_2_reachedmax, REdgeACK, REdgeREQ, REdgeRST;
  wire [3:0] counter_2_q;
  wire [15:0] subtractor_1_out;
  wire [31:0] DINb, EdgeCases_data, multiplexer_2_out, random_1_out, random_2_out, register_1_q;

  Clock sysclk ();  // open: out
  Clock CLK (.out(CLK_out));
  Counter #(.max('h3ffff), .width(18)) counter_1 (
    .clk(CLK_out), .carry(counter_1_carry), .Q(CYCLE));  // open: clr, load, up, count, D
  not not_1 (not_1_out, ACK);
  Random #(.seed(100), .width(32)) random_1 (.clk(CLK_out), .out(random_1_out));  // open: clr, next
  Counter #(.max('he), .ongoal("stay"), .width(4)) counter_2 (
    .count(NXTOP), .clk(CLK_out), .carry(counter_2_carry), .Q(counter_2_q));  // open: clr, load, up, D
  Register #(.width(32)) register_1 (.D(random_1_out), .en(NXTOP), .clk(CLK_out), .Q(register_1_q));  // open: clr
  or or_1 (OLDNXTOP, EdgeACK, and_1_out);
  and and_1 (and_1_out, REdgeRST, GT2RST);
  and and_2 (and_2_out, REdgeRST, GT2RST);
  GenPulseAtNegEdge genpulseatnegedge_1 (.CLK(CLK_out), .X(ACK), .PULSE(FEdgeACK));
  GenPulseAtNegEdge genpulseatnegedge_2 (.CLK(CLK_out), .X(not_1_out), .PULSE(REdgeACK));
  Multiplexer #(.width(32)) multiplexer_1 (.in0(register_1_q), .in1(32'hffff7f7f), .out(DINb), .sel(1'b0));
  ROM #(.addrWidth(4), .dataWidth(32)) EdgeCases (.addr(counter_2_q), .data(EdgeCases_data));
  or or_2 (NXTOP, FEdgeREQ, and_2_out);
  SysRunnerL sysrunnerl_1 (
    .CLK(CLK_out), .RUNMIN(16'h2000), .RUNMAX(16'hfffe), .RSTMIN(13'h1), .RSTMAX(13'h8), .RST(RST));
  or or_3 (EdgeACK, FEdgeACK, REdgeACK);
  not not_2 (not_2_out, RST);
  not not_3 (not_3_out, REQ);
  CountNegEdges16b countnegedges16b_1 (
    .CLK(CLK_out), .X(RST), .REACHEDMAX(countnegedges16b_1_reachedmax), .COUNT(CNTRST));
  GenPulseAtNegEdge genpulseatnegedge_3 (.CLK(CLK_out), .X(not_2_out), .PULSE(REdgeRST));
  DUT dut_1 (.X1(X1), .Y1(Y1), .X2(X2), .Y2(Y2), .REQ(REQ), .CLK(CLK_out), .RST(RST), .DIST(DIST), .ACK(ACK));
  Random #(.seed(43), .width(32)) random_2 (.next(REdgeACK), .clk(CLK_out), .out(random_2_out));  // open: clr
  RndDlyHSClient rnddlyhsclient_1 (.CLK(CLK_out), .RST(RST), .ACK(ACK), .REQ(REQ));
  GenPulseAtNegEdge genpulseatnegedge_4 (.CLK(CLK_out), .X(REQ), .PULSE(FEdgeREQ));
  GenPulseAtNegEdge genpulseatnegedge_5 (.CLK(CLK_out), .X(not_3_out), .PULSE(REdgeREQ));
  Comparator #(.mode("unsigned"), .width(16)) comparator_1 (.a(CNTRST), .b({16{1'b0}}), .gt(GT2RST));  // open: eq, lt
  // Probe on multiplexer_2_out
  Multiplexer #(.width(32)) multiplexer_2 (
    .in0(EdgeCases_data), .in1(DINb), .out(multiplexer_2_out), .sel(counter_2_carry));
  LED led_1 (.in(RST));
  LED led_2 (.in(REQ));
  LED led_3 (.in(ACK));
  or or_4 (or_4_out, FEdgeREQ, REdgeREQ);
  Multiplexer #(.width(32)) multiplexer_3 (
    .in0(random_2_out), .in1(multiplexer_2_out), .out({Y2, X2, Y1, X1}), .sel(REQ));
  PulseCounter16b pulsecounter16b_1 (.CLK(CLK_out), .PULSE(or_4_out), .COUNT(CNTREQ));  // open: RST, REACHEDMAX
  PulseCounter16b pulsecounter16b_2 (
    .CLK(CLK_out), .PULSE(EdgeACK), .REACHEDMAX(pulsecounter16b_2_reachedmax), .COUNT(CNTACK));  // open: RST
  or or_5 (halt, counter_1_carry, countnegedges16b_1_reachedmax, pulsecounter16b_2_reachedmax);
  Subtractor #(.width(16)) subtractor_1 (.a(CNTREQ), .b(CNTACK), .out(subtractor_1_out));  // open: bin, bout
  Comparator #(.width(16)) comparator_2 (.a(subtractor_1_out), .b(16'h2), .lt(ASSERTIONS));  // open: gt, eq

  // Other names for the same wires on the sheet: DIN[31:0] = {Y2, X2, Y1, X1}

  // Notes on the sheet:
  //   contents of EdgeCases (hex, n*v repeats v):
  //   0 ffffffff fffff 7f7f 7fff7fff 7f7fffff ff7f7fff 7f7f0000 7fff0000 3f3f8080 3f3f00 808000 7f7f7f7f
  //   fedcba 456789 dcba98
  //   Edge@Ack
  //   Change to 1 to use constant DIN
  //   Edge@Req
endmodule

module CountNegEdges16b (
  input  CLK,
  input  X,
  output REACHEDMAX,
  output [15:0] COUNT
);

  wire genpulseatnegedge_1_pulse;

  GenPulseAtNegEdge genpulseatnegedge_1 (.CLK(CLK), .X(X), .PULSE(genpulseatnegedge_1_pulse));
  Counter #(.max('hffff), .width(16)) counter_1 (
    .count(genpulseatnegedge_1_pulse), .clk(CLK), .carry(REACHEDMAX), .Q(COUNT));  // open: clr, load, up, D
endmodule

module Tester_OLD (
  output halt,
  output [17:0] CYCLE,
  output RST,
  output GO1,
  output GO2,
  output DONE,
  output [7:0] X1,
  output [7:0] Y1,
  output [7:0] X2,
  output [7:0] Y2,
  output [11:0] DIST,
  output [15:0] CNTRST,
  output [15:0] CNTGO1,
  output [15:0] CNTGO2,
  output [15:0] CNTDONE
);

  wire CLK_out, comparator_1_eq, comparator_2_eq, counter_2_carry, counter_3_carry,
       genpulseatnegedge_1_pulse, not_1_out, not_2_out, not_3_out, not_4_out, not_5_out, not_6_out,
       not_7_out, or_1_out;
  wire [3:0] multiplexer_1_out, multiplexer_2_out, random_1_out, random_2_out;
  wire [15:0] random_3_out, random_4_out;

  Clock sysclk ();  // open: out
  Clock CLK (.out(CLK_out));
  Counter #(.max('h3ffff), .width(18)) counter_1 (
    .clk(CLK_out), .carry(halt), .Q(CYCLE));  // open: clr, load, up, count, D
  Random #(.seed(10), .width(4)) random_1 (.next(not_1_out), .clk(CLK_out), .out(random_1_out));  // open: clr
  Random #(.seed(100), .width(4)) random_2 (.next(not_1_out), .clk(CLK_out), .out(random_2_out));  // open: clr
  not not_1 (not_1_out, RST);
  Multiplexer #(.width(4)) multiplexer_1 (
    .in0(random_1_out), .in1(4'b1110), .out(multiplexer_1_out), .sel(comparator_1_eq));
  Comparator #(.width(4)) comparator_1 (.a(random_1_out), .b(4'b1111), .eq(comparator_1_eq));  // open: gt, lt
  Multiplexer #(.width(4)) multiplexer_2 (
    .in0(random_2_out), .in1(4'b1110), .out(multiplexer_2_out), .sel(comparator_2_eq));
  Comparator #(.width(4)) comparator_2 (.a(random_2_out), .b(4'b1111), .eq(comparator_2_eq));  // open: gt, lt
  SysRunnerL sysrunnerl_1 (
    .CLK(CLK_out), .RUNMIN(16'h2000), .RUNMAX(16'hfffe), .RSTMIN(13'h1), .RSTMAX(13'h8), .RST(RST));
  LED led_1 (.in(RST));
  Counter #(.max('hf), .ongoal("stay"), .width(4)) counter_2 (
    .load(or_1_out), .clk(CLK_out), .D(multiplexer_1_out), .carry(counter_2_carry));  // open: clr, up, count, Q
  Counter #(.max('hf), .ongoal("stay"), .width(4)) counter_3 (
    .load(or_1_out), .clk(CLK_out), .D(multiplexer_2_out), .carry(counter_3_carry));  // open: clr, up, count, Q
  not not_2 (not_2_out, DONE);
  not not_3 (not_3_out, counter_2_carry);
  not not_4 (not_4_out, counter_3_carry);
  Random #(.seed(4242), .width(16)) random_3 (
    .next(genpulseatnegedge_1_pulse), .clk(CLK_out), .out(random_3_out));  // open: clr
  GenPulseAtNegEdge genpulseatnegedge_1 (.CLK(CLK_out), .X(not_2_out), .PULSE(genpulseatnegedge_1_pulse));
  Random #(.seed(5151), .width(16)) random_4 (
    .next(genpulseatnegedge_1_pulse), .clk(CLK_out), .out(random_4_out));  // open: clr
  or or_1 (or_1_out, RST, genpulseatnegedge_1_pulse);
  LED led_2 (.in(RST));
  // DUT dut_1: pin names not known; wires that end beside it: X1, Y1, X2, Y2, GO1, GO2, CLK_out, RST, DIST, DONE
  GenPulseAtNegEdge genpulseatnegedge_2 (.CLK(CLK_out), .X(not_3_out), .PULSE(GO1));
  GenPulseAtNegEdge genpulseatnegedge_3 (.CLK(CLK_out), .X(not_4_out), .PULSE(GO2));
  LED led_3 (.in(GO1));
  LED led_4 (.in(GO2));
  LED led_5 (.in(DONE));
  Multiplexer #(.width(16)) multiplexer_3 (.in0(16'habcd), .in1(random_3_out), .out({Y1, X1}), .sel(GO1));
  Multiplexer #(.width(16)) multiplexer_4 (.in0(16'h2431), .in1(random_4_out), .out({Y2, X2}), .sel(GO2));
  not not_5 (not_5_out, GO1);
  not not_6 (not_6_out, GO2);
  not not_7 (not_7_out, DONE);
  CountNegEdges16b countnegedges16b_1 (.CLK(CLK_out), .X(RST), .COUNT(CNTRST));  // open: REACHEDMAX
  CountNegEdges16b countnegedges16b_2 (.CLK(CLK_out), .X(not_5_out), .COUNT(CNTGO1));  // open: REACHEDMAX
  CountNegEdges16b countnegedges16b_3 (.CLK(CLK_out), .X(not_6_out), .COUNT(CNTGO2));  // open: REACHEDMAX
  CountNegEdges16b countnegedges16b_4 (.CLK(CLK_out), .X(not_7_out), .COUNT(CNTDONE));  // open: REACHEDMAX
endmodule
