// Logisim project da1_task1_tb.circ as structural Verilog: 1 circuit, main circuit Tester
module Tester (
  output [6:0] A_IN,
  output [31:0] X3_OUT_REF,
  output [31:0] X2_OUT_REF,
  output [31:0] X1_OUT_REF,
  output [31:0] X0_OUT_REF,
  output [31:0] X3_OUT_DUT,
  output [31:0] X2_OUT_DUT,
  output [31:0] X1_OUT_DUT,
  output [31:0] X0_OUT_DUT,
  output MATCH,
  output halt
);

  wire clock_1_out, comparator_1_eq, comparator_2_eq, comparator_3_eq, comparator_4_eq;

  Counter #(.width(7), .max('h7f)) counter_1 (
    .clk(clock_1_out), .carry(halt), .Q(A_IN));  // open: clr, load, up, count, D
  Clock clock_1 (.out(clock_1_out));
  REF ref_1 (.A(A_IN), .X3(X3_OUT_REF), .X2(X2_OUT_REF), .X1(X1_OUT_REF), .X0(X0_OUT_REF));
  // DUT dut_1: pin names not known; wires that end beside it: A_IN, X3_OUT_DUT, X2_OUT_DUT, X1_OUT_DUT, X0_OUT_DUT
  Comparator #(.width(32), .mode("unsigned")) comparator_1 (
    .a(X3_OUT_DUT), .b(X3_OUT_REF), .eq(comparator_1_eq));  // open: gt, lt
  Comparator #(.width(32), .mode("unsigned")) comparator_2 (
    .a(X2_OUT_DUT), .b(X2_OUT_REF), .eq(comparator_2_eq));  // open: gt, lt
  Comparator #(.width(32), .mode("unsigned")) comparator_3 (
    .a(X1_OUT_DUT), .b(X1_OUT_REF), .eq(comparator_3_eq));  // open: gt, lt
  Comparator #(.width(32), .mode("unsigned")) comparator_4 (
    .a(X0_OUT_DUT), .b(X0_OUT_REF), .eq(comparator_4_eq));  // open: gt, lt
  and and_1 (MATCH, comparator_1_eq, comparator_2_eq, comparator_3_eq, comparator_4_eq);

  // Notes on the sheet:
  //   period=2
endmodule
