// Logisim project da1_task2.circ as structural Verilog: 2 circuits, main circuit DUT
module DUT (
  input  [3:0] A,
  input  [3:0] B,
  input  [3:0] C,
  output [3:0] MEDIAN
);


  // Notes on the sheet:
  //   Please put your deisgn below. You may also use subcircuits.
  //   However, do not move or rename any pins.
endmodule

module TB (
  input  [3:0] A,
  input  [3:0] B,
  input  [3:0] C,
  output [3:0] MEDIAN
);

  DUT dut_1 (.A(A), .B(B), .C(C), .MEDIAN(MEDIAN));

  // Notes on the sheet:
  //   DO NOT MODIFY THIS
  //   TEST YOUR CIRCUITS USING THIS TO MAKE SURE YOU HAVE NOT ALTERED PIN OUT
endmodule
