// Logisim project da1_task2_ref.circ as structural Verilog: 1 circuit, main circuit REF
module REF (
  input  [3:0] A,
  input  [3:0] B,
  input  [3:0] C,
  output [3:0] MEDIAN
);

  wire [2:0] comparator_3_gt;

  Comparator #(.width(4), .mode("unsigned")) comparator_1 (.a(A), .b(B), .gt(comparator_3_gt[2]));  // open: eq, lt
  Comparator #(.width(4), .mode("unsigned")) comparator_2 (.a(B), .b(C), .gt(comparator_3_gt[1]));  // open: eq, lt
  Comparator #(.width(4), .mode("unsigned")) comparator_3 (.a(C), .b(A), .gt(comparator_3_gt[0]));  // open: eq, lt
  Multiplexer #(.select(3), .width(4), .enable("false")) multiplexer_1 (
    .in0(B), .in1(B), .in2(A), .in3(C), .in4(C), .in5(A), .in6(B), .in7(4'b0000), .out(MEDIAN),
    .sel(comparator_3_gt));

  // Notes on the sheet:
  //   A>B
  //   B>C
  //   C>A
endmodule
