// Logisim project da1_task2_tb.circ as structural Verilog: 1 circuit, main circuit Tester
module Tester (
  output [3:0] A_IN,
  output [3:0] B_IN,
  output [3:0] C_IN,
  output [3:0] MEDIAN_OUT_REF,
  output [3:0] MEDIAN_OUT_DUT,
  output MATCH,
  output halt
);

  wire clock_1_out, undriven;

  Counter #(.width(12), .max('hfff)) counter_1 (
    .count(undriven), .clk(clock_1_out), .carry(halt), .Q({C_IN, B_IN, A_IN}));  // open: clr, load, up, D
  Clock clock_1 (.out(clock_1_out));
  REF ref_1 (.A(A_IN), .B(B_IN), .C(C_IN), .MEDIAN(MEDIAN_OUT_REF));
  DUT dut_1 (.A(A_IN), .B(B_IN), .C(C_IN), .MEDIAN(MEDIAN_OUT_DUT));
  Comparator #(.width(4), .mode("unsigned")) comparator_1 (
    .a(MEDIAN_OUT_REF), .b(MEDIAN_OUT_DUT), .eq(MATCH));  // open: gt, lt

  // Notes on the sheet:
  //   period=2
endmodule
