// Logisim project da1_task3.circ as structural Verilog: 2 circuits, main circuit DUT
module DUT (
  input  [5:0] CODON,
  output [4:0] AA
);


  // Notes on the sheet:
  //   Please put your deisgn below. You may also use subcircuits.
  //   However, do not move or rename any pins.
endmodule

module TB (
  input  [5:0] CODON,
  output [4:0] AA
);

  DUT dut_1 (.CODON(CODON), .AA(AA));

  // Notes on the sheet:
  //   DO NOT MODIFY THIS
  //   TEST YOUR CIRCUITS USING THIS TO MAKE SURE YOU HAVE NOT ALTERED PIN OUT
endmodule
