// Logisim project da1_task3_ref.circ as structural Verilog: 1 circuit, main circuit REF
module REF (
  input  [5:0] CODON,
  output [4:0] AA
);

  wire and_2_out, and_3_out, and_4_out, and_5_out, and_6_out, and_7_out, and_8_out, and_9_out, and_10_out,
       and_11_out, and_12_out, and_13_out, and_14_out, and_15_out, and_16_out, and_17_out, and_18_out,
       and_19_out, and_20_out, and_21_out, and_22_out, and_23_out, and_24_out, not_1_out, not_2_out,
       not_3_out, not_4_out, not_5_out, not_6_out, not_7_out, not_8_out, not_9_out, not_10_out, not_11_out,
       not_12_out, not_13_out, not_14_out, not_15_out, not_16_out, not_17_out, not_18_out, not_19_out,
       not_20_out, not_21_out, not_22_out, not_23_out, not_24_out, not_25_out, not_26_out, not_27_out,
       not_28_out, not_29_out, not_30_out, not_31_out, not_32_out, not_33_out, not_34_out, not_35_out,
       not_36_out, not_37_out, not_38_out, not_39_out;

  not not_1 (not_1_out, CODON[5]);
  not not_2 (not_2_out, CODON[4]);
  not not_3 (not_3_out, CODON[2]);
  not not_4 (not_4_out, CODON[0]);
  not not_5 (not_5_out, CODON[4]);
  not not_6 (not_6_out, CODON[2]);
  not not_7 (not_7_out, CODON[2]);
  not not_8 (not_8_out, CODON[5]);
  not not_9 (not_9_out, CODON[2]);
  not not_10 (not_10_out, CODON[0]);
  not not_11 (not_11_out, CODON[4]);
  not not_12 (not_12_out, CODON[1]);
  not not_13 (not_13_out, CODON[0]);
  not not_14 (not_14_out, CODON[5]);
  not not_15 (not_15_out, CODON[2]);
  not not_16 (not_16_out, CODON[3]);
  not not_17 (not_17_out, CODON[2]);
  not not_18 (not_18_out, CODON[1]);
  not not_19 (not_19_out, CODON[0]);
  not not_20 (not_20_out, CODON[4]);
  not not_21 (not_21_out, CODON[3]);
  not not_22 (not_22_out, CODON[4]);
  not not_23 (not_23_out, CODON[3]);
  not not_24 (not_24_out, CODON[5]);
  not not_25 (not_25_out, CODON[2]);
  not not_26 (not_26_out, CODON[3]);
  not not_27 (not_27_out, CODON[0]);
  and and_1 (AA[4], not_1_out, not_2_out);
  and and_2 (and_2_out, CODON[5], not_3_out, not_4_out);
  and and_3 (and_3_out, CODON[5], not_5_out, CODON[2]);
  and and_4 (and_4_out, CODON[5], CODON[3], not_6_out);
  and and_5 (and_5_out, CODON[5], CODON[4], not_7_out);
  not not_28 (not_28_out, CODON[5]);
  not not_29 (not_29_out, CODON[3]);
  and and_6 (and_6_out, not_28_out, not_29_out, not_30_out);
  not not_30 (not_30_out, CODON[2]);
  and and_7 (and_7_out, not_8_out, CODON[4], not_9_out, not_10_out);
  and and_8 (and_8_out, CODON[5], not_11_out, CODON[2], not_12_out, not_13_out);
  not not_31 (not_31_out, CODON[4]);
  and and_9 (and_9_out, CODON[5], not_31_out, CODON[3]);
  and and_10 (and_10_out, CODON[5], CODON[3], CODON[2]);
  not not_32 (not_32_out, CODON[4]);
  and and_11 (and_11_out, not_32_out, CODON[3], not_33_out);
  not not_33 (not_33_out, CODON[2]);
  and and_12 (and_12_out, not_14_out, CODON[3], not_15_out, CODON[0]);
  and and_13 (and_13_out, CODON[4], not_16_out, not_17_out, not_18_out, not_19_out);
  and and_14 (and_14_out, CODON[4], CODON[3], CODON[2]);
  not not_34 (not_34_out, CODON[3]);
  and and_15 (and_15_out, CODON[5], not_34_out, not_35_out);
  not not_35 (not_35_out, CODON[2]);
  and and_16 (and_16_out, CODON[5], not_20_out, not_21_out, CODON[0]);
  and and_17 (and_17_out, CODON[5], not_22_out, not_23_out, CODON[1]);
  not not_36 (not_36_out, CODON[4]);
  and and_18 (and_18_out, not_36_out, CODON[3], not_37_out);
  not not_37 (not_37_out, CODON[0]);
  not not_38 (not_38_out, CODON[4]);
  and and_19 (and_19_out, not_38_out, CODON[3], CODON[2]);
  and and_20 (and_20_out, not_24_out, CODON[4], not_25_out, CODON[0]);
  and and_21 (and_21_out, CODON[4], not_26_out, CODON[2], not_27_out);
  and and_22 (and_22_out, CODON[5], CODON[2], CODON[0]);
  and and_23 (and_23_out, CODON[5], CODON[2], CODON[1]);
  and and_24 (and_24_out, CODON[5], CODON[3], not_39_out);
  not not_39 (not_39_out, CODON[0]);
  or or_1 (AA[3], and_2_out, and_3_out, and_4_out, and_5_out);
  or or_2 (AA[2], and_6_out, and_7_out, and_8_out, and_9_out, and_10_out);
  or or_3 (AA[1], and_11_out, and_12_out, and_13_out, and_14_out, and_15_out, and_16_out, and_17_out);
  or or_4 (AA[0], and_18_out, and_19_out, and_20_out, and_21_out, and_22_out, and_23_out, and_24_out);

  // Notes on the sheet:
  //   AA4
  //   AA3
  //   AA2
  //   AA1
  //   AA0
endmodule
