// Logisim project da1_task3_tb.circ as structural Verilog: 1 circuit, main circuit Tester
module Tester (
  output [5:0] CODON_IN,
  output [4:0] AA_OUT_REF,
  output [4:0] AA_OUT_DUT,
  output MATCH,
  output halt
);

  wire clock_1_out;

  Clock clock_1 (.out(clock_1_out));
  Counter #(.width(6), .max('h3f)) counter_1 (
    .clk(clock_1_out), .carry(halt), .Q(CODON_IN));  // open: clr, load, up, count, D
  REF ref_1 (.CODON(CODON_IN), .AA(AA_OUT_REF));
  DUT dut_1 (.CODON(CODON_IN), .AA(AA_OUT_DUT));
  Comparator #(.width(5), .mode("unsigned")) comparator_1 (.a(AA_OUT_DUT), .b(AA_OUT_REF), .eq(MATCH));  // open: gt, lt
endmodule
