// Logisim project da1_task4.circ as structural Verilog: 2 circuits, main circuit DUT
module DUT (
  input  [4:0] P,
  input  [4:0] K,
  output [4:0] C
);


  // Notes on the sheet:
  //   Please put your deisgn below. You may also use subcircuits.
  //   However, do not move or rename any pins.
endmodule

module TB (
  input  [4:0] P,
  input  [4:0] K,
  output [4:0] C
);

  DUT dut_1 (.P(P), .K(K), .C(C));

  // Notes on the sheet:
  //   DO NOT MODIFY THIS
  //   TEST YOUR CIRCUITS USING THIS TO MAKE SURE YOU HAVE NOT ALTERED PIN OUT
endmodule
