// Logisim project da1_task5.circ as structural Verilog: 2 circuits, main circuit DUT
module DUT (
  input  [3:0] D1,
  input  [3:0] D0,
  output [6:0] Z
);


  // Notes on the sheet:
  //   Please put your deisgn below. You may also use subcircuits.
  //   However, do not move or rename any pins.
endmodule

module TB (
  input  [3:0] D1,
  input  [3:0] D0,
  output [6:0] Z
);

  DUT dut_1 (.D1(D1), .D0(D0), .Z(Z));

  // Notes on the sheet:
  //   DO NOT MODIFY THIS
  //   TEST YOUR CIRCUITS USING THIS TO MAKE SURE YOU HAVE NOT ALTERED PIN OUT
endmodule
