// Logisim project da2_task1_tb.circ as structural Verilog: 2 circuits, main circuit main
module main (
  output halt,
  output [7:0] CYCLE,
  output RST,
  output DIN,
  output DOUT
);

  wire CLK_out;

  Clock sysclk ();  // open: out
  Clock CLK (.out(CLK_out));
  Counter counter_1 (.clk(CLK_out), .carry(halt), .Q(CYCLE));  // open: clr, load, up, count, D
  Random #(.width(1), .seed(10)) RNGDIN (.clk(CLK_out), .out(DIN));  // open: clr, next
  poweron_reset_random poweron_reset_random_1 (.CLK(CLK_out), .RST(RST));
  DUT dut_1 (.DIN(DIN), .CLK(CLK_out), .RST(RST), .DOUT(DOUT));
endmodule

module poweron_reset_random (
  input  CLK,
  output RST
);

  wire and_1_out, clock_1_out, d_ff_1_q, not_1_out, RNGRST_out, t_ff_1_qn;

  Clock clock_1 (.out(clock_1_out));
  Random #(.width(1), .seed(20)) RNGRST (.next(t_ff_1_qn), .clk(clock_1_out), .out(RNGRST_out));  // open: clr
  T_Flip_Flop t_ff_1 (.T(and_1_out), .clk(clock_1_out), .Qn(t_ff_1_qn));  // open: Q, reset, preset
  and and_1 (and_1_out, t_ff_1_qn, not_1_out, d_ff_1_q);
  not not_1 (not_1_out, RNGRST_out);
  D_Flip_Flop d_ff_1 (.D(RNGRST_out), .clk(clock_1_out), .Q(d_ff_1_q));  // open: Qn, preset, reset
  and and_2 (RST, t_ff_1_qn, d_ff_1_q);
  TTY #(.rows(4), .cols(16)) tty_1 (.data({6'b011000, RST}), .clk(clock_1_out));  // open: we, clr
endmodule
