// Logisim project da2_task2.circ as structural Verilog: 3 circuits, main circuit DUT
module DUT (
  input  DIN,
  input  CLK,
  input  RST,
  output DOUT_SHORT,
  output DOUT_LONG
);

  wire nor_1_out, nor_2_out, not_1_out, not_2_out, or_1_out, Press1_q, Press2_q, Press3_q, Press4_q,
       Press5_q, Press6_q, Press7_q, Reset_States_q;

  D_Flip_Flop Press1 (.D(DIN), .clk(CLK), .Q(Press1_q), .reset(or_1_out));  // open: Qn, preset
  not not_1 (not_1_out, DIN);
  D_Flip_Flop Press2 (.D(Press1_q), .clk(CLK), .Q(Press2_q), .reset(or_1_out));  // open: Qn, preset
  D_Flip_Flop Reset_States (.D(not_1_out), .clk(CLK), .Q(Reset_States_q));  // open: Qn, preset, reset
  D_Flip_Flop Press3 (.D(Press2_q), .clk(CLK), .Q(Press3_q), .reset(or_1_out));  // open: Qn, preset
  D_Flip_Flop Press4 (.D(Press3_q), .clk(CLK), .Q(Press4_q), .reset(or_1_out));  // open: Qn, preset
  or or_1 (or_1_out, Reset_States_q, RST);
  D_Flip_Flop Press5 (.D(Press4_q), .clk(CLK), .Q(Press5_q), .reset(or_1_out));  // open: Qn, preset
  D_Flip_Flop Press6 (.D(Press5_q), .clk(CLK), .Q(Press6_q), .reset(or_1_out));  // open: Qn, preset
  D_Flip_Flop Press7 (.D(Press6_q), .clk(CLK), .Q(Press7_q), .reset(or_1_out));  // open: Qn, preset
  not not_2 (not_2_out, Press7_q);
  nor nor_1 (nor_1_out, Press7_q, or_1_out, DIN);
  nor nor_2 (nor_2_out, not_2_out, or_1_out, DIN);
  D_Flip_Flop Short (.D(nor_1_out), .clk(CLK), .Q(DOUT_SHORT));  // open: Qn, preset, reset
  D_Flip_Flop Long (.D(nor_2_out), .clk(CLK), .Q(DOUT_LONG));  // open: Qn, preset, reset

  // Notes on the sheet:
  //   Please put your deisgn below. You may also use subcircuits.
  //   However, do not move, rename, add, or delete any pins.
  //   Put your design below and wire it up to the pins.
  //   Feel free to remove this text.
endmodule

module TB (
);

  wire BUTTON_1_out, clk_out, dut_1_dout_long, dut_1_dout_short, pwr_on_reset_1_rst, t_ff_1_q, t_ff_2_q;

  Clock sysclk ();  // open: out
  Button BUTTON_1 (.out(BUTTON_1_out));
  Clock #(.highDuration(2), .lowDuration(2)) clk (.out(clk_out));
  pwr_on_reset pwr_on_reset_1 (.CLK(clk_out), .RST(pwr_on_reset_1_rst));
  T_Flip_Flop t_ff_1 (.T(dut_1_dout_short), .clk(clk_out), .Q(t_ff_1_q));  // open: Qn, reset, preset
  DUT dut_1 (
    .DIN(BUTTON_1_out), .CLK(clk_out), .RST(pwr_on_reset_1_rst), .DOUT_SHORT(dut_1_dout_short),
    .DOUT_LONG(dut_1_dout_long));
  LED LED1 (.in(t_ff_1_q));
  T_Flip_Flop t_ff_2 (.T(dut_1_dout_long), .clk(clk_out), .Q(t_ff_2_q));  // open: Qn, reset, preset
  LED LED2 (.in(t_ff_2_q));

  // Notes on the sheet:
  //   DO NOT MODIFY THIS
  //   YOU MAY TEST YOUR CIRCUITS USING THIS TO MAKE SURE YOU HAVE NOT ALTERED PIN OUT
  //   LED1 and LED2 will toggle every clock tick that the corresponding output of test circuit is high.
endmodule

module pwr_on_reset (
  input  CLK,
  output RST
);

  wire d_ff_1_q, nor_1_out, not_1_out;

  not not_1 (not_1_out, nor_1_out);
  D_Flip_Flop d_ff_1 (.D(not_1_out), .clk(CLK), .Q(d_ff_1_q));  // open: Qn, preset, reset
  D_Flip_Flop d_ff_2 (.D(nor_1_out), .clk(CLK), .Q(RST));  // open: Qn, preset, reset
  nor nor_1 (nor_1_out, d_ff_1_q, RST);

  // Notes on the sheet:
  //   DO NOT MODIFY THIS
endmodule
