// Logisim project da2_task2_tb.circ as structural Verilog: 2 circuits, main circuit main
module main (
  output halt,
  output [7:0] CYCLE,
  output RST,
  output DIN,
  output DOUT_SHORT,
  output DOUT_LONG
);

  wire CLK_out, comparator_1_lt, comparator_2_gt, RNGDIN2_out;
  wire [4:0] bitadder_1_out;
  wire [15:0] RNGDIN1_out;

  Clock sysclk ();  // open: out
  Clock CLK (.out(CLK_out));
  Random #(.width(16), .seed(10)) RNGDIN1 (.clk(CLK_out), .out(RNGDIN1_out));  // open: clr, next
  Counter counter_1 (.clk(CLK_out), .carry(halt), .Q(CYCLE));  // open: clr, load, up, count, D
  Random #(.width(1), .seed(10)) RNGDIN2 (.clk(CLK_out), .out(RNGDIN2_out));  // open: clr, next
  BitAdder #(.width(16)) bitadder_1 (.in0(RNGDIN1_out), .out(bitadder_1_out));
  Comparator #(.width(5), .mode("unsigned")) comparator_1 (
    .a(bitadder_1_out), .b(5'b01010), .lt(comparator_1_lt));  // open: gt, eq
  poweron_reset_random poweron_reset_random_1 (.CLK(CLK_out), .RST(RST));
  Multiplexer #(.enable("false")) multiplexer_1 (
    .in0(RNGDIN2_out), .in1(comparator_1_lt), .out(DIN), .sel(comparator_2_gt));
  Comparator #(.mode("unsigned")) comparator_2 (.a(CYCLE), .b(8'h40), .gt(comparator_2_gt));  // open: eq, lt
  TTY #(.rows(4), .cols(10)) tty_1 (.data({6'b011000, DIN}), .clk(CLK_out));  // open: we, clr
  DUT dut_1 (.DIN(DIN), .CLK(CLK_out), .RST(RST), .DOUT_SHORT(DOUT_SHORT), .DOUT_LONG(DOUT_LONG));
endmodule

module poweron_reset_random (
  input  CLK,
  output RST
);

  wire and_1_out, clock_1_out, d_ff_1_q, not_1_out, RNGRST_out, t_ff_1_qn;

  Clock clock_1 (.out(clock_1_out));
  Random #(.width(1), .seed(20)) RNGRST (.next(t_ff_1_qn), .clk(clock_1_out), .out(RNGRST_out));  // open: clr
  T_Flip_Flop t_ff_1 (.T(and_1_out), .clk(clock_1_out), .Qn(t_ff_1_qn));  // open: Q, reset, preset
  and and_1 (and_1_out, t_ff_1_qn, not_1_out, d_ff_1_q);
  not not_1 (not_1_out, RNGRST_out);
  D_Flip_Flop d_ff_1 (.D(RNGRST_out), .clk(clock_1_out), .Q(d_ff_1_q));  // open: Qn, preset, reset
  and and_2 (RST, t_ff_1_qn, d_ff_1_q);
  TTY #(.rows(4), .cols(16)) tty_1 (.data({6'b011000, RST}), .clk(clock_1_out));  // open: we, clr
endmodule
