// Logisim project da2_task4.circ as structural Verilog: 16 circuits, main circuit DUT
module DUT (
  input  [6:0] DIN,
  input  RDY,
  input  CLK,
  input  RST,
  output F
);

  Detector detector_1 (.DIN(DIN), .RDY(RDY), .CLK(CLK), .RST(RST), .F(F));

  // Notes on the sheet:
  //   Please put your deisgn below. You may also use subcircuits.
  //   However, do not move, rename, add, or delete any pins.
  //   Put your design below and wire it up to the pins.
  //   Feel free to remove this text.
endmodule

module TB (
);

  wire clk_out, keyboard_1_avail, pwr_on_reset_1_rst;
  wire [0:0] dut_1_f;
  wire [6:0] keyboard_1_data;

  Keyboard keyboard_1 (.clk(clk_out), .avail(keyboard_1_avail), .data(keyboard_1_data));  // open: re, clr
  Clock #(.highDuration(2), .lowDuration(2)) clk (.out(clk_out));
  Clock sysclk ();  // open: out
  pwr_on_reset pwr_on_reset_1 (.CLK(clk_out), .RST(pwr_on_reset_1_rst));
  DUT dut_1 (.DIN(keyboard_1_data), .RDY(keyboard_1_avail), .CLK(clk_out), .RST(pwr_on_reset_1_rst), .F(dut_1_f[0]));
  TTY tty_1 (.data(keyboard_1_data), .clk(clk_out));  // open: we, clr
  TTY tty_2 (.data({6'b011000, dut_1_f[0]}), .clk(clk_out));  // open: we, clr

  // Notes on the sheet:
  //   DO NOT MODIFY THIS
  //   YOU MAY TEST YOUR CIRCUITS USING THIS TO MAKE SURE YOU HAVE NOT ALTERED PIN OUT
  //   Top display will show what was typed thus far
  //   Bottom display will show output F
endmodule

module pwr_on_reset (
  input  CLK,
  output RST
);

  wire d_ff_1_q, nor_1_out, not_1_out;

  not not_1 (not_1_out, nor_1_out);
  D_Flip_Flop d_ff_1 (.D(not_1_out), .clk(CLK), .Q(d_ff_1_q));  // open: Qn, preset, reset
  D_Flip_Flop d_ff_2 (.D(nor_1_out), .clk(CLK), .Q(RST));  // open: Qn, preset, reset
  nor nor_1 (nor_1_out, d_ff_1_q, RST);

  // Notes on the sheet:
  //   DO NOT MODIFY THIS
endmodule

module Detector (
  input  [6:0] DIN,
  input  RDY,
  input  CLK,
  input  RST,
  output F
);

  wire and_1_out, and_2_out, and_3_out, and_4_out, and_5_out, and_6_out, and_7_out, and_8_out, and_9_out,
       and_10_out, and_11_out, and_12_out, and_13_out, and_14_out, and_15_out, and_16_out, and_17_out,
       and_18_out, and_20_out, and_21_out, and_22_out, and_23_out, and_24_out, and_25_out, and_26_out,
       and_27_out, and_28_out, and_29_out, and_30_out, and_31_out, and_32_out, and_33_out, and_34_out,
       and_35_out, and_36_out, and_37_out, and_38_out, and_39_out, and_40_out, and_41_out, and_42_out, C,
       combined, compare_a_1_out_2, compare_a_2_out_2, compare_c_1_out_2, compare_d_1_out_2,
       compare_d_2_out_2, compare_i_1_out_2, compare_i_2_out_2, compare_i_3_out_2, compare_i_4_out_2,
       compare_n_1_out_2, compare_n_2_out_2, compare_o_1_out_2, compare_o_2_out_2, compare_o_3_out_2,
       compare_o_4_out_2, compare_r_1_out_2, compare_r_2_out_2, compare_r_3_out_2, compare_r_4_out_2,
       compare_r_5_out_2, compare_s_2_out_2, compare_u_1_out_2, compare_u_2_out_2, compare_v_1_out_2,
       compare_v_2_out_2, I, i2, N, notvc_1_out_2, notvc_2_out_2, notvc_3_out_2, notvc_4_out_2,
       notvc_5_out_2, notvc_6_out_2, notvc_7_out_2, notvc_8_out_2, notvc_9_out_2, notvc_10_out_2,
       notvc_11_out_2, notvc_12_out_2, notvc_13_out_2, O, O2, or_1_out, or_2_out, or_3_out, or_4_out,
       or_5_out, or_7_out, or_8_out, or_9_out, or_10_out, or_11_out, or_12_out, or_13_out, or_14_out,
       or_15_out, or_16_out, or_17_out, or_18_out, or_19_out, R, R2, START_q, starttrans, U, V, v2;

  compare_d compare_d_1 (.DIN(DIN), .out_2(compare_d_1_out_2));
  compare_r compare_r_1 (.DIN(DIN), .out_2(compare_r_1_out_2));
  notvc notvc_1 (.DIN(DIN), .out_2(notvc_1_out_2));
  compare_o compare_o_1 (.DIN(DIN), .out_2(compare_o_1_out_2));
  notvc notvc_2 (.DIN(DIN), .out_2(notvc_2_out_2));
  compare_r compare_r_2 (.DIN(DIN), .out_2(compare_r_2_out_2));
  notvc notvc_3 (.DIN(DIN), .out_2(notvc_3_out_2));
  compare_o compare_o_2 (.DIN(DIN), .out_2(compare_o_2_out_2));
  notvc notvc_4 (.DIN(DIN), .out_2(notvc_4_out_2));
  compare_n compare_n_1 (.DIN(DIN), .out_2(compare_n_1_out_2));
  notvc notvc_5 (.DIN(DIN), .out_2(notvc_5_out_2));
  compare_a compare_a_1 (.DIN(DIN), .out_2(compare_a_1_out_2));
  notvc notvc_6 (.DIN(DIN), .out_2(notvc_6_out_2));
  or or_1 (or_1_out, compare_d_1_out_2, compare_r_1_out_2);
  notvc notvc_7 (.DIN(DIN), .out_2(notvc_7_out_2));
  compare_i compare_i_1 (.DIN(DIN), .out_2(compare_i_1_out_2));
  notvc notvc_8 (.DIN(DIN), .out_2(notvc_8_out_2));
  compare_r compare_r_3 (.DIN(DIN), .out_2(compare_r_3_out_2));
  notvc notvc_9 (.DIN(DIN), .out_2(notvc_9_out_2));
  compare_u compare_u_1 (.DIN(DIN), .out_2(compare_u_1_out_2));
  notvc notvc_10 (.DIN(DIN), .out_2(notvc_10_out_2));
  compare_s compare_s_1 (.DIN(DIN));  // open: out_2
  notvc notvc_11 (.DIN(DIN), .out_2(notvc_11_out_2));
  compare_i compare_i_2 (.DIN(DIN), .out_2(compare_i_2_out_2));
  notvc notvc_12 (.DIN(DIN), .out_2(notvc_12_out_2));
  and and_1 (and_1_out, RDY, START_q, notvc_13_out_2);
  notvc notvc_13 (.DIN(DIN), .out_2(notvc_13_out_2));
  and and_2 (and_2_out, notvc_1_out_2, C, ~compare_o_1_out_2);  // AND_Gate
  and and_3 (and_3_out, notvc_2_out_2, O, ~compare_r_2_out_2);  // AND_Gate
  and and_4 (and_4_out, notvc_3_out_2, R, ~compare_o_2_out_2);  // AND_Gate
  and and_5 (and_5_out, notvc_4_out_2, O2, ~compare_n_1_out_2);  // AND_Gate
  and and_6 (and_6_out, notvc_5_out_2, N, ~compare_a_1_out_2);  // AND_Gate
  and and_7 (and_7_out, notvc_6_out_2, i2, ~or_1_out);  // AND_Gate
  and and_8 (and_8_out, notvc_7_out_2, V, ~compare_i_1_out_2);  // AND_Gate
  and and_9 (and_9_out, notvc_8_out_2, I, ~compare_r_3_out_2);  // AND_Gate
  and and_10 (and_10_out, notvc_9_out_2, R2, ~compare_u_1_out_2);  // AND_Gate
  and and_11 (and_11_out, notvc_10_out_2, U);  // AND_Gate
  and and_12 (and_12_out, notvc_11_out_2, v2, ~compare_i_2_out_2);  // AND_Gate
  and and_13 (and_13_out, notvc_12_out_2, F);
  or or_2 (or_2_out, START_q, F);
  or or_3 (or_3_out, and_1_out, starttrans);
  and and_14 (and_14_out, ~RDY, or_2_out);  // AND_Gate
  D_Flip_Flop START (.D(or_4_out), .clk(CLK), .Q(START_q), .preset(RST));  // open: Qn, reset
  or or_4 (or_4_out, and_14_out, or_3_out, RST);
  or or_5 (or_5_out, and_2_out, and_3_out, and_4_out, and_5_out, and_6_out, and_7_out, and_8_out, and_9_out, and_10_out, and_11_out, and_12_out, and_13_out);
  compare_c compare_c_1 (.DIN(DIN), .out_2(compare_c_1_out_2));
  and and_15 (and_15_out, RDY, compare_c_1_out_2, combined);
  or or_6 (combined, START_q, C, O, R, O2, N, v2, V, I, R2, U, i2, F);
  and and_16 (and_16_out, ~RDY, C);  // AND_Gate
  D_Flip_Flop u_C (.D(or_7_out), .clk(CLK), .Q(C), .reset(RST));  // open: Qn, preset
  or or_7 (or_7_out, and_16_out, and_15_out);
  and and_17 (and_17_out, RDY, compare_v_1_out_2, and_18_out);
  compare_v compare_v_1 (.DIN(DIN), .out_2(compare_v_1_out_2));
  and and_18 (and_18_out, combined, ~O);  // AND_Gate
  and and_19 (starttrans, RDY, or_5_out);
  compare_o compare_o_3 (.DIN(DIN), .out_2(compare_o_3_out_2));
  D_Flip_Flop u_V (.D(or_8_out), .clk(CLK), .Q(V), .reset(RST));  // open: Qn, preset
  and and_20 (and_20_out, ~RDY, V);  // AND_Gate
  or or_8 (or_8_out, and_20_out, and_17_out);
  and and_21 (and_21_out, ~RDY, O);  // AND_Gate
  and and_22 (and_22_out, RDY, C, compare_o_3_out_2);
  D_Flip_Flop u_O (.D(or_9_out), .clk(CLK), .Q(O), .reset(RST));  // open: Qn, preset
  or or_9 (or_9_out, and_21_out, and_22_out);
  compare_r compare_r_4 (.DIN(DIN), .out_2(compare_r_4_out_2));
  and and_23 (and_23_out, ~RDY, R);  // AND_Gate
  and and_24 (and_24_out, RDY, O, compare_r_4_out_2);
  and and_25 (and_25_out, ~RDY, I);  // AND_Gate
  and and_26 (and_26_out, RDY, V, compare_i_3_out_2);
  compare_i compare_i_3 (.DIN(DIN), .out_2(compare_i_3_out_2));
  D_Flip_Flop u_R (.D(or_10_out), .clk(CLK), .Q(R), .reset(RST));  // open: Qn, preset
  or or_10 (or_10_out, and_23_out, and_24_out);
  D_Flip_Flop u_I (.D(or_11_out), .clk(CLK), .Q(I), .reset(RST));  // open: Qn, preset
  or or_11 (or_11_out, and_25_out, and_26_out);
  or or_12 (or_12_out, i2, I);
  compare_v compare_v_2 (.DIN(DIN), .out_2(compare_v_2_out_2));
  and and_27 (and_27_out, ~RDY, v2);  // AND_Gate
  and and_28 (and_28_out, RDY, O, compare_v_2_out_2);
  compare_a compare_a_2 (.DIN(DIN), .out_2(compare_a_2_out_2));
  and and_29 (and_29_out, compare_a_2_out_2, N);
  compare_s compare_s_2 (.DIN(DIN), .out_2(compare_s_2_out_2));
  and and_30 (and_30_out, compare_s_2_out_2, U);
  compare_d compare_d_2 (.DIN(DIN), .out_2(compare_d_2_out_2));
  and and_31 (and_31_out, compare_d_2_out_2, i2);
  and and_32 (and_32_out, ~RDY, O2);  // AND_Gate
  and and_33 (and_33_out, RDY, R, compare_o_4_out_2);
  compare_o compare_o_4 (.DIN(DIN), .out_2(compare_o_4_out_2));
  and and_34 (and_34_out, ~RDY, R2);  // AND_Gate
  and and_35 (and_35_out, RDY, or_12_out, compare_r_5_out_2);
  compare_r compare_r_5 (.DIN(DIN), .out_2(compare_r_5_out_2));
  D_Flip_Flop u_v2 (.D(or_13_out), .clk(CLK), .Q(v2), .reset(RST));  // open: Qn, preset
  or or_13 (or_13_out, and_27_out, and_28_out);
  D_Flip_Flop u_O2 (.D(or_14_out), .clk(CLK), .Q(O2), .reset(RST));  // open: Qn, preset
  or or_14 (or_14_out, and_32_out, and_33_out);
  or or_15 (or_15_out, and_34_out, and_35_out);
  or or_16 (or_16_out, and_29_out, and_30_out, and_31_out);
  D_Flip_Flop u_R2 (.D(or_15_out), .clk(CLK), .Q(R2), .reset(RST));  // open: Qn, preset
  and and_36 (and_36_out, RDY, or_16_out);
  D_Flip_Flop MATCH (.D(and_36_out), .clk(CLK), .Q(F), .reset(RST));  // open: Qn, preset
  compare_n compare_n_2 (.DIN(DIN), .out_2(compare_n_2_out_2));
  compare_u compare_u_2 (.DIN(DIN), .out_2(compare_u_2_out_2));
  and and_37 (and_37_out, ~RDY, i2);  // AND_Gate
  and and_38 (and_38_out, RDY, v2, compare_i_4_out_2);
  compare_i compare_i_4 (.DIN(DIN), .out_2(compare_i_4_out_2));
  and and_39 (and_39_out, ~RDY, N);  // AND_Gate
  and and_40 (and_40_out, RDY, O2, compare_n_2_out_2);
  and and_41 (and_41_out, ~RDY, U);  // AND_Gate
  and and_42 (and_42_out, RDY, R2, compare_u_2_out_2);
  D_Flip_Flop u_i2 (.D(or_17_out), .clk(CLK), .Q(i2), .reset(RST));  // open: Qn, preset
  or or_17 (or_17_out, and_37_out, and_38_out);
  D_Flip_Flop u_N (.D(or_18_out), .clk(CLK), .Q(N), .reset(RST));  // open: Qn, preset
  or or_18 (or_18_out, and_39_out, and_40_out);
  D_Flip_Flop u_U (.D(or_19_out), .clk(CLK), .Q(U), .reset(RST));  // open: Qn, preset
  or or_19 (or_19_out, and_41_out, and_42_out);

  // Other names for the same wires on the sheet: MATCH = F

  // Notes on the sheet:
  //   Rdy
  //   CLK
  //   RST
  //   DIN
  //   CLK
  //   RDY
  //   RDY
  //   DIN
  //   Din
  //   RST
  //   DIN
  //   RDY
  //   CLK
  //   RST
  //   CLK
  //   RDY
endmodule

module compare_c (
  input  [6:0] DIN,
  output out_2
);

  wire comparator_1_eq, comparator_2_eq;

  Comparator #(.width(7), .mode("unsigned")) comparator_1 (
    .a(DIN), .b(7'b1000011), .eq(comparator_1_eq));  // open: gt, lt
  Comparator #(.width(7), .mode("unsigned")) comparator_2 (
    .a(DIN), .b(7'b1100011), .eq(comparator_2_eq));  // open: gt, lt
  or or_1 (out_2, comparator_1_eq, comparator_2_eq);
endmodule

module compare_o (
  input  [6:0] DIN,
  output out_2
);

  wire comparator_1_eq, comparator_2_eq;

  Comparator #(.width(7), .mode("unsigned")) comparator_1 (
    .a(DIN), .b(7'b1001111), .eq(comparator_1_eq));  // open: gt, lt
  Comparator #(.width(7), .mode("unsigned")) comparator_2 (
    .a(DIN), .b(7'b1101111), .eq(comparator_2_eq));  // open: gt, lt
  or or_1 (out_2, comparator_1_eq, comparator_2_eq);
endmodule

module compare_v (
  input  [6:0] DIN,
  output out_2
);

  wire comparator_1_eq, comparator_2_eq;

  Comparator #(.width(7), .mode("unsigned")) comparator_1 (
    .a(DIN), .b(7'b1010110), .eq(comparator_1_eq));  // open: gt, lt
  Comparator #(.width(7), .mode("unsigned")) comparator_2 (
    .a(DIN), .b(7'b1110110), .eq(comparator_2_eq));  // open: gt, lt
  or or_1 (out_2, comparator_1_eq, comparator_2_eq);
endmodule

module compare_i (
  input  [6:0] DIN,
  output out_2
);

  wire comparator_1_eq, comparator_2_eq;

  Comparator #(.width(7), .mode("unsigned")) comparator_1 (
    .a(DIN), .b(7'b1001001), .eq(comparator_1_eq));  // open: gt, lt
  Comparator #(.width(7), .mode("unsigned")) comparator_2 (
    .a(DIN), .b(7'b1101001), .eq(comparator_2_eq));  // open: gt, lt
  or or_1 (out_2, comparator_1_eq, comparator_2_eq);
endmodule

module compare_n (
  input  [6:0] DIN,
  output out_2
);

  wire comparator_1_eq, comparator_2_eq;

  Comparator #(.width(7), .mode("unsigned")) comparator_1 (
    .a(DIN), .b(7'b1001110), .eq(comparator_1_eq));  // open: gt, lt
  Comparator #(.width(7), .mode("unsigned")) comparator_2 (
    .a(DIN), .b(7'b1101110), .eq(comparator_2_eq));  // open: gt, lt
  or or_1 (out_2, comparator_1_eq, comparator_2_eq);
endmodule

module compare_a (
  input  [6:0] DIN,
  output out_2
);

  wire comparator_1_eq, comparator_2_eq;

  Comparator #(.width(7), .mode("unsigned")) comparator_1 (
    .a(DIN), .b(7'b1000001), .eq(comparator_1_eq));  // open: gt, lt
  Comparator #(.width(7), .mode("unsigned")) comparator_2 (
    .a(DIN), .b(7'b1100001), .eq(comparator_2_eq));  // open: gt, lt
  or or_1 (out_2, comparator_1_eq, comparator_2_eq);
endmodule

module compare_r (
  input  [6:0] DIN,
  output out_2
);

  wire comparator_1_eq, comparator_2_eq;

  Comparator #(.width(7), .mode("unsigned")) comparator_1 (
    .a(DIN), .b(7'b1010010), .eq(comparator_1_eq));  // open: gt, lt
  Comparator #(.width(7), .mode("unsigned")) comparator_2 (
    .a(DIN), .b(7'b1110010), .eq(comparator_2_eq));  // open: gt, lt
  or or_1 (out_2, comparator_1_eq, comparator_2_eq);
endmodule

module compare_u (
  input  [6:0] DIN,
  output out_2
);

  wire comparator_1_eq, comparator_2_eq;

  Comparator #(.width(7), .mode("unsigned")) comparator_1 (
    .a(DIN), .b(7'b1010101), .eq(comparator_1_eq));  // open: gt, lt
  Comparator #(.width(7), .mode("unsigned")) comparator_2 (
    .a(DIN), .b(7'b1110101), .eq(comparator_2_eq));  // open: gt, lt
  or or_1 (out_2, comparator_1_eq, comparator_2_eq);
endmodule

module compare_s (
  input  [6:0] DIN,
  output out_2
);

  wire comparator_1_eq, comparator_2_eq;

  Comparator #(.width(7), .mode("unsigned")) comparator_1 (
    .a(DIN), .b(7'b1010011), .eq(comparator_1_eq));  // open: gt, lt
  Comparator #(.width(7), .mode("unsigned")) comparator_2 (
    .a(DIN), .b(7'b1110011), .eq(comparator_2_eq));  // open: gt, lt
  or or_1 (out_2, comparator_1_eq, comparator_2_eq);
endmodule

module compare_d (
  input  [6:0] DIN,
  output out_2
);

  wire comparator_1_eq, comparator_2_eq;

  Comparator #(.width(7), .mode("unsigned")) comparator_1 (
    .a(DIN), .b(7'b1000100), .eq(comparator_1_eq));  // open: gt, lt
  Comparator #(.width(7), .mode("unsigned")) comparator_2 (
    .a(DIN), .b(7'b1100100), .eq(comparator_2_eq));  // open: gt, lt
  or or_1 (out_2, comparator_1_eq, comparator_2_eq);
endmodule

module notvc (
  input  [6:0] DIN,
  output out_2
);

  wire compare_c_1_out_2, compare_v_1_out_2;

  compare_c compare_c_1 (.DIN(DIN), .out_2(compare_c_1_out_2));
  compare_v compare_v_1 (.DIN(DIN), .out_2(compare_v_1_out_2));
  and and_1 (out_2, ~compare_c_1_out_2, ~compare_v_1_out_2);  // AND_Gate
endmodule

module \checker  (
);

  wire and_1_out, and_2_out, and_3_out, button_1_out, button_2_out, clock_1_out, clock_2_out,
       comparator_1_eq, detector_1_p4, t_ff_1_q, xor_1_out;
  wire [3:0] rom_1_data;
  wire [11:0] counter_1_q;

  Clock clock_1 (.out(clock_1_out));
  Button button_1 (.out(button_1_out));
  Counter #(.width(12), .max('hfff)) counter_1 (
    .clr(button_1_out), .up(1'b1), .clk(and_1_out), .Q(counter_1_q));  // open: load, count, D, carry
  and and_1 (and_1_out, clock_1_out, ~and_2_out);  // AND_Gate
  ROM #(.addrWidth(12), .dataWidth(4)) rom_1 (.addr(counter_1_q), .data(rom_1_data));
  Comparator #(.width(12)) comparator_1 (.a({12{1'b1}}), .b(counter_1_q), .eq(comparator_1_eq));  // open: gt, lt
  Clock clock_2 (.out(clock_2_out));
  and and_2 (and_2_out, and_3_out, xor_1_out);
  T_Flip_Flop t_ff_1 (.T(comparator_1_eq), .clk(clock_2_out), .Q(t_ff_1_q));  // open: Qn, reset, preset
  LED led_1 (.in(t_ff_1_q));
  and and_3 (and_3_out, ~button_2_out, xor_1_out);  // AND_Gate
  Button button_2 (.out(button_2_out));
  xor xor_1 (xor_1_out, rom_1_data[0], detector_1_p4);
  LED led_2 (.in(xor_1_out));
  // Detector detector_1: pin names not known; wires that end beside it: rom_1_data[3], rom_1_data[2], rom_1_data[1], detector_1_p4

  // Notes on the sheet:
  //   contents of rom_1 (hex, n*v repeats v):
  //   4*6 4*2 4 c c c 4*8 4*d 4*9 4*c 4*8 4*c 4*8 4*c 4*8 4*c 4*8 4*c 4*8
endmodule
