// Logisim project M16 Components.circ as structural Verilog: 11 circuits, main circuit poweron_reset_random
module poweron_reset_random (
  input  CLK,
  output RST
);

  wire and_1_out, d_ff_1_q, not_1_out, RNGRST_out, t_ff_1_qn;

  Random #(.width(1), .seed(10)) RNGRST (.next(t_ff_1_qn), .clk(CLK), .out(RNGRST_out));  // open: clr
  T_Flip_Flop t_ff_1 (.T(and_1_out), .clk(CLK), .Qn(t_ff_1_qn));  // open: Q, reset, preset
  and and_1 (and_1_out, t_ff_1_qn, not_1_out, d_ff_1_q);
  not not_1 (not_1_out, RNGRST_out);
  D_Flip_Flop d_ff_1 (.D(RNGRST_out), .clk(CLK), .Q(d_ff_1_q));  // open: Qn, preset, reset
  and and_2 (RST, t_ff_1_qn, d_ff_1_q);
  TTY #(.rows(4), .cols(16)) tty_1 (.data({6'b011000, RST}), .clk(CLK));  // open: we, clr
endmodule

module RndDlyHSClient (
  input  CLK,
  input  RST,
  input  ACK,
  output REQ
);

  wire d_ff_1_qn, decoder_1_out0, decoder_1_out2, decoder_1_out4, decoder_1_out5, decoder_1_out9,
       decoder_1_out11, decoder_1_out12, decoder_1_out13, multiplexer_1_out, or_1_out, xor_1_out;
  wire [2:1] counter_1_carry;
  wire [3:0] random_1_out;

  Clock sysclk ();  // open: out
  Decoder #(.select(4)) decoder_1 (
    .out0(decoder_1_out0), .out2(decoder_1_out2), .out4(decoder_1_out4), .out5(decoder_1_out5),
    .out9(decoder_1_out9), .out11(decoder_1_out11), .out12(decoder_1_out12), .out13(decoder_1_out13),
    .sel({REQ, counter_1_carry, ACK}));  // open: out1, out3, out6, out7, out8, out10, out14, out15, en
  Random #(.width(4), .seed(10)) random_1 (.clk(CLK), .out(random_1_out));  // open: clr, next
  D_Flip_Flop d_ff_1 (.D(or_1_out), .clk(CLK), .Q(counter_1_carry[2]), .Qn(d_ff_1_qn), .reset(RST));  // open: preset
  or or_1 (or_1_out, decoder_1_out0, decoder_1_out2, decoder_1_out4, decoder_1_out5, decoder_1_out9, decoder_1_out11, decoder_1_out12, decoder_1_out13);
  Counter #(.width(4), .max('hf), .ongoal("stay")) counter_1 (
    .load(d_ff_1_qn), .up(1'b1), .clk(CLK), .D(random_1_out), .carry(counter_1_carry[1]));  // open: clr, count, Q
  Multiplexer #(.enable("false")) multiplexer_1 (
    .in0(REQ), .in1(xor_1_out), .out(multiplexer_1_out), .sel(counter_1_carry[1]));
  xor xor_1 (xor_1_out, REQ, counter_1_carry[2]);
  D_Flip_Flop d_ff_2 (.D(multiplexer_1_out), .clk(CLK), .Q(REQ), .reset(RST));  // open: Qn, preset

  // Notes on the sheet:
  //   Initial: REQ=0, ACK=0
  //   1. Wait for random time
  //   2. Set REQ=1
  //   3. Wait for ACK==1
  //   4. Wait for random time
  //   5. Set REQ = 0
  //   6. Wait for ACK==0
  //   7. Go to Step 1
  //   This module implements the client side of the REQ-ACK Handshake.
endmodule

module GenPulseAtNegEdge (
  input  CLK,
  input  X,
  output PULSE
);

  wire d_ff_1_q, not_1_out;

  not not_1 (not_1_out, X);
  D_Flip_Flop d_ff_1 (.D(X), .clk(CLK), .Q(d_ff_1_q));  // open: Qn, preset, reset
  and and_1 (PULSE, not_1_out, d_ff_1_q);
endmodule

module OperandSequencer (
  input  CLK,
  input  RST,
  input  NXT,
  output DONE,
  output [7:0] i,
  output [15:0] D
);

  Counter #(.ongoal("stay")) counter_1 (
    .load(RST), .count(NXT), .clk(CLK), .D({8{1'b0}}), .carry(DONE), .Q(i));  // open: clr, up
  ROM #(.dataWidth(16)) rom_1 (.addr(i), .data(D));

  // Notes on the sheet:
  //   i = iteration number; D = i-th operand in ROM; DONE indicated end
  //   contents of rom_1 (hex, n*v repeats v):
  //   16*8000 16*ffff 16*0 16*1 16*7fff 16*2 16*3 16*4 16*9 16*64 16*fffe 16*fffd 16*fffc 16*fff7 16*ff9c
  //   16*f0ff
  //   Iterates through data in the ROM, moving to new value on every clock tick that NXT=1
endmodule

module poweron_reset (
  input  CLK,
  output RST
);

  wire d_ff_1_q, nor_1_out, not_1_out;

  not not_1 (not_1_out, nor_1_out);
  D_Flip_Flop d_ff_1 (.D(not_1_out), .clk(CLK), .Q(d_ff_1_q));  // open: Qn, preset, reset
  D_Flip_Flop d_ff_2 (.D(nor_1_out), .clk(CLK), .Q(RST));  // open: Qn, preset, reset
  nor nor_1 (nor_1_out, d_ff_1_q, RST);
endmodule

module MulDivUnsigned16 (
  input  SelDiv,
  input  [15:0] A,
  input  [15:0] B,
  output [15:0] X,
  output [15:0] Y
);

  wire [15:0] divider_1_out, divider_1_rem, multiplier_1_cout, multiplier_1_out;

  Multiplier #(.width(16)) multiplier_1 (.a(A), .b(B), .out(multiplier_1_out), .cout(multiplier_1_cout));  // open: cin
  Divider #(.width(16)) divider_1 (.a(A), .b(B), .out(divider_1_out), .rem(divider_1_rem));  // open: upper
  Multiplexer #(.width(16), .enable("false")) multiplexer_1 (
    .in0(multiplier_1_out), .in1(divider_1_out), .out(X), .sel(SelDiv));
  Multiplexer #(.width(16), .enable("false")) multiplexer_2 (
    .in0(multiplier_1_cout), .in1(divider_1_rem), .out(Y), .sel(SelDiv));

  // Notes on the sheet:
  //   If SelDiv==0, performs unsigned multiplication with Y[15:0] & X[15:0] being upper & lower bits of A[15:0]*B[15:0]
  //   If SelDiv==1, performs unsigned division with X[15:0]=A[15:0]/B[15:0] and Y[15:0]=A[15:0]%Y[15:0]
  //   If SelDiv==1 and B[15:0] then no division is performed, i.e. divisor is assumed to be 1
endmodule

module RandomTimer (
  input  CLK,
  input  GO,
  output DONE
);

  wire and_1_out, and_2_out, d_ff_1_qn, not_1_out;
  wire [4:0] multiplexer_1_out, random_1_out;

  Random #(.width(5), .seed(10)) random_1 (.next(and_1_out), .clk(CLK), .out(random_1_out));  // open: clr
  D_Flip_Flop d_ff_1 (.D(GO), .clk(CLK), .Qn(d_ff_1_qn));  // open: Q, preset, reset
  not not_1 (not_1_out, GO);
  and and_1 (and_1_out, d_ff_1_qn, GO);
  Multiplexer #(.width(5), .enable("false")) multiplexer_1 (
    .in0(random_1_out), .in1(5'b00001), .out(multiplexer_1_out), .sel(and_2_out));
  and and_2 (and_2_out, random_1_out[0], random_1_out[1], random_1_out[2], random_1_out[3], random_1_out[4]);
  Counter #(.width(5), .max('h1f), .ongoal("stay")) counter_1 (
    .load(not_1_out), .clk(CLK), .D(multiplexer_1_out), .carry(DONE));  // open: clr, up, count, Q
  LED led_1 (.in(DONE));

  // Notes on the sheet:
  //   Makes DONE=1 a random # of clock ticks (>0) after GO==1; DONE=0 as soom as GO=1
endmodule

module RndDlyHSServer (
  input  CLK,
  input  RST,
  input  REQ,
  output ACK
);

  wire not_1_out;

  not not_1 (not_1_out, REQ);
  RndDlyHSClient rnddlyhsclient_1 (.CLK(CLK), .RST(RST), .ACK(not_1_out), .REQ(ACK));
endmodule

module RndDlyAdd (
  input  CLK,
  input  GO,
  input  [31:0] A,
  input  [31:0] B,
  output DONE,
  output [31:0] DOUT
);

  wire [31:0] adder_1_out, multiplexer_1_out, multiplexer_2_out, register_1_q;

  Multiplexer #(.width(32), .enable("false")) multiplexer_1 (
    .in0({32{1'b0}}), .in1(A), .out(multiplexer_1_out), .sel(GO));
  Multiplexer #(.width(32), .enable("false")) multiplexer_2 (
    .in0({32{1'b0}}), .in1(B), .out(multiplexer_2_out), .sel(GO));
  Adder #(.width(32)) adder_1 (.a(multiplexer_1_out), .b(multiplexer_2_out), .out(adder_1_out));  // open: cin, cout
  Register #(.width(32)) register_1 (.D(adder_1_out), .en(1'b1), .clk(CLK), .Q(register_1_q));  // open: clr
  RandomTimer randomtimer_1 (.CLK(CLK), .GO(GO), .DONE(DONE));
  Multiplexer #(.width(32), .enable("false")) multiplexer_3 (
    .in0({32{1'b0}}), .in1(register_1_q), .out(DOUT), .sel(DONE));

  // Notes on the sheet:
  //   Adder that take random # of clock cycles to compute
endmodule

module RndDlyMul (
  input  CLK,
  input  GO,
  input  [31:0] A,
  input  [31:0] B,
  output DONE,
  output [31:0] AxBLo,
  output [31:0] AxBHi
);

  wire [31:0] multiplexer_1_out, multiplexer_2_out, multiplier_1_cout, multiplier_1_out, register_1_q;

  Multiplexer #(.width(32), .enable("false")) multiplexer_1 (
    .in0({32{1'b0}}), .in1(A), .out(multiplexer_1_out), .sel(GO));
  Multiplexer #(.width(32), .enable("false")) multiplexer_2 (
    .in0({32{1'b0}}), .in1(B), .out(multiplexer_2_out), .sel(GO));
  Multiplier #(.width(32)) multiplier_1 (
    .a(multiplexer_1_out), .b(multiplexer_2_out), .out(multiplier_1_out), .cout(multiplier_1_cout));  // open: cin
  Register #(.width(32)) register_1 (.D(multiplier_1_out), .en(1'b1), .clk(CLK), .Q(register_1_q));  // open: clr
  RandomTimer randomtimer_1 (.CLK(CLK), .GO(GO), .DONE(DONE));
  Multiplexer #(.width(32), .enable("false")) multiplexer_3 (
    .in0({32{1'b0}}), .in1(register_1_q), .out(AxBLo), .sel(DONE));
  Multiplexer #(.width(32), .enable("false")) multiplexer_4 (
    .in0({32{1'b0}}), .in1(multiplier_1_cout), .out(AxBHi), .sel(DONE));

  // Notes on the sheet:
  //   Multiplier that take random # of clock cycles to compute
endmodule

module DatapathALU (
  input  CLK,
  input  [1:0] SELA,
  input  [1:0] SELB,
  input  [3:0] OP,
  input  SELSA,
  input  [4:0] SA,
  input  LDR0,
  input  LDR1,
  input  SELOUT,
  input  [31:0] DIN0,
  input  [31:0] DIN1,
  output [31:0] DOUT,
  output MSBR0,
  output LSBR0,
  output MSBR1,
  output MSBR2
);

  wire [4:0] alu_1_p4;
  wire [30:1] register_1_q, register_2_q;
  wire [31:0] alu_1_p5, multiplexer_1_out, multiplexer_2_out;

  Multiplexer #(.select(2), .width(32), .enable("false")) multiplexer_1 (
    .in0(DIN0), .in1(DIN1), .in2({MSBR0, register_1_q, LSBR0}), .in3({MSBR1, register_2_q, MSBR2}),
    .out(multiplexer_1_out), .sel(SELA));
  Multiplexer #(.select(2), .width(32), .enable("false")) multiplexer_2 (
    .in0(DIN0), .in1(DIN1), .in2({MSBR0, register_1_q, LSBR0}), .in3({MSBR1, register_2_q, MSBR2}),
    .out(multiplexer_2_out), .sel(SELB));
  // ALU alu_1: pin names not known; wires that end beside it: multiplexer_1_out, multiplexer_2_out, OP, alu_1_p4, alu_1_p5
  Multiplexer #(.width(5), .enable("false")) multiplexer_3 (
    .in0(multiplexer_1_out[4:0]), .in1(SA), .out(alu_1_p4), .sel(SELSA));
  Register #(.width(32)) register_1 (
    .D(alu_1_p5), .en(LDR0), .clk(CLK), .Q({MSBR0, register_1_q, LSBR0}));  // open: clr
  Register #(.width(32)) register_2 (
    .D(alu_1_p5), .en(LDR1), .clk(CLK), .Q({MSBR1, register_2_q, MSBR2}));  // open: clr
  Multiplexer #(.width(32), .enable("false")) multiplexer_4 (
    .in0({MSBR0, register_1_q, LSBR0}), .in1({MSBR1, register_2_q, MSBR2}), .out(DOUT), .sel(SELOUT));
endmodule
