// Logisim project final_v2.circ as structural Verilog: 8 circuits, main circuit FSM_2PHS
module FSM_2PHS (
  input  CLK,
  input  RST,
  input  REQ,
  input  DONE,
  output ACK,
  output GO
);


  // Notes on the sheet:
  //   You Need to Edit This
  //   Two Phase Handshake FSM from Part 1
  //   Do not move/delete/add/rename pins
endmodule

module TB_FSM_2PHS (
  input  REQ,
  input  [31:0] X,
  output [31:0] out_3,
  output [31:0] X_SQUARE
);

  wire CLK_out, DUT_ack, DUT_go, poweron_reset_random_1_rst, rnddlymul_1_done;

  Clock sysclk ();  // open: out
  Clock CLK (.out(CLK_out));
  poweron_reset_random poweron_reset_random_1 (.CLK(CLK_out), .RST(poweron_reset_random_1_rst));
  LED REQis1 (.in(poweron_reset_random_1_rst));
  LED ACKis1 (.in(DUT_ack));
  FSM_2PHS DUT (
    .CLK(CLK_out), .RST(poweron_reset_random_1_rst), .REQ(REQ), .DONE(rnddlymul_1_done), .ACK(DUT_ack),
    .GO(DUT_go));
  RndDlyMul rnddlymul_1 (
    .CLK(CLK_out), .GO(DUT_go), .A(X), .B(X), .DONE(rnddlymul_1_done), .AxBLo(X_SQUARE), .AxBHi(out_3));

  // Notes on the sheet:
  //   Simple testbench for manual testing of FSM_2PHS
  //   Feel free to edit it for your needs.
endmodule

module FSM_SQROOT (
  input  CLK,
  input  RST,
  input  GO,
  input  STATUS,
  output DONE,
  output COMMAND
);


  // Notes on the sheet:
  //   You Need to Edit This
  //   Controller for Part 2
  //   Modify Status and Command signals for Datapath
  //   If you don't need controller, just feed GO to COMMAND, and STATUS to DONE
endmodule

module DP_SQROOT (
  input  CLK,
  input  RST,
  input  COMMAND,
  input  [15:0] DIN,
  output STATUS,
  output [7:0] DOUT
);


  // Notes on the sheet:
  //   You Need to Edit This
  //   Datapath for Part 2
  //   Modify Status and Command signals for Controller
  //   If you don't have a controller then COMMAND is GO, and STATUS is DONE
endmodule

module MAIN (
  input  CLK,
  input  RST,
  input  REQ,
  input  [15:0] DIN,
  output ACK,
  output [7:0] DOUT
);

  wire dp_sqroot_1_status, fsm_2phs_1_go, fsm_sqroot_1_command, fsm_sqroot_1_done;

  FSM_2PHS fsm_2phs_1 (.CLK(CLK), .RST(RST), .REQ(REQ), .DONE(fsm_sqroot_1_done), .ACK(ACK), .GO(fsm_2phs_1_go));
  FSM_SQROOT fsm_sqroot_1 (
    .CLK(CLK), .RST(RST), .GO(fsm_2phs_1_go), .STATUS(dp_sqroot_1_status), .DONE(fsm_sqroot_1_done),
    .COMMAND(fsm_sqroot_1_command));
  DP_SQROOT dp_sqroot_1 (
    .CLK(CLK), .RST(RST), .COMMAND(fsm_sqroot_1_command), .DIN(DIN), .STATUS(dp_sqroot_1_status), .DOUT(DOUT));

  // Notes on the sheet:
  //   No Need to Edit This
endmodule

module TB_MAIN (
  input  REQ,
  input  [15:0] DIN,
  output [7:0] DOUT
);

  wire CLK_out, DUT_ack, poweron_reset_random_1_rst;

  Clock sysclk ();  // open: out
  Clock CLK (.out(CLK_out));
  poweron_reset_random poweron_reset_random_1 (.CLK(CLK_out), .RST(poweron_reset_random_1_rst));
  LED REQis1 (.in(poweron_reset_random_1_rst));
  LED ACKis1 (.in(DUT_ack));
  MAIN DUT (.CLK(CLK_out), .RST(poweron_reset_random_1_rst), .REQ(REQ), .DIN(DIN), .ACK(DUT_ack), .DOUT(DOUT));

  // Notes on the sheet:
  //   X
  //   Testbench for manual testing of MAIN system
  //   Feel free to edit it for your needs.
  //   sqrt(X)
endmodule

module DONTUSE_TB_AUTO_FSM_2PHS (
  output [31:0] out_1,
  output [31:0] X_SQUARED,
  output [31:0] X
);

  wire CLK_out, DUT_ack, DUT_go, genpulseatnegedge_1_pulse, genpulseatnegedge_2_pulse, not_1_out, or_1_out,
       poweron_reset_random_1_rst, rnddlyhsclient_1_req, rnddlymul_1_done;

  Clock sysclk ();  // open: out
  Clock CLK (.out(CLK_out));
  not not_1 (not_1_out, rnddlyhsclient_1_req);
  RndDlyHSClient rnddlyhsclient_1 (
    .CLK(CLK_out), .RST(poweron_reset_random_1_rst), .ACK(DUT_ack), .REQ(rnddlyhsclient_1_req));
  GenPulseAtNegEdge genpulseatnegedge_1 (.CLK(rnddlyhsclient_1_req), .PULSE(genpulseatnegedge_1_pulse));  // open: X
  or or_1 (or_1_out, genpulseatnegedge_1_pulse, genpulseatnegedge_2_pulse);
  GenPulseAtNegEdge genpulseatnegedge_2 (.CLK(not_1_out), .PULSE(genpulseatnegedge_2_pulse));  // open: X
  poweron_reset_random poweron_reset_random_1 (.CLK(CLK_out), .RST(poweron_reset_random_1_rst));
  Counter #(.width(32), .max('hffffffff), .ongoal("stay")) counter_1 (
    .load(poweron_reset_random_1_rst), .count(or_1_out), .clk(CLK_out), .D({32{1'b0}}), .Q(X));  // open: clr, up, carry
  FSM_2PHS DUT (
    .CLK(CLK_out), .RST(poweron_reset_random_1_rst), .REQ(rnddlyhsclient_1_req), .DONE(rnddlymul_1_done),
    .ACK(DUT_ack), .GO(DUT_go));
  RndDlyMul rnddlymul_1 (
    .CLK(CLK_out), .GO(DUT_go), .A(X), .B(X), .DONE(rnddlymul_1_done), .AxBLo(X_SQUARED), .AxBHi(out_1));

  // Notes on the sheet:
  //   Testbench for automated testing of TB_FSM_2PHS
  //   NOT FUNCTIONAL - DONOT USE
endmodule

module DONTUSE_TB_AUTO (
  input  [15:0] X,
  output [7:0] sqrt_X
);

  wire clock_2_out, main_1_ack, poweron_reset_random_1_rst, rnddlyhsclient_1_req;

  Clock clock_1 ();  // open: out
  Clock clock_2 (.out(clock_2_out));
  RndDlyHSClient rnddlyhsclient_1 (
    .CLK(clock_2_out), .RST(poweron_reset_random_1_rst), .ACK(main_1_ack), .REQ(rnddlyhsclient_1_req));
  poweron_reset_random poweron_reset_random_1 (.CLK(clock_2_out), .RST(poweron_reset_random_1_rst));
  LED led_1 (.in(poweron_reset_random_1_rst));
  LED led_2 (.in(main_1_ack));
  MAIN main_1 (
    .CLK(clock_2_out), .RST(poweron_reset_random_1_rst), .REQ(rnddlyhsclient_1_req), .DIN(X),
    .ACK(main_1_ack), .DOUT(sqrt_X));

  // Notes on the sheet:
  //   Testbench for automated testing of MAIN system
endmodule
